// Logisim project project1.circ as structural Verilog: 4 circuits, main circuit 8 bit register
module _8_bit_register (
  input  E,
  input  [7:0] Input,
  input  [1:0] FunSel,
  output [7:0] Q
);

  wire and_1_out, and_2_out, and_3_out, and_4_out, and_5_out, and_6_out, clock_1_out, multiplexer_1_out,
       multiplexer_2_out, multiplexer_3_out, multiplexer_4_out, multiplexer_5_out, multiplexer_6_out,
       multiplexer_7_out, multiplexer_8_out, not_1_out, not_2_out, not_3_out, not_4_out, not_5_out,
       not_6_out, not_7_out, not_8_out, or_1_out, or_2_out, or_3_out, or_4_out, or_5_out, or_6_out,
       xor_1_out, xor_2_out, xor_3_out, xor_4_out, xor_5_out, xor_6_out, xor_7_out, xor_8_out, xor_9_out,
       xor_10_out, xor_11_out, xor_12_out, xor_13_out, xor_14_out;

  not not_1 (not_1_out, Q[0]);
  and and_1 (and_1_out, Q[0], Q[1]);
  and and_2 (and_2_out, Q[0], Q[1], Q[2]);
  and and_3 (and_3_out, Q[0], Q[1], Q[2], Q[3]);
  and and_4 (and_4_out, Q[0], Q[1], Q[2], Q[3], Q[4]);
  and and_5 (and_5_out, Q[0], Q[1], Q[2], Q[3], Q[4], Q[5]);
  and and_6 (and_6_out, Q[0], Q[1], Q[2], Q[3], Q[4], Q[5], Q[6]);
  not not_2 (not_2_out, Q[0]);
  or or_1 (or_1_out, Q[1], Q[0]);
  or or_2 (or_2_out, Q[2], Q[1], Q[0]);
  or or_3 (or_3_out, Q[3], Q[2], Q[1], Q[0]);
  or or_4 (or_4_out, Q[4], Q[3], Q[2], Q[1], Q[0]);
  or or_5 (or_5_out, Q[5], Q[4], Q[3], Q[2], Q[1], Q[0]);
  or or_6 (or_6_out, Q[6], Q[5], Q[4], Q[3], Q[2], Q[1], Q[0]);
  xor xor_1 (xor_1_out, not_2_out, Q[1]);
  xor xor_2 (xor_2_out, Q[0], Q[1]);
  not not_3 (not_3_out, or_1_out);
  xor xor_3 (xor_3_out, not_3_out, Q[2]);
  xor xor_4 (xor_4_out, Q[2], and_1_out);
  not not_4 (not_4_out, or_2_out);
  xor xor_5 (xor_5_out, not_4_out, Q[3]);
  xor xor_6 (xor_6_out, Q[3], and_2_out);
  not not_5 (not_5_out, or_3_out);
  xor xor_7 (xor_7_out, not_5_out, Q[4]);
  xor xor_8 (xor_8_out, Q[4], and_3_out);
  not not_6 (not_6_out, or_4_out);
  xor xor_9 (xor_9_out, not_6_out, Q[5]);
  xor xor_10 (xor_10_out, Q[5], and_4_out);
  not not_7 (not_7_out, or_5_out);
  xor xor_11 (xor_11_out, not_7_out, Q[6]);
  xor xor_12 (xor_12_out, Q[6], and_5_out);
  not not_8 (not_8_out, or_6_out);
  xor xor_13 (xor_13_out, not_8_out, Q[7]);
  xor xor_14 (xor_14_out, Q[7], and_6_out);
  Multiplexer #(.select(2), .enable("false")) multiplexer_1 (
    .in0(Input[0]), .in1(not_1_out), .in2(not_1_out), .in3(1'b0), .out(multiplexer_1_out), .sel(FunSel));
  Multiplexer #(.select(2), .enable("false")) multiplexer_2 (
    .in0(Input[1]), .in1(xor_1_out), .in2(xor_2_out), .in3(1'b0), .out(multiplexer_2_out), .sel(FunSel));
  Multiplexer #(.select(2), .enable("false")) multiplexer_3 (
    .in0(Input[2]), .in1(xor_3_out), .in2(xor_4_out), .in3(1'b0), .out(multiplexer_3_out), .sel(FunSel));
  Multiplexer #(.select(2), .enable("false")) multiplexer_4 (
    .in0(Input[3]), .in1(xor_5_out), .in2(xor_6_out), .in3(1'b0), .out(multiplexer_4_out), .sel(FunSel));
  Multiplexer #(.select(2), .enable("false")) multiplexer_5 (
    .in0(Input[4]), .in1(xor_7_out), .in2(xor_8_out), .in3(1'b0), .out(multiplexer_5_out), .sel(FunSel));
  Multiplexer #(.select(2), .enable("false")) multiplexer_6 (
    .in0(Input[5]), .in1(xor_9_out), .in2(xor_10_out), .in3(1'b0), .out(multiplexer_6_out), .sel(FunSel));
  Multiplexer #(.select(2), .enable("false")) multiplexer_7 (
    .in0(Input[6]), .in1(xor_11_out), .in2(xor_12_out), .in3(1'b0), .out(multiplexer_7_out), .sel(FunSel));
  Multiplexer #(.select(2), .enable("false")) multiplexer_8 (
    .in0(Input[7]), .in1(xor_13_out), .in2(xor_14_out), .in3(1'b0), .out(multiplexer_8_out), .sel(FunSel));
  Clock clock_1 (.out(clock_1_out));
  D_Flip_Flop #(.enable("true")) d_ff_1 (
    .clk(clock_1_out), .D(multiplexer_1_out), .Q(Q[0]), .en(E));  // open: Qn, preset, reset
  D_Flip_Flop #(.enable("true")) d_ff_2 (
    .clk(clock_1_out), .D(multiplexer_2_out), .Q(Q[1]), .en(E));  // open: Qn, preset, reset
  D_Flip_Flop #(.enable("true")) d_ff_3 (
    .clk(clock_1_out), .D(multiplexer_3_out), .Q(Q[2]), .en(E));  // open: Qn, preset, reset
  D_Flip_Flop #(.enable("true")) d_ff_4 (
    .clk(clock_1_out), .D(multiplexer_4_out), .Q(Q[3]), .en(E));  // open: Qn, preset, reset
  D_Flip_Flop #(.enable("true")) d_ff_5 (
    .clk(clock_1_out), .D(multiplexer_5_out), .Q(Q[4]), .en(E));  // open: Qn, preset, reset
  D_Flip_Flop #(.enable("true")) d_ff_6 (
    .clk(clock_1_out), .D(multiplexer_6_out), .Q(Q[5]), .en(E));  // open: Qn, preset, reset
  D_Flip_Flop #(.enable("true")) d_ff_7 (
    .clk(clock_1_out), .D(multiplexer_7_out), .Q(Q[6]), .en(E));  // open: Qn, preset, reset
  D_Flip_Flop #(.enable("true")) d_ff_8 (
    .clk(clock_1_out), .D(multiplexer_8_out), .Q(Q[7]), .en(E));  // open: Qn, preset, reset
endmodule

module _16_bit_regiser (
  input  E,
  input  [7:0] Input,
  input  [1:0] FunSel,
  output [7:0] Q
);

  wire and_1_out, and_2_out, and_3_out, and_4_out, and_5_out, and_6_out, clock_1_out, multiplexer_1_out,
       multiplexer_2_out, multiplexer_3_out, multiplexer_4_out, multiplexer_5_out, multiplexer_6_out,
       multiplexer_7_out, multiplexer_8_out, not_1_out, not_2_out, not_3_out, not_4_out, not_5_out,
       not_6_out, not_7_out, not_8_out, or_1_out, or_2_out, or_3_out, or_4_out, or_5_out, or_6_out,
       xor_1_out, xor_2_out, xor_3_out, xor_4_out, xor_5_out, xor_6_out, xor_7_out, xor_8_out, xor_9_out,
       xor_10_out, xor_11_out, xor_12_out, xor_13_out, xor_14_out;

  not not_1 (not_1_out, Q[0]);
  and and_1 (and_1_out, Q[0], Q[1]);
  and and_2 (and_2_out, Q[0], Q[1], Q[2]);
  and and_3 (and_3_out, Q[0], Q[1], Q[2], Q[3]);
  and and_4 (and_4_out, Q[0], Q[1], Q[2], Q[3], Q[4]);
  and and_5 (and_5_out, Q[0], Q[1], Q[2], Q[3], Q[4], Q[5]);
  and and_6 (and_6_out, Q[0], Q[1], Q[2], Q[3], Q[4], Q[5], Q[6]);
  not not_2 (not_2_out, Q[0]);
  or or_1 (or_1_out, Q[1], Q[0]);
  or or_2 (or_2_out, Q[2], Q[1], Q[0]);
  or or_3 (or_3_out, Q[3], Q[2], Q[1], Q[0]);
  or or_4 (or_4_out, Q[4], Q[3], Q[2], Q[1], Q[0]);
  or or_5 (or_5_out, Q[5], Q[4], Q[3], Q[2], Q[1], Q[0]);
  or or_6 (or_6_out, Q[6], Q[5], Q[4], Q[3], Q[2], Q[1], Q[0]);
  xor xor_1 (xor_1_out, not_2_out, Q[1]);
  xor xor_2 (xor_2_out, Q[0], Q[1]);
  not not_3 (not_3_out, or_1_out);
  xor xor_3 (xor_3_out, not_3_out, Q[2]);
  xor xor_4 (xor_4_out, Q[2], and_1_out);
  not not_4 (not_4_out, or_2_out);
  xor xor_5 (xor_5_out, not_4_out, Q[3]);
  xor xor_6 (xor_6_out, Q[3], and_2_out);
  not not_5 (not_5_out, or_3_out);
  xor xor_7 (xor_7_out, not_5_out, Q[4]);
  xor xor_8 (xor_8_out, Q[4], and_3_out);
  not not_6 (not_6_out, or_4_out);
  xor xor_9 (xor_9_out, not_6_out, Q[5]);
  xor xor_10 (xor_10_out, Q[5], and_4_out);
  not not_7 (not_7_out, or_5_out);
  xor xor_11 (xor_11_out, not_7_out, Q[6]);
  xor xor_12 (xor_12_out, Q[6], and_5_out);
  not not_8 (not_8_out, or_6_out);
  xor xor_13 (xor_13_out, not_8_out, Q[7]);
  xor xor_14 (xor_14_out, Q[7], and_6_out);
  Multiplexer #(.select(2), .enable("false")) multiplexer_1 (
    .in0(Input[0]), .in1(not_1_out), .in2(not_1_out), .in3(1'b0), .out(multiplexer_1_out), .sel(FunSel));
  Multiplexer #(.select(2), .enable("false")) multiplexer_2 (
    .in0(Input[1]), .in1(xor_1_out), .in2(xor_2_out), .in3(1'b0), .out(multiplexer_2_out), .sel(FunSel));
  Multiplexer #(.select(2), .enable("false")) multiplexer_3 (
    .in0(Input[2]), .in1(xor_3_out), .in2(xor_4_out), .in3(1'b0), .out(multiplexer_3_out), .sel(FunSel));
  Multiplexer #(.select(2), .enable("false")) multiplexer_4 (
    .in0(Input[3]), .in1(xor_5_out), .in2(xor_6_out), .in3(1'b0), .out(multiplexer_4_out), .sel(FunSel));
  Multiplexer #(.select(2), .enable("false")) multiplexer_5 (
    .in0(Input[4]), .in1(xor_7_out), .in2(xor_8_out), .in3(1'b0), .out(multiplexer_5_out), .sel(FunSel));
  Multiplexer #(.select(2), .enable("false")) multiplexer_6 (
    .in0(Input[5]), .in1(xor_9_out), .in2(xor_10_out), .in3(1'b0), .out(multiplexer_6_out), .sel(FunSel));
  Multiplexer #(.select(2), .enable("false")) multiplexer_7 (
    .in0(Input[6]), .in1(xor_11_out), .in2(xor_12_out), .in3(1'b0), .out(multiplexer_7_out), .sel(FunSel));
  Multiplexer #(.select(2), .enable("false")) multiplexer_8 (
    .in0(Input[7]), .in1(xor_13_out), .in2(xor_14_out), .in3(1'b0), .out(multiplexer_8_out), .sel(FunSel));
  Clock clock_1 (.out(clock_1_out));
  D_Flip_Flop #(.enable("true")) d_ff_1 (
    .clk(clock_1_out), .D(multiplexer_1_out), .Q(Q[0]), .en(E));  // open: Qn, preset, reset
  D_Flip_Flop #(.enable("true")) d_ff_2 (
    .clk(clock_1_out), .D(multiplexer_2_out), .Q(Q[1]), .en(E));  // open: Qn, preset, reset
  D_Flip_Flop #(.enable("true")) d_ff_3 (
    .clk(clock_1_out), .D(multiplexer_3_out), .Q(Q[2]), .en(E));  // open: Qn, preset, reset
  D_Flip_Flop #(.enable("true")) d_ff_4 (
    .clk(clock_1_out), .D(multiplexer_4_out), .Q(Q[3]), .en(E));  // open: Qn, preset, reset
  D_Flip_Flop #(.enable("true")) d_ff_5 (
    .clk(clock_1_out), .D(multiplexer_5_out), .Q(Q[4]), .en(E));  // open: Qn, preset, reset
  D_Flip_Flop #(.enable("true")) d_ff_6 (
    .clk(clock_1_out), .D(multiplexer_6_out), .Q(Q[5]), .en(E));  // open: Qn, preset, reset
  D_Flip_Flop #(.enable("true")) d_ff_7 (
    .clk(clock_1_out), .D(multiplexer_7_out), .Q(Q[6]), .en(E));  // open: Qn, preset, reset
  D_Flip_Flop #(.enable("true")) d_ff_8 (
    .clk(clock_1_out), .D(multiplexer_8_out), .Q(Q[7]), .en(E));  // open: Qn, preset, reset
endmodule

module Register_file (
  input  [7:0] Input,
  input  [1:0] FunSel,
  input  [3:0] RegSel,
  input  [1:0] OutASel,
  input  [1:0] OutBSel,
  output [7:0] Output_A,
  output [7:0] Output_B
);

  wire [7:0] n8_bit_register_1_q, n8_bit_register_2_q, n8_bit_register_3_q, n8_bit_register_4_q;

  _8_bit_register u_8_bit_register_1 (.E(RegSel[0]), .Input(Input), .FunSel(FunSel), .Q(n8_bit_register_1_q));
  _8_bit_register u_8_bit_register_2 (.E(RegSel[1]), .Input(Input), .FunSel(FunSel), .Q(n8_bit_register_2_q));
  _8_bit_register u_8_bit_register_3 (.E(RegSel[2]), .Input(Input), .FunSel(FunSel), .Q(n8_bit_register_3_q));
  _8_bit_register u_8_bit_register_4 (.E(RegSel[3]), .Input(Input), .FunSel(FunSel), .Q(n8_bit_register_4_q));
  Multiplexer #(.select(2), .width(8), .enable("false")) multiplexer_1 (
    .in0(n8_bit_register_4_q), .in1(n8_bit_register_3_q), .in2(n8_bit_register_2_q),
    .in3(n8_bit_register_1_q), .out(Output_B), .sel(OutBSel));
  Multiplexer #(.select(2), .width(8), .enable("false")) multiplexer_2 (
    .in0(n8_bit_register_4_q), .in1(n8_bit_register_3_q), .in2(n8_bit_register_2_q),
    .in3(n8_bit_register_1_q), .out(Output_A), .sel(OutASel));
endmodule

module Address_Registers (
  input  [7:0] Input,
  input  [1:0] FunSel,
  input  [2:0] RegSel,
  input  [1:0] OutCSel,
  output [7:0] Output_C
);

  wire [7:0] n8_bit_register_1_q, n8_bit_register_2_q, n8_bit_register_3_q;

  _8_bit_register u_8_bit_register_1 (.E(RegSel[0]), .Input(Input), .FunSel(FunSel), .Q(n8_bit_register_1_q));
  _8_bit_register u_8_bit_register_2 (.E(RegSel[1]), .Input(Input), .FunSel(FunSel), .Q(n8_bit_register_2_q));
  _8_bit_register u_8_bit_register_3 (.E(RegSel[2]), .Input(Input), .FunSel(FunSel), .Q(n8_bit_register_3_q));
  Multiplexer #(.select(2), .width(8), .enable("false")) multiplexer_1 (
    .in0(n8_bit_register_3_q), .in1(n8_bit_register_3_q), .in2(n8_bit_register_2_q),
    .in3(n8_bit_register_1_q), .out(Output_C), .sel(OutCSel));

  // Notes on the sheet:
  //   AR
  //   SP
  //   PC
endmodule
