// Logisim project 8bit_funsel_register.circ as structural Verilog: 1 circuit, main circuit 8bit FunSel Register
module _8bit_FunSel_Register (
  input  Enable,
  input  Sel,
  input  Fun,
  input  [7:0] I_MSB,
  output [7:0] Q_MSB,
  output Cout
);

  wire and_1_out, and_2_out, and_3_out, and_4_out, and_5_out, and_6_out, and_7_out, and_8_out, and_17_out,
       and_18_out, and_19_out, and_20_out, and_21_out, and_22_out, and_23_out, and_24_out, clock_1_out,
       decoder_1_out0, decoder_1_out1, decoder_1_out2, decoder_1_out3, or_1_out;
  wire [7:0] adder_1_out, xor_1_out;

  xor xor_1 (xor_1_out[0], 1'b1, decoder_1_out1);
  xor xor_2 (xor_1_out[7], 1'b0, decoder_1_out1);
  Decoder #(.select(2), .enable("false")) decoder_1 (
    .out0(decoder_1_out0), .out1(decoder_1_out1), .out2(decoder_1_out2), .out3(decoder_1_out3),
    .sel({Fun, Sel}));
  Adder adder_1 (
    .a(Q_MSB), .b({{7{xor_1_out[7]}}, xor_1_out[0]}), .out(adder_1_out), .cin(decoder_1_out1), .cout(Cout));
  or or_1 (or_1_out, decoder_1_out1, decoder_1_out2);
  and and_1 (and_1_out, decoder_1_out0, I_MSB[7]);
  and and_2 (and_2_out, decoder_1_out0, I_MSB[6]);
  and and_3 (and_3_out, decoder_1_out0, I_MSB[5]);
  and and_4 (and_4_out, decoder_1_out0, I_MSB[4]);
  and and_5 (and_5_out, decoder_1_out0, I_MSB[3]);
  and and_6 (and_6_out, decoder_1_out0, I_MSB[2]);
  and and_7 (and_7_out, decoder_1_out0, I_MSB[1]);
  and and_8 (and_8_out, decoder_1_out0, I_MSB[0]);
  and and_9 (and_8_out, adder_1_out[0], or_1_out);
  and and_10 (and_7_out, adder_1_out[1], or_1_out);
  and and_11 (and_6_out, adder_1_out[2], or_1_out);
  and and_12 (and_5_out, adder_1_out[3], or_1_out);
  and and_13 (and_4_out, adder_1_out[4], or_1_out);
  and and_14 (and_3_out, adder_1_out[5], or_1_out);
  and and_15 (and_2_out, adder_1_out[6], or_1_out);
  and and_16 (and_1_out, adder_1_out[7], or_1_out);
  and and_17 (and_17_out, and_8_out, Enable);
  and and_18 (and_18_out, and_7_out, Enable);
  and and_19 (and_19_out, and_6_out, Enable);
  and and_20 (and_20_out, and_5_out, Enable);
  and and_21 (and_21_out, and_4_out, Enable);
  and and_22 (and_22_out, and_3_out, Enable);
  and and_23 (and_23_out, and_2_out, Enable);
  and and_24 (and_24_out, and_1_out, Enable);
  D_Flip_Flop d_ff_1 (
    .clk(clock_1_out), .D(and_17_out), .Q(Q_MSB[0]), .preset(1'b0), .reset(decoder_1_out3));  // open: Qn
  D_Flip_Flop d_ff_2 (
    .clk(clock_1_out), .D(and_18_out), .Q(Q_MSB[1]), .preset(1'b0), .reset(decoder_1_out3));  // open: Qn
  D_Flip_Flop d_ff_3 (
    .clk(clock_1_out), .D(and_19_out), .Q(Q_MSB[2]), .preset(1'b0), .reset(decoder_1_out3));  // open: Qn
  D_Flip_Flop d_ff_4 (
    .clk(clock_1_out), .D(and_20_out), .Q(Q_MSB[3]), .preset(1'b0), .reset(decoder_1_out3));  // open: Qn
  D_Flip_Flop d_ff_5 (
    .clk(clock_1_out), .D(and_21_out), .Q(Q_MSB[4]), .preset(1'b0), .reset(decoder_1_out3));  // open: Qn
  D_Flip_Flop d_ff_6 (
    .clk(clock_1_out), .D(and_22_out), .Q(Q_MSB[5]), .preset(1'b0), .reset(decoder_1_out3));  // open: Qn
  D_Flip_Flop d_ff_7 (
    .clk(clock_1_out), .D(and_23_out), .Q(Q_MSB[6]), .preset(1'b0), .reset(decoder_1_out3));  // open: Qn
  D_Flip_Flop d_ff_8 (
    .clk(clock_1_out), .D(and_24_out), .Q(Q_MSB[7]), .preset(1'b0), .reset(decoder_1_out3));  // open: Qn
  Clock clock_1 (.out(clock_1_out));

  // Notes on the sheet:
  //   I
  //   I:LSB
  //   LSB
  //   MSB
  //   Reset
  //   CLK
  //   Q:LSB
  //   Q
endmodule
