// Logisim project FunSel Register.circ as structural Verilog: 5 circuits, main circuit 8bit FunSel Register
module _8bit_FunSel_Register (
  input  in_1,
  input  Sel,
  input  Fun,
  input  [7:0] I_MSB,
  output [7:0] Q_MSB
);

  wire adder_1_cout, and_1_out, and_2_out, and_3_out, and_4_out, and_5_out, and_6_out, and_7_out, and_8_out,
       and_9_out, and_10_out, clock_1_out, decoder_1_out1, decoder_1_out2, decoder_1_out3, multiplexer_1_out,
       multiplexer_2_out, multiplexer_3_out, multiplexer_4_out, multiplexer_5_out, multiplexer_6_out,
       multiplexer_7_out, multiplexer_8_out, or_1_out;
  wire [1:1] not_1_out;
  wire [7:0] adder_1_out, xor_1_out;

  xor xor_1 (xor_1_out[0], 1'b1, decoder_1_out1);
  xor xor_2 (xor_1_out[7], 1'b0, decoder_1_out1);
  Decoder #(.select(2), .enable("false")) decoder_1 (
    .out1(decoder_1_out1), .out2(decoder_1_out2), .out3(decoder_1_out3), .sel({Fun, Sel}));  // open: out0
  Adder adder_1 (
    .a(Q_MSB), .b({{7{xor_1_out[7]}}, xor_1_out[0]}), .out(adder_1_out), .cin(decoder_1_out1),
    .cout(adder_1_cout));
  or or_1 (or_1_out, decoder_1_out1, decoder_1_out2);
  and and_1 (and_1_out, or_1_out, in_1);
  and and_2 (and_2_out, adder_1_out[0], and_1_out);
  and and_3 (and_3_out, adder_1_out[1], and_1_out);
  and and_4 (and_4_out, adder_1_out[2], and_1_out);
  and and_5 (and_5_out, adder_1_out[3], and_1_out);
  and and_6 (and_6_out, adder_1_out[4], and_1_out);
  and and_7 (and_7_out, adder_1_out[5], and_1_out);
  and and_8 (and_8_out, adder_1_out[6], and_1_out);
  and and_9 (and_9_out, adder_1_out[7], and_1_out);
  Multiplexer #(.select(2), .enable("false")) multiplexer_1 (
    .in0(Q_MSB[0]), .in1(and_2_out), .in2(Q_MSB[0]), .in3(I_MSB[0]), .out(multiplexer_1_out),
    .sel({not_1_out[1], in_1}));
  Multiplexer #(.select(2), .enable("false")) multiplexer_2 (
    .in0(Q_MSB[1]), .in1(and_3_out), .in2(Q_MSB[1]), .in3(I_MSB[1]), .out(multiplexer_2_out),
    .sel({not_1_out[1], in_1}));
  Multiplexer #(.select(2), .enable("false")) multiplexer_3 (
    .in0(Q_MSB[2]), .in1(and_4_out), .in2(Q_MSB[2]), .in3(I_MSB[2]), .out(multiplexer_3_out),
    .sel({not_1_out[1], in_1}));
  Multiplexer #(.select(2), .enable("false")) multiplexer_4 (
    .in0(Q_MSB[3]), .in1(and_5_out), .in2(Q_MSB[3]), .in3(I_MSB[3]), .out(multiplexer_4_out),
    .sel({not_1_out[1], in_1}));
  Multiplexer #(.select(2), .enable("false")) multiplexer_5 (
    .in0(Q_MSB[4]), .in1(and_6_out), .in2(Q_MSB[4]), .in3(I_MSB[4]), .out(multiplexer_5_out),
    .sel({not_1_out[1], in_1}));
  Multiplexer #(.select(2), .enable("false")) multiplexer_6 (
    .in0(Q_MSB[5]), .in1(and_7_out), .in2(Q_MSB[5]), .in3(I_MSB[5]), .out(multiplexer_6_out),
    .sel({not_1_out[1], in_1}));
  Multiplexer #(.select(2), .enable("false")) multiplexer_7 (
    .in0(Q_MSB[6]), .in1(and_8_out), .in2(Q_MSB[6]), .in3(I_MSB[6]), .out(multiplexer_7_out),
    .sel({not_1_out[1], in_1}));
  Multiplexer #(.select(2), .enable("false")) multiplexer_8 (
    .in0(Q_MSB[7]), .in1(and_9_out), .in2(Q_MSB[7]), .in3(I_MSB[7]), .out(multiplexer_8_out),
    .sel({not_1_out[1], in_1}));
  not not_1 (not_1_out[1], or_1_out);
  and and_10 (and_10_out, in_1, decoder_1_out3);
  Clock clock_1 (.out(clock_1_out));
  D_Flip_Flop d_ff_1 (
    .clk(clock_1_out), .D(multiplexer_1_out), .Q(Q_MSB[0]), .preset(1'b0), .reset(and_10_out));  // open: Qn
  D_Flip_Flop d_ff_2 (
    .clk(clock_1_out), .D(multiplexer_2_out), .Q(Q_MSB[1]), .preset(1'b0), .reset(and_10_out));  // open: Qn
  D_Flip_Flop d_ff_3 (
    .clk(clock_1_out), .D(multiplexer_3_out), .Q(Q_MSB[2]), .preset(1'b0), .reset(and_10_out));  // open: Qn
  D_Flip_Flop d_ff_4 (
    .clk(clock_1_out), .D(multiplexer_4_out), .Q(Q_MSB[3]), .preset(1'b0), .reset(and_10_out));  // open: Qn
  D_Flip_Flop d_ff_5 (
    .clk(clock_1_out), .D(multiplexer_5_out), .Q(Q_MSB[4]), .preset(1'b0), .reset(and_10_out));  // open: Qn
  D_Flip_Flop d_ff_6 (
    .clk(clock_1_out), .D(multiplexer_6_out), .Q(Q_MSB[5]), .preset(1'b0), .reset(and_10_out));  // open: Qn
  D_Flip_Flop d_ff_7 (
    .clk(clock_1_out), .D(multiplexer_7_out), .Q(Q_MSB[6]), .preset(1'b0), .reset(and_10_out));  // open: Qn
  D_Flip_Flop d_ff_8 (
    .clk(clock_1_out), .D(multiplexer_8_out), .Q(Q_MSB[7]), .preset(1'b0), .reset(and_10_out));  // open: Qn

  // Notes on the sheet:
  //   I
  //   I:LSB
  //   Enable
  //   CLK
  //   LSB
  //   MSB
  //   Reset
  //   Cout
  //   Q:LSB
  //   Q
endmodule

module _16bit_FunSel_Register (
  input  in_1,
  input  Sel,
  input  Fun,
  input  [15:0] I_MSB,
  output [15:0] Q_MSB
);

  wire adder_1_cout, and_1_out, and_2_out, and_3_out, and_4_out, and_5_out, and_6_out, and_7_out, and_8_out,
       and_9_out, and_10_out, and_11_out, and_12_out, and_13_out, and_14_out, and_15_out, and_16_out,
       and_17_out, and_18_out, clock_1_out, decoder_1_out1, decoder_1_out2, decoder_1_out3,
       multiplexer_1_out, multiplexer_2_out, multiplexer_3_out, multiplexer_4_out, multiplexer_5_out,
       multiplexer_6_out, multiplexer_7_out, multiplexer_8_out, multiplexer_9_out, multiplexer_10_out,
       multiplexer_11_out, multiplexer_12_out, multiplexer_13_out, multiplexer_14_out, multiplexer_15_out,
       multiplexer_16_out, or_1_out;
  wire [1:1] not_1_out;
  wire [15:0] adder_1_out, xor_2_out;

  xor xor_1 (xor_2_out[15], 1'b0, decoder_1_out1);
  xor xor_2 (xor_2_out[0], 1'b1, decoder_1_out1);
  Decoder #(.select(2), .enable("false")) decoder_1 (
    .out1(decoder_1_out1), .out2(decoder_1_out2), .out3(decoder_1_out3), .sel({Fun, Sel}));  // open: out0
  Adder #(.width(16)) adder_1 (
    .a(Q_MSB), .b({{15{xor_2_out[15]}}, xor_2_out[0]}), .out(adder_1_out), .cin(decoder_1_out1),
    .cout(adder_1_cout));
  or or_1 (or_1_out, decoder_1_out1, decoder_1_out2);
  and and_1 (and_1_out, adder_1_out[0], and_17_out);
  and and_2 (and_2_out, adder_1_out[1], and_17_out);
  and and_3 (and_3_out, adder_1_out[2], and_17_out);
  and and_4 (and_4_out, adder_1_out[3], and_17_out);
  and and_5 (and_5_out, adder_1_out[4], and_17_out);
  and and_6 (and_6_out, adder_1_out[5], and_17_out);
  and and_7 (and_7_out, adder_1_out[6], and_17_out);
  and and_8 (and_8_out, adder_1_out[7], and_17_out);
  and and_9 (and_9_out, adder_1_out[8], and_17_out);
  and and_10 (and_10_out, adder_1_out[9], and_17_out);
  and and_11 (and_11_out, adder_1_out[10], and_17_out);
  and and_12 (and_12_out, adder_1_out[11], and_17_out);
  and and_13 (and_13_out, adder_1_out[12], and_17_out);
  and and_14 (and_14_out, adder_1_out[13], and_17_out);
  and and_15 (and_15_out, adder_1_out[14], and_17_out);
  and and_16 (and_16_out, adder_1_out[15], and_17_out);
  and and_17 (and_17_out, or_1_out, in_1);
  not not_1 (not_1_out[1], or_1_out);
  Multiplexer #(.select(2), .enable("false")) multiplexer_1 (
    .in0(Q_MSB[0]), .in1(and_1_out), .in2(Q_MSB[0]), .in3(I_MSB[0]), .out(multiplexer_1_out),
    .sel({not_1_out[1], in_1}));
  Multiplexer #(.select(2), .enable("false")) multiplexer_2 (
    .in0(Q_MSB[1]), .in1(and_2_out), .in2(Q_MSB[1]), .in3(I_MSB[1]), .out(multiplexer_2_out),
    .sel({not_1_out[1], in_1}));
  Multiplexer #(.select(2), .enable("false")) multiplexer_3 (
    .in0(Q_MSB[2]), .in1(and_3_out), .in2(Q_MSB[2]), .in3(I_MSB[2]), .out(multiplexer_3_out),
    .sel({not_1_out[1], in_1}));
  Multiplexer #(.select(2), .enable("false")) multiplexer_4 (
    .in0(Q_MSB[3]), .in1(and_4_out), .in2(Q_MSB[3]), .in3(I_MSB[3]), .out(multiplexer_4_out),
    .sel({not_1_out[1], in_1}));
  Multiplexer #(.select(2), .enable("false")) multiplexer_5 (
    .in0(Q_MSB[4]), .in1(and_5_out), .in2(Q_MSB[4]), .in3(I_MSB[4]), .out(multiplexer_5_out),
    .sel({not_1_out[1], in_1}));
  Multiplexer #(.select(2), .enable("false")) multiplexer_6 (
    .in0(Q_MSB[5]), .in1(and_6_out), .in2(Q_MSB[5]), .in3(I_MSB[5]), .out(multiplexer_6_out),
    .sel({not_1_out[1], in_1}));
  Multiplexer #(.select(2), .enable("false")) multiplexer_7 (
    .in0(Q_MSB[6]), .in1(and_7_out), .in2(Q_MSB[6]), .in3(I_MSB[6]), .out(multiplexer_7_out),
    .sel({not_1_out[1], in_1}));
  Multiplexer #(.select(2), .enable("false")) multiplexer_8 (
    .in0(Q_MSB[7]), .in1(and_8_out), .in2(Q_MSB[7]), .in3(I_MSB[7]), .out(multiplexer_8_out),
    .sel({not_1_out[1], in_1}));
  Multiplexer #(.select(2), .enable("false")) multiplexer_9 (
    .in0(Q_MSB[8]), .in1(and_9_out), .in2(Q_MSB[8]), .in3(I_MSB[8]), .out(multiplexer_9_out),
    .sel({not_1_out[1], in_1}));
  Multiplexer #(.select(2), .enable("false")) multiplexer_10 (
    .in0(Q_MSB[9]), .in1(and_10_out), .in2(Q_MSB[9]), .in3(I_MSB[9]), .out(multiplexer_10_out),
    .sel({not_1_out[1], in_1}));
  Multiplexer #(.select(2), .enable("false")) multiplexer_11 (
    .in0(Q_MSB[10]), .in1(and_11_out), .in2(Q_MSB[10]), .in3(I_MSB[10]), .out(multiplexer_11_out),
    .sel({not_1_out[1], in_1}));
  Multiplexer #(.select(2), .enable("false")) multiplexer_12 (
    .in0(Q_MSB[11]), .in1(and_12_out), .in2(Q_MSB[11]), .in3(I_MSB[11]), .out(multiplexer_12_out),
    .sel({not_1_out[1], in_1}));
  Multiplexer #(.select(2), .enable("false")) multiplexer_13 (
    .in0(Q_MSB[12]), .in1(and_13_out), .in2(Q_MSB[12]), .in3(I_MSB[12]), .out(multiplexer_13_out),
    .sel({not_1_out[1], in_1}));
  Multiplexer #(.select(2), .enable("false")) multiplexer_14 (
    .in0(Q_MSB[13]), .in1(and_14_out), .in2(Q_MSB[13]), .in3(I_MSB[13]), .out(multiplexer_14_out),
    .sel({not_1_out[1], in_1}));
  Multiplexer #(.select(2), .enable("false")) multiplexer_15 (
    .in0(Q_MSB[14]), .in1(and_15_out), .in2(Q_MSB[14]), .in3(I_MSB[14]), .out(multiplexer_15_out),
    .sel({not_1_out[1], in_1}));
  Multiplexer #(.select(2), .enable("false")) multiplexer_16 (
    .in0(Q_MSB[15]), .in1(and_16_out), .in2(Q_MSB[15]), .in3(I_MSB[15]), .out(multiplexer_16_out),
    .sel({not_1_out[1], in_1}));
  D_Flip_Flop d_ff_1 (
    .clk(clock_1_out), .D(multiplexer_1_out), .Q(Q_MSB[0]), .preset(1'b0), .reset(and_18_out));  // open: Qn
  D_Flip_Flop d_ff_2 (
    .clk(clock_1_out), .D(multiplexer_2_out), .Q(Q_MSB[1]), .preset(1'b0), .reset(and_18_out));  // open: Qn
  D_Flip_Flop d_ff_3 (
    .clk(clock_1_out), .D(multiplexer_3_out), .Q(Q_MSB[2]), .preset(1'b0), .reset(and_18_out));  // open: Qn
  D_Flip_Flop d_ff_4 (
    .clk(clock_1_out), .D(multiplexer_4_out), .Q(Q_MSB[3]), .preset(1'b0), .reset(and_18_out));  // open: Qn
  D_Flip_Flop d_ff_5 (
    .clk(clock_1_out), .D(multiplexer_5_out), .Q(Q_MSB[4]), .preset(1'b0), .reset(and_18_out));  // open: Qn
  D_Flip_Flop d_ff_6 (
    .clk(clock_1_out), .D(multiplexer_6_out), .Q(Q_MSB[5]), .preset(1'b0), .reset(and_18_out));  // open: Qn
  D_Flip_Flop d_ff_7 (
    .clk(clock_1_out), .D(multiplexer_7_out), .Q(Q_MSB[6]), .preset(1'b0), .reset(and_18_out));  // open: Qn
  D_Flip_Flop d_ff_8 (
    .clk(clock_1_out), .D(multiplexer_8_out), .Q(Q_MSB[7]), .preset(1'b0), .reset(and_18_out));  // open: Qn
  D_Flip_Flop d_ff_9 (
    .clk(clock_1_out), .D(multiplexer_9_out), .Q(Q_MSB[8]), .preset(1'b0), .reset(and_18_out));  // open: Qn
  D_Flip_Flop d_ff_10 (
    .clk(clock_1_out), .D(multiplexer_10_out), .Q(Q_MSB[9]), .preset(1'b0), .reset(and_18_out));  // open: Qn
  D_Flip_Flop d_ff_11 (
    .clk(clock_1_out), .D(multiplexer_11_out), .Q(Q_MSB[10]), .preset(1'b0), .reset(and_18_out));  // open: Qn
  D_Flip_Flop d_ff_12 (
    .clk(clock_1_out), .D(multiplexer_12_out), .Q(Q_MSB[11]), .preset(1'b0), .reset(and_18_out));  // open: Qn
  D_Flip_Flop d_ff_13 (
    .clk(clock_1_out), .D(multiplexer_13_out), .Q(Q_MSB[12]), .preset(1'b0), .reset(and_18_out));  // open: Qn
  D_Flip_Flop d_ff_14 (
    .clk(clock_1_out), .D(multiplexer_14_out), .Q(Q_MSB[13]), .preset(1'b0), .reset(and_18_out));  // open: Qn
  D_Flip_Flop d_ff_15 (
    .clk(clock_1_out), .D(multiplexer_15_out), .Q(Q_MSB[14]), .preset(1'b0), .reset(and_18_out));  // open: Qn
  D_Flip_Flop d_ff_16 (
    .clk(clock_1_out), .D(multiplexer_16_out), .Q(Q_MSB[15]), .preset(1'b0), .reset(and_18_out));  // open: Qn
  and and_18 (and_18_out, in_1, decoder_1_out3);
  Clock clock_1 (.out(clock_1_out));

  // Notes on the sheet:
  //   Cout
  //   I
  //   I:LSB
  //   Enable
  //   LSB
  //   CLK
  //   MSB
  //   Reset
  //   Q:LSB
  //   Q
endmodule

module RegSel (
  input  [7:0] I,
  input  [3:0] RegSel,
  input  Fun,
  input  Sel,
  input  [1:0] OutASel,
  input  [1:0] OutBSel,
  output [7:0] OutA,
  output [7:0] OutB
);

  wire decoder_1_out1, decoder_1_out2, decoder_1_out3, decoder_1_out4, decoder_1_out5, decoder_1_out6,
       decoder_1_out7, decoder_1_out8, decoder_1_out9, decoder_1_out10, decoder_1_out12, or_1_out, or_2_out,
       or_3_out, or_4_out;
  wire [7:0] n8bit_funsel_register_1_q_msb, n8bit_funsel_register_2_q_msb, n8bit_funsel_register_3_q_msb,
       n8bit_funsel_register_4_q_msb;

  Decoder #(.select(4), .enable("false")) decoder_1 (
    .out1(decoder_1_out1), .out2(decoder_1_out2), .out3(decoder_1_out3), .out4(decoder_1_out4),
    .out5(decoder_1_out5), .out6(decoder_1_out6), .out7(decoder_1_out7), .out8(decoder_1_out8),
    .out9(decoder_1_out9), .out10(decoder_1_out10), .out11(decoder_1_out4), .out12(decoder_1_out12),
    .out13(decoder_1_out6), .out14(decoder_1_out5), .out15(decoder_1_out6), .sel(RegSel));  // open: out0
  or or_1 (or_1_out, decoder_1_out1, decoder_1_out3, decoder_1_out5, decoder_1_out7, decoder_1_out9, decoder_1_out4, decoder_1_out6, decoder_1_out6);
  or or_2 (or_2_out, decoder_1_out2, decoder_1_out3, decoder_1_out6, decoder_1_out7, decoder_1_out10, decoder_1_out4, decoder_1_out5, decoder_1_out6);
  or or_3 (or_3_out, decoder_1_out4, decoder_1_out5, decoder_1_out6, decoder_1_out7, decoder_1_out12, decoder_1_out6, decoder_1_out5, decoder_1_out6);
  or or_4 (or_4_out, decoder_1_out8, decoder_1_out9, decoder_1_out10, decoder_1_out4, decoder_1_out12, decoder_1_out6, decoder_1_out5, decoder_1_out6);
  _8bit_FunSel_Register u_8bit_funsel_register_1 (
    .Sel(Sel), .Fun(Fun), .in_1(or_1_out), .I_MSB(I), .Q_MSB(n8bit_funsel_register_1_q_msb));
  _8bit_FunSel_Register u_8bit_funsel_register_2 (
    .Sel(Sel), .Fun(Fun), .in_1(or_2_out), .I_MSB(I), .Q_MSB(n8bit_funsel_register_2_q_msb));
  _8bit_FunSel_Register u_8bit_funsel_register_3 (
    .Sel(Sel), .Fun(Fun), .in_1(or_3_out), .I_MSB(I), .Q_MSB(n8bit_funsel_register_3_q_msb));
  _8bit_FunSel_Register u_8bit_funsel_register_4 (
    .Sel(Sel), .Fun(Fun), .in_1(or_4_out), .I_MSB(I), .Q_MSB(n8bit_funsel_register_4_q_msb));
  Multiplexer #(.select(2), .width(8), .enable("false")) multiplexer_1 (
    .in0(n8bit_funsel_register_1_q_msb), .in1(n8bit_funsel_register_2_q_msb),
    .in2(n8bit_funsel_register_3_q_msb), .in3(n8bit_funsel_register_4_q_msb), .out(OutA), .sel(OutASel));
  Multiplexer #(.select(2), .width(8), .enable("false")) multiplexer_2 (
    .in0(n8bit_funsel_register_1_q_msb), .in1(n8bit_funsel_register_2_q_msb),
    .in2(n8bit_funsel_register_3_q_msb), .in3(n8bit_funsel_register_4_q_msb), .out(OutB), .sel(OutBSel));
endmodule

module OutC_Register (
  input  [7:0] I,
  input  [2:0] RegSel,
  input  Fun,
  input  Sel,
  output [7:0] out_5
);

  wire decoder_1_out1, decoder_1_out2, decoder_1_out3, decoder_1_out4, decoder_1_out5, decoder_1_out6,
       decoder_1_out7, or_1_out, or_2_out, or_3_out;
  wire [7:0] AR_q_msb, PC_q_msb, SP_q_msb;

  Decoder #(.select(3), .enable("false")) decoder_1 (
    .out1(decoder_1_out1), .out2(decoder_1_out2), .out3(decoder_1_out3), .out4(decoder_1_out4),
    .out5(decoder_1_out5), .out6(decoder_1_out6), .out7(decoder_1_out7), .sel(RegSel));  // open: out0
  or or_1 (or_1_out, decoder_1_out1, decoder_1_out3, decoder_1_out5, decoder_1_out7);
  or or_2 (or_2_out, decoder_1_out2, decoder_1_out3, decoder_1_out6, decoder_1_out7);
  or or_3 (or_3_out, decoder_1_out4, decoder_1_out5, decoder_1_out6, decoder_1_out7);
  _8bit_FunSel_Register AR (.Sel(Sel), .Fun(Fun), .in_1(or_1_out), .I_MSB(I), .Q_MSB(AR_q_msb));
  _8bit_FunSel_Register SP (.Sel(Sel), .Fun(Fun), .in_1(or_2_out), .I_MSB(I), .Q_MSB(SP_q_msb));
  _8bit_FunSel_Register PC (.Sel(Sel), .Fun(Fun), .in_1(or_3_out), .I_MSB(I), .Q_MSB(PC_q_msb));
  Multiplexer #(.select(2), .width(8), .enable("false")) multiplexer_1 (
    .in0(AR_q_msb), .in1(SP_q_msb), .in2(PC_q_msb), .in3(PC_q_msb), .out(out_5));  // open: sel
endmodule

module IR_Register (
  input  [7:0] I,
  input  Fun,
  input  Sel,
  input  L_H,
  input  Enable
);

  wire or_1_out;

  or or_1 (or_1_out, Fun, Sel);
  // OR_Gate or_2 has open pins: in0=or_1_out, in1=L_H, out=open
  _8bit_FunSel_Register u_8bit_funsel_register_1 (.in_1(Enable));  // open: Sel, Fun, I_MSB, Q_MSB
  _8bit_FunSel_Register u_8bit_funsel_register_2 (.in_1(Enable));  // open: Sel, Fun, I_MSB, Q_MSB
  Multiplexer #(.enable("false")) multiplexer_1 ();  // open: in0, in1, out, sel
endmodule
