// Logisim project project1.circ as structural Verilog: 5 circuits, main circuit 8 bit register
module _8_bit_register (
  input  E,
  input  [7:0] Input,
  input  [1:0] FunSel,
  output [7:0] Q
);

  wire and_1_out, and_2_out, and_3_out, and_4_out, and_5_out, and_6_out, clock_1_out, multiplexer_1_out,
       multiplexer_2_out, multiplexer_3_out, multiplexer_4_out, multiplexer_5_out, multiplexer_6_out,
       multiplexer_7_out, multiplexer_8_out, not_1_out, not_2_out, not_3_out, not_4_out, not_5_out,
       not_6_out, not_7_out, not_8_out, or_1_out, or_2_out, or_3_out, or_4_out, or_5_out, or_6_out,
       xor_1_out, xor_2_out, xor_3_out, xor_4_out, xor_5_out, xor_6_out, xor_7_out, xor_8_out, xor_9_out,
       xor_10_out, xor_11_out, xor_12_out, xor_13_out, xor_14_out;

  Hex_Digit_Display hex_digit_display_1 (.value(Input[7:4]));  // open: dp
  Hex_Digit_Display hex_digit_display_2 (.value(Input[3:0]));  // open: dp
  not not_1 (not_1_out, Q[0]);
  and and_1 (and_1_out, Q[0], Q[1]);
  and and_2 (and_2_out, Q[0], Q[1], Q[2]);
  and and_3 (and_3_out, Q[0], Q[1], Q[2], Q[3]);
  and and_4 (and_4_out, Q[0], Q[1], Q[2], Q[3], Q[4]);
  and and_5 (and_5_out, Q[0], Q[1], Q[2], Q[3], Q[4], Q[5]);
  and and_6 (and_6_out, Q[0], Q[1], Q[2], Q[3], Q[4], Q[5], Q[6]);
  not not_2 (not_2_out, Q[0]);
  or or_1 (or_1_out, Q[1], Q[0]);
  or or_2 (or_2_out, Q[2], Q[1], Q[0]);
  or or_3 (or_3_out, Q[3], Q[2], Q[1], Q[0]);
  or or_4 (or_4_out, Q[4], Q[3], Q[2], Q[1], Q[0]);
  or or_5 (or_5_out, Q[5], Q[4], Q[3], Q[2], Q[1], Q[0]);
  or or_6 (or_6_out, Q[6], Q[5], Q[4], Q[3], Q[2], Q[1], Q[0]);
  xor xor_1 (xor_1_out, not_2_out, Q[1]);
  xor xor_2 (xor_2_out, Q[0], Q[1]);
  not not_3 (not_3_out, or_1_out);
  xor xor_3 (xor_3_out, not_3_out, Q[2]);
  xor xor_4 (xor_4_out, Q[2], and_1_out);
  not not_4 (not_4_out, or_2_out);
  xor xor_5 (xor_5_out, not_4_out, Q[3]);
  xor xor_6 (xor_6_out, Q[3], and_2_out);
  not not_5 (not_5_out, or_3_out);
  xor xor_7 (xor_7_out, not_5_out, Q[4]);
  xor xor_8 (xor_8_out, Q[4], and_3_out);
  not not_6 (not_6_out, or_4_out);
  xor xor_9 (xor_9_out, not_6_out, Q[5]);
  xor xor_10 (xor_10_out, Q[5], and_4_out);
  not not_7 (not_7_out, or_5_out);
  xor xor_11 (xor_11_out, not_7_out, Q[6]);
  xor xor_12 (xor_12_out, Q[6], and_5_out);
  not not_8 (not_8_out, or_6_out);
  xor xor_13 (xor_13_out, not_8_out, Q[7]);
  xor xor_14 (xor_14_out, Q[7], and_6_out);
  Multiplexer #(.select(2), .enable("false")) multiplexer_1 (
    .in0(Input[0]), .in1(not_1_out), .in2(not_1_out), .in3(1'b0), .out(multiplexer_1_out), .sel(FunSel));
  Multiplexer #(.select(2), .enable("false")) multiplexer_2 (
    .in0(Input[1]), .in1(xor_1_out), .in2(xor_2_out), .in3(1'b0), .out(multiplexer_2_out), .sel(FunSel));
  Multiplexer #(.select(2), .enable("false")) multiplexer_3 (
    .in0(Input[2]), .in1(xor_3_out), .in2(xor_4_out), .in3(1'b0), .out(multiplexer_3_out), .sel(FunSel));
  Multiplexer #(.select(2), .enable("false")) multiplexer_4 (
    .in0(Input[3]), .in1(xor_5_out), .in2(xor_6_out), .in3(1'b0), .out(multiplexer_4_out), .sel(FunSel));
  Multiplexer #(.select(2), .enable("false")) multiplexer_5 (
    .in0(Input[4]), .in1(xor_7_out), .in2(xor_8_out), .in3(1'b0), .out(multiplexer_5_out), .sel(FunSel));
  Multiplexer #(.select(2), .enable("false")) multiplexer_6 (
    .in0(Input[5]), .in1(xor_9_out), .in2(xor_10_out), .in3(1'b0), .out(multiplexer_6_out), .sel(FunSel));
  Multiplexer #(.select(2), .enable("false")) multiplexer_7 (
    .in0(Input[6]), .in1(xor_11_out), .in2(xor_12_out), .in3(1'b0), .out(multiplexer_7_out), .sel(FunSel));
  Multiplexer #(.select(2), .enable("false")) multiplexer_8 (
    .in0(Input[7]), .in1(xor_13_out), .in2(xor_14_out), .in3(1'b0), .out(multiplexer_8_out), .sel(FunSel));
  Clock clock_1 (.out(clock_1_out));
  D_Flip_Flop #(.enable("true")) d_ff_1 (
    .clk(clock_1_out), .D(multiplexer_1_out), .Q(Q[0]), .en(E));  // open: Qn, preset, reset
  D_Flip_Flop #(.enable("true")) d_ff_2 (
    .clk(clock_1_out), .D(multiplexer_2_out), .Q(Q[1]), .en(E));  // open: Qn, preset, reset
  D_Flip_Flop #(.enable("true")) d_ff_3 (
    .clk(clock_1_out), .D(multiplexer_3_out), .Q(Q[2]), .en(E));  // open: Qn, preset, reset
  D_Flip_Flop #(.enable("true")) d_ff_4 (
    .clk(clock_1_out), .D(multiplexer_4_out), .Q(Q[3]), .en(E));  // open: Qn, preset, reset
  D_Flip_Flop #(.enable("true")) d_ff_5 (
    .clk(clock_1_out), .D(multiplexer_5_out), .Q(Q[4]), .en(E));  // open: Qn, preset, reset
  D_Flip_Flop #(.enable("true")) d_ff_6 (
    .clk(clock_1_out), .D(multiplexer_6_out), .Q(Q[5]), .en(E));  // open: Qn, preset, reset
  D_Flip_Flop #(.enable("true")) d_ff_7 (
    .clk(clock_1_out), .D(multiplexer_7_out), .Q(Q[6]), .en(E));  // open: Qn, preset, reset
  D_Flip_Flop #(.enable("true")) d_ff_8 (
    .clk(clock_1_out), .D(multiplexer_8_out), .Q(Q[7]), .en(E));  // open: Qn, preset, reset
  Hex_Digit_Display hex_digit_display_3 (.value(Q[7:4]));  // open: dp
  Hex_Digit_Display hex_digit_display_4 (.value(Q[3:0]));  // open: dp
endmodule

module _16_bit_regiser (
  input  E,
  input  [1:0] FunSel,
  input  [15:0] Input,
  output [15:0] Q_Output
);

  wire and_1_out, and_2_out, and_3_out, and_4_out, and_5_out, and_6_out, and_7_out, and_8_out, and_9_out,
       and_10_out, and_11_out, and_12_out, and_13_out, and_14_out, clock_1_out, multiplexer_1_out,
       multiplexer_2_out, multiplexer_3_out, multiplexer_4_out, multiplexer_5_out, multiplexer_6_out,
       multiplexer_7_out, multiplexer_8_out, multiplexer_9_out, multiplexer_10_out, multiplexer_11_out,
       multiplexer_12_out, multiplexer_13_out, multiplexer_14_out, multiplexer_15_out, multiplexer_16_out,
       not_1_out, not_2_out, not_3_out, not_4_out, not_5_out, not_6_out, not_7_out, not_8_out, not_9_out,
       not_10_out, not_11_out, not_12_out, not_13_out, not_14_out, not_15_out, not_16_out, or_1_out,
       or_2_out, or_3_out, or_4_out, or_5_out, or_6_out, or_7_out, or_8_out, or_9_out, or_10_out, or_11_out,
       or_12_out, or_13_out, or_14_out, xor_1_out, xor_2_out, xor_3_out, xor_4_out, xor_5_out, xor_6_out,
       xor_7_out, xor_8_out, xor_9_out, xor_10_out, xor_11_out, xor_12_out, xor_13_out, xor_14_out,
       xor_15_out, xor_16_out, xor_17_out, xor_18_out, xor_19_out, xor_20_out, xor_21_out, xor_22_out,
       xor_23_out, xor_24_out, xor_25_out, xor_26_out, xor_27_out, xor_28_out, xor_29_out, xor_30_out;

  Hex_Digit_Display hex_digit_display_1 (.value(Input[15:12]));  // open: dp
  Hex_Digit_Display hex_digit_display_2 (.value(Input[7:4]));  // open: dp
  Hex_Digit_Display hex_digit_display_3 (.value(Input[11:8]));  // open: dp
  Hex_Digit_Display hex_digit_display_4 (.value(Input[3:0]));  // open: dp
  not not_1 (not_1_out, or_1_out);
  or or_1 (or_1_out, Q_Output[0], Q_Output[1]);
  and and_1 (and_1_out, Q_Output[0], Q_Output[1]);
  or or_2 (or_2_out, or_1_out, Q_Output[2]);
  and and_2 (and_2_out, and_1_out, Q_Output[2]);
  not not_2 (not_2_out, Q_Output[0]);
  not not_3 (not_3_out, or_2_out);
  or or_3 (or_3_out, or_2_out, Q_Output[3]);
  not not_4 (not_4_out, or_3_out);
  and and_3 (and_3_out, and_2_out, Q_Output[3]);
  and and_4 (and_4_out, and_3_out, Q_Output[4]);
  not not_5 (not_5_out, or_4_out);
  or or_4 (or_4_out, or_11_out, Q_Output[7]);
  and and_5 (and_5_out, and_13_out, Q_Output[7]);
  or or_5 (or_5_out, or_4_out, Q_Output[8]);
  and and_6 (and_6_out, and_5_out, Q_Output[8]);
  or or_6 (or_6_out, or_13_out, Q_Output[12]);
  and and_7 (and_7_out, and_14_out, Q_Output[12]);
  not not_6 (not_6_out, Q_Output[0]);
  not not_7 (not_7_out, or_7_out);
  or or_7 (or_7_out, or_3_out, Q_Output[4]);
  or or_8 (or_8_out, or_7_out, Q_Output[5]);
  and and_8 (and_8_out, and_4_out, Q_Output[5]);
  not not_8 (not_8_out, or_5_out);
  or or_9 (or_9_out, or_5_out, Q_Output[9]);
  not not_9 (not_9_out, or_9_out);
  and and_9 (and_9_out, and_6_out, Q_Output[9]);
  and and_10 (and_10_out, and_9_out, Q_Output[10]);
  not not_10 (not_10_out, or_6_out);
  not not_11 (not_11_out, or_10_out);
  or or_10 (or_10_out, or_6_out, Q_Output[13]);
  and and_11 (and_11_out, and_7_out, Q_Output[13]);
  and and_12 (and_12_out, and_11_out, Q_Output[14]);
  not not_12 (not_12_out, or_8_out);
  not not_13 (not_13_out, or_11_out);
  or or_11 (or_11_out, or_8_out, Q_Output[6]);
  and and_13 (and_13_out, and_8_out, Q_Output[6]);
  or or_12 (or_12_out, or_9_out, Q_Output[10]);
  not not_14 (not_14_out, or_12_out);
  or or_13 (or_13_out, or_12_out, Q_Output[11]);
  and and_14 (and_14_out, and_10_out, Q_Output[11]);
  or or_14 (or_14_out, or_10_out, Q_Output[14]);
  not not_15 (not_15_out, or_14_out);
  xor xor_1 (xor_1_out, not_2_out, Q_Output[1]);
  xor xor_2 (xor_2_out, Q_Output[0], Q_Output[1]);
  xor xor_3 (xor_3_out, not_1_out, Q_Output[2]);
  xor xor_4 (xor_4_out, and_1_out, Q_Output[2]);
  xor xor_5 (xor_5_out, not_3_out, Q_Output[3]);
  xor xor_6 (xor_6_out, and_2_out, Q_Output[3]);
  xor xor_7 (xor_7_out, not_4_out, Q_Output[4]);
  xor xor_8 (xor_8_out, and_3_out, Q_Output[4]);
  xor xor_9 (xor_9_out, not_7_out, Q_Output[5]);
  xor xor_10 (xor_10_out, and_4_out, Q_Output[5]);
  xor xor_11 (xor_11_out, not_12_out, Q_Output[6]);
  xor xor_12 (xor_12_out, and_8_out, Q_Output[6]);
  xor xor_13 (xor_13_out, not_13_out, Q_Output[7]);
  xor xor_14 (xor_14_out, and_13_out, Q_Output[7]);
  xor xor_15 (xor_15_out, not_5_out, Q_Output[8]);
  xor xor_16 (xor_16_out, and_5_out, Q_Output[8]);
  xor xor_17 (xor_17_out, not_8_out, Q_Output[9]);
  xor xor_18 (xor_18_out, and_6_out, Q_Output[9]);
  xor xor_19 (xor_19_out, not_9_out, Q_Output[10]);
  xor xor_20 (xor_20_out, and_9_out, Q_Output[10]);
  xor xor_21 (xor_21_out, not_14_out, Q_Output[11]);
  xor xor_22 (xor_22_out, and_10_out, Q_Output[11]);
  not not_16 (not_16_out, or_13_out);
  buf xor_23 (xor_23_out, not_16_out);  // XOR_Gate
  xor xor_24 (xor_24_out, and_14_out, Q_Output[12]);
  xor xor_25 (xor_25_out, not_10_out, Q_Output[13]);
  xor xor_26 (xor_26_out, and_7_out, Q_Output[13]);
  xor xor_27 (xor_27_out, not_11_out, Q_Output[14]);
  xor xor_28 (xor_28_out, and_11_out, Q_Output[14]);
  xor xor_29 (xor_29_out, not_15_out, Q_Output[15]);
  xor xor_30 (xor_30_out, and_12_out, Q_Output[15]);
  Multiplexer #(.select(2), .enable("false")) multiplexer_1 (
    .in0(Input[0]), .in1(not_6_out), .in2(not_6_out), .in3(1'b0), .out(multiplexer_1_out), .sel(FunSel));
  Multiplexer #(.select(2), .enable("false")) multiplexer_2 (
    .in0(Input[1]), .in1(xor_1_out), .in2(xor_2_out), .in3(1'b0), .out(multiplexer_2_out), .sel(FunSel));
  Multiplexer #(.select(2), .enable("false")) multiplexer_3 (
    .in0(Input[2]), .in1(xor_3_out), .in2(xor_4_out), .in3(1'b0), .out(multiplexer_3_out), .sel(FunSel));
  Multiplexer #(.select(2), .enable("false")) multiplexer_4 (
    .in0(Input[3]), .in1(xor_5_out), .in2(xor_6_out), .in3(1'b0), .out(multiplexer_4_out), .sel(FunSel));
  Multiplexer #(.select(2), .enable("false")) multiplexer_5 (
    .in0(Input[4]), .in1(xor_7_out), .in2(xor_8_out), .in3(1'b0), .out(multiplexer_5_out), .sel(FunSel));
  Multiplexer #(.select(2), .enable("false")) multiplexer_6 (
    .in0(Input[5]), .in1(xor_9_out), .in2(xor_10_out), .in3(1'b0), .out(multiplexer_6_out), .sel(FunSel));
  Multiplexer #(.select(2), .enable("false")) multiplexer_7 (
    .in0(Input[6]), .in1(xor_11_out), .in2(xor_12_out), .in3(1'b0), .out(multiplexer_7_out), .sel(FunSel));
  Multiplexer #(.select(2), .enable("false")) multiplexer_8 (
    .in0(Input[7]), .in1(xor_13_out), .in2(xor_14_out), .in3(1'b0), .out(multiplexer_8_out), .sel(FunSel));
  Multiplexer #(.select(2), .enable("false")) multiplexer_9 (
    .in0(Input[8]), .in1(xor_15_out), .in2(xor_16_out), .in3(1'b0), .out(multiplexer_9_out), .sel(FunSel));
  Multiplexer #(.select(2), .enable("false")) multiplexer_10 (
    .in0(Input[9]), .in1(xor_17_out), .in2(xor_18_out), .in3(1'b0), .out(multiplexer_10_out), .sel(FunSel));
  Multiplexer #(.select(2), .enable("false")) multiplexer_11 (
    .in0(Input[10]), .in1(xor_19_out), .in2(xor_20_out), .in3(1'b0), .out(multiplexer_11_out), .sel(FunSel));
  Multiplexer #(.select(2), .enable("false")) multiplexer_12 (
    .in0(Input[11]), .in1(xor_21_out), .in2(xor_22_out), .in3(1'b0), .out(multiplexer_12_out), .sel(FunSel));
  Multiplexer #(.select(2), .enable("false")) multiplexer_13 (
    .in0(Input[12]), .in1(xor_23_out), .in2(xor_24_out), .in3(1'b0), .out(multiplexer_13_out), .sel(FunSel));
  Multiplexer #(.select(2), .enable("false")) multiplexer_14 (
    .in0(Input[13]), .in1(xor_25_out), .in2(xor_26_out), .in3(1'b0), .out(multiplexer_14_out), .sel(FunSel));
  Multiplexer #(.select(2), .enable("false")) multiplexer_15 (
    .in0(Input[14]), .in1(xor_27_out), .in2(xor_28_out), .in3(1'b0), .out(multiplexer_15_out), .sel(FunSel));
  Multiplexer #(.select(2), .enable("false")) multiplexer_16 (
    .in0(Input[15]), .in1(xor_29_out), .in2(xor_30_out), .in3(1'b0), .out(multiplexer_16_out), .sel(FunSel));
  Clock clock_1 (.out(clock_1_out));
  D_Flip_Flop #(.enable("true")) d_ff_1 (
    .clk(clock_1_out), .D(multiplexer_1_out), .Q(Q_Output[0]), .en(E));  // open: Qn, preset, reset
  D_Flip_Flop #(.enable("true")) d_ff_2 (
    .clk(clock_1_out), .D(multiplexer_2_out), .Q(Q_Output[1]), .en(E));  // open: Qn, preset, reset
  D_Flip_Flop #(.enable("true")) d_ff_3 (
    .clk(clock_1_out), .D(multiplexer_3_out), .Q(Q_Output[2]), .en(E));  // open: Qn, preset, reset
  D_Flip_Flop #(.enable("true")) d_ff_4 (
    .clk(clock_1_out), .D(multiplexer_4_out), .Q(Q_Output[3]), .en(E));  // open: Qn, preset, reset
  D_Flip_Flop #(.enable("true")) d_ff_5 (
    .clk(clock_1_out), .D(multiplexer_5_out), .Q(Q_Output[4]), .en(E));  // open: Qn, preset, reset
  D_Flip_Flop #(.enable("true")) d_ff_6 (
    .clk(clock_1_out), .D(multiplexer_6_out), .Q(Q_Output[5]), .en(E));  // open: Qn, preset, reset
  D_Flip_Flop #(.enable("true")) d_ff_7 (
    .clk(clock_1_out), .D(multiplexer_7_out), .Q(Q_Output[6]), .en(E));  // open: Qn, preset, reset
  D_Flip_Flop #(.enable("true")) d_ff_8 (
    .clk(clock_1_out), .D(multiplexer_8_out), .Q(Q_Output[7]), .en(E));  // open: Qn, preset, reset
  D_Flip_Flop #(.enable("true")) d_ff_9 (
    .clk(clock_1_out), .D(multiplexer_9_out), .Q(Q_Output[8]), .en(E));  // open: Qn, preset, reset
  D_Flip_Flop #(.enable("true")) d_ff_10 (
    .clk(clock_1_out), .D(multiplexer_10_out), .Q(Q_Output[9]), .en(E));  // open: Qn, preset, reset
  D_Flip_Flop #(.enable("true")) d_ff_11 (
    .clk(clock_1_out), .D(multiplexer_11_out), .Q(Q_Output[10]), .en(E));  // open: Qn, preset, reset
  D_Flip_Flop #(.enable("true")) d_ff_12 (
    .clk(clock_1_out), .D(multiplexer_12_out), .Q(Q_Output[11]), .en(E));  // open: Qn, preset, reset
  D_Flip_Flop #(.enable("true")) d_ff_13 (
    .clk(clock_1_out), .D(multiplexer_13_out), .Q(Q_Output[12]), .en(E));  // open: Qn, preset, reset
  D_Flip_Flop #(.enable("true")) d_ff_14 (
    .clk(clock_1_out), .D(multiplexer_14_out), .Q(Q_Output[13]), .en(E));  // open: Qn, preset, reset
  D_Flip_Flop #(.enable("true")) d_ff_15 (
    .clk(clock_1_out), .D(multiplexer_15_out), .Q(Q_Output[14]), .en(E));  // open: Qn, preset, reset
  D_Flip_Flop #(.enable("true")) d_ff_16 (
    .clk(clock_1_out), .D(multiplexer_16_out), .Q(Q_Output[15]), .en(E));  // open: Qn, preset, reset
  Hex_Digit_Display hex_digit_display_5 (.value(Q_Output[11:8]));  // open: dp
  Hex_Digit_Display hex_digit_display_6 (.value(Q_Output[15:12]));  // open: dp
  Hex_Digit_Display hex_digit_display_7 (.value(Q_Output[7:4]));  // open: dp
  Hex_Digit_Display hex_digit_display_8 (.value(Q_Output[3:0]));  // open: dp
endmodule

module Register_file (
  input  [7:0] Input,
  input  [1:0] FunSel,
  input  [3:0] RegSel,
  input  [1:0] OutASel,
  input  [1:0] OutBSel,
  output [7:0] Output_A,
  output [7:0] Output_B
);

  wire [7:0] n8_bit_register_1_q, n8_bit_register_2_q, n8_bit_register_3_q, n8_bit_register_4_q;

  Hex_Digit_Display hex_digit_display_1 (.value(Input[7:4]));  // open: dp
  Hex_Digit_Display hex_digit_display_2 (.value(Input[3:0]));  // open: dp
  _8_bit_register u_8_bit_register_1 (.E(RegSel[0]), .Input(Input), .FunSel(FunSel), .Q(n8_bit_register_1_q));
  _8_bit_register u_8_bit_register_2 (.E(RegSel[1]), .Input(Input), .FunSel(FunSel), .Q(n8_bit_register_2_q));
  _8_bit_register u_8_bit_register_3 (.E(RegSel[2]), .Input(Input), .FunSel(FunSel), .Q(n8_bit_register_3_q));
  _8_bit_register u_8_bit_register_4 (.E(RegSel[3]), .Input(Input), .FunSel(FunSel), .Q(n8_bit_register_4_q));
  Hex_Digit_Display hex_digit_display_3 (.value(Output_B[3:0]));  // open: dp
  Hex_Digit_Display hex_digit_display_4 (.value(Output_B[7:4]));  // open: dp
  Multiplexer #(.select(2), .width(8), .enable("false")) multiplexer_1 (
    .in0(n8_bit_register_4_q), .in1(n8_bit_register_3_q), .in2(n8_bit_register_2_q),
    .in3(n8_bit_register_1_q), .out(Output_B), .sel(OutBSel));
  Hex_Digit_Display hex_digit_display_5 (.value(Output_A[7:4]));  // open: dp
  Multiplexer #(.select(2), .width(8), .enable("false")) multiplexer_2 (
    .in0(n8_bit_register_4_q), .in1(n8_bit_register_3_q), .in2(n8_bit_register_2_q),
    .in3(n8_bit_register_1_q), .out(Output_A), .sel(OutASel));
  Hex_Digit_Display hex_digit_display_6 (.value(Output_A[3:0]));  // open: dp

  // Notes on the sheet:
  //   R1
  //   R2
  //   R3
  //   R4
endmodule

module Address_Registers (
  input  [7:0] Input,
  input  [1:0] FunSel,
  input  [2:0] RegSel,
  input  [1:0] OutCSel,
  output [7:0] Output_C
);

  wire [7:0] n8_bit_register_1_q, n8_bit_register_2_q, n8_bit_register_3_q;

  Hex_Digit_Display hex_digit_display_1 (.value(Input[7:4]));  // open: dp
  Hex_Digit_Display hex_digit_display_2 (.value(Input[3:0]));  // open: dp
  _8_bit_register u_8_bit_register_1 (.E(RegSel[0]), .Input(Input), .FunSel(FunSel), .Q(n8_bit_register_1_q));
  _8_bit_register u_8_bit_register_2 (.E(RegSel[1]), .Input(Input), .FunSel(FunSel), .Q(n8_bit_register_2_q));
  _8_bit_register u_8_bit_register_3 (.E(RegSel[2]), .Input(Input), .FunSel(FunSel), .Q(n8_bit_register_3_q));
  Hex_Digit_Display hex_digit_display_3 (.value(Output_C[7:4]));  // open: dp
  Multiplexer #(.select(2), .width(8), .enable("false")) multiplexer_1 (
    .in0(n8_bit_register_3_q), .in1(n8_bit_register_2_q), .in2(n8_bit_register_1_q),
    .in3(n8_bit_register_1_q), .out(Output_C), .sel(OutCSel));
  Hex_Digit_Display hex_digit_display_4 (.value(Output_C[3:0]));  // open: dp

  // Notes on the sheet:
  //   AR
  //   SP
  //   SP
  //   SP
  //   PC
endmodule

module IR_Register (
  input  E,
  input  [1:0] FunSel,
  input  [7:0] in_3,
  input  L_H,
  output [15:0] Q_Output
);

  wire and_1_out, and_2_out, and_3_out, and_4_out, and_5_out, and_6_out, and_7_out, and_8_out, and_9_out,
       and_10_out, and_11_out, and_12_out, and_13_out, and_14_out, clock_1_out, multiplexer_1_out,
       multiplexer_2_out, multiplexer_3_out, multiplexer_4_out, multiplexer_5_out, multiplexer_6_out,
       multiplexer_7_out, multiplexer_8_out, multiplexer_9_out, multiplexer_10_out, multiplexer_11_out,
       multiplexer_12_out, multiplexer_13_out, multiplexer_14_out, multiplexer_15_out, multiplexer_16_out,
       multiplexer_17_out, multiplexer_18_out, multiplexer_19_out, multiplexer_20_out, multiplexer_21_out,
       multiplexer_22_out, multiplexer_23_out, multiplexer_24_out, multiplexer_25_out, multiplexer_26_out,
       multiplexer_27_out, multiplexer_28_out, multiplexer_29_out, multiplexer_30_out, multiplexer_31_out,
       multiplexer_32_out, not_1_out, not_2_out, not_3_out, not_4_out, not_5_out, not_6_out, not_7_out,
       not_8_out, not_9_out, not_10_out, not_11_out, not_12_out, not_13_out, not_14_out, not_15_out,
       not_16_out, not_17_out, not_18_out, or_1_out, or_2_out, or_3_out, or_4_out, or_5_out, or_6_out,
       or_7_out, or_8_out, or_9_out, or_10_out, or_11_out, or_12_out, or_13_out, or_14_out, xor_1_out,
       xor_2_out, xor_3_out, xor_4_out, xor_5_out, xor_6_out, xor_7_out, xor_8_out, xor_9_out, xor_10_out,
       xor_11_out, xor_12_out, xor_13_out, xor_14_out, xor_15_out, xor_16_out, xor_17_out, xor_18_out,
       xor_19_out, xor_20_out, xor_21_out, xor_22_out, xor_23_out, xor_24_out, xor_25_out, xor_26_out,
       xor_27_out, xor_28_out, xor_29_out, xor_30_out;
  wire [7:0] demultiplexer_1_out0, demultiplexer_1_out1;

  Hex_Digit_Display hex_digit_display_1 (.value(in_3[7:4]));  // open: dp
  Hex_Digit_Display hex_digit_display_2 (.value(Q_Output[11:8]));  // open: dp
  Hex_Digit_Display hex_digit_display_3 (.value(Q_Output[15:12]));  // open: dp
  Hex_Digit_Display hex_digit_display_4 (.value(in_3[3:0]));  // open: dp
  Hex_Digit_Display hex_digit_display_5 (.value(Q_Output[7:4]));  // open: dp
  Hex_Digit_Display hex_digit_display_6 (.value(Q_Output[3:0]));  // open: dp
  Demultiplexer #(.width(8), .enable("false")) demultiplexer_1 (
    .out0(demultiplexer_1_out0), .out1(demultiplexer_1_out1), .in(in_3), .sel(not_1_out));
  not not_1 (not_1_out, L_H);
  not not_2 (not_2_out, not_1_out);
  Multiplexer #(.enable("false")) multiplexer_1 (
    .in0(demultiplexer_1_out0[0]), .in1(Q_Output[0]), .out(multiplexer_1_out), .sel(not_1_out));
  Multiplexer #(.enable("false")) multiplexer_2 (
    .in0(demultiplexer_1_out0[1]), .in1(Q_Output[1]), .out(multiplexer_2_out), .sel(not_1_out));
  Multiplexer #(.enable("false")) multiplexer_3 (
    .in0(demultiplexer_1_out0[2]), .in1(Q_Output[2]), .out(multiplexer_3_out), .sel(not_1_out));
  Multiplexer #(.enable("false")) multiplexer_4 (
    .in0(demultiplexer_1_out0[3]), .in1(Q_Output[3]), .out(multiplexer_4_out), .sel(not_1_out));
  Multiplexer #(.enable("false")) multiplexer_5 (
    .in0(demultiplexer_1_out0[4]), .in1(Q_Output[4]), .out(multiplexer_5_out), .sel(not_1_out));
  Multiplexer #(.enable("false")) multiplexer_6 (
    .in0(demultiplexer_1_out0[5]), .in1(Q_Output[5]), .out(multiplexer_6_out), .sel(not_1_out));
  Multiplexer #(.enable("false")) multiplexer_7 (
    .in0(demultiplexer_1_out0[6]), .in1(Q_Output[6]), .out(multiplexer_7_out), .sel(not_1_out));
  Multiplexer #(.enable("false")) multiplexer_8 (
    .in0(demultiplexer_1_out0[7]), .in1(Q_Output[7]), .out(multiplexer_8_out), .sel(not_1_out));
  Multiplexer #(.enable("false")) multiplexer_9 (
    .in0(demultiplexer_1_out1[0]), .in1(Q_Output[8]), .out(multiplexer_9_out), .sel(not_2_out));
  Multiplexer #(.enable("false")) multiplexer_10 (
    .in0(demultiplexer_1_out1[1]), .in1(Q_Output[9]), .out(multiplexer_10_out), .sel(not_2_out));
  Multiplexer #(.enable("false")) multiplexer_11 (
    .in0(demultiplexer_1_out1[2]), .in1(Q_Output[10]), .out(multiplexer_11_out), .sel(not_2_out));
  Multiplexer #(.enable("false")) multiplexer_12 (
    .in0(demultiplexer_1_out1[3]), .in1(Q_Output[11]), .out(multiplexer_12_out), .sel(not_2_out));
  Multiplexer #(.enable("false")) multiplexer_13 (
    .in0(demultiplexer_1_out1[4]), .in1(Q_Output[12]), .out(multiplexer_13_out), .sel(not_2_out));
  Multiplexer #(.enable("false")) multiplexer_14 (
    .in0(demultiplexer_1_out1[5]), .in1(Q_Output[13]), .out(multiplexer_14_out), .sel(not_2_out));
  Multiplexer #(.enable("false")) multiplexer_15 (
    .in0(demultiplexer_1_out1[6]), .in1(Q_Output[14]), .out(multiplexer_15_out), .sel(not_2_out));
  Multiplexer #(.enable("false")) multiplexer_16 (
    .in0(demultiplexer_1_out1[7]), .in1(Q_Output[15]), .out(multiplexer_16_out), .sel(not_2_out));
  or or_1 (or_1_out, Q_Output[0], Q_Output[1]);
  and and_1 (and_1_out, Q_Output[0], Q_Output[1]);
  not not_3 (not_3_out, Q_Output[0]);
  not not_4 (not_4_out, or_1_out);
  not not_5 (not_5_out, or_2_out);
  or or_2 (or_2_out, or_1_out, Q_Output[2]);
  and and_2 (and_2_out, and_1_out, Q_Output[2]);
  or or_3 (or_3_out, or_2_out, Q_Output[3]);
  and and_3 (and_3_out, and_2_out, Q_Output[3]);
  or or_4 (or_4_out, or_11_out, Q_Output[7]);
  and and_4 (and_4_out, and_11_out, Q_Output[7]);
  not not_6 (not_6_out, or_3_out);
  or or_5 (or_5_out, or_3_out, Q_Output[4]);
  and and_5 (and_5_out, and_3_out, Q_Output[4]);
  not not_7 (not_7_out, or_4_out);
  or or_6 (or_6_out, or_4_out, Q_Output[8]);
  not not_8 (not_8_out, or_6_out);
  and and_6 (and_6_out, and_4_out, Q_Output[8]);
  or or_7 (or_7_out, or_6_out, Q_Output[9]);
  and and_7 (and_7_out, and_6_out, Q_Output[9]);
  not not_9 (not_9_out, or_8_out);
  or or_8 (or_8_out, or_14_out, Q_Output[12]);
  and and_8 (and_8_out, and_14_out, Q_Output[12]);
  or or_9 (or_9_out, or_8_out, Q_Output[13]);
  and and_9 (and_9_out, and_8_out, Q_Output[13]);
  not not_10 (not_10_out, Q_Output[0]);
  not not_11 (not_11_out, or_5_out);
  or or_10 (or_10_out, or_5_out, Q_Output[5]);
  not not_12 (not_12_out, or_10_out);
  and and_10 (and_10_out, and_5_out, Q_Output[5]);
  or or_11 (or_11_out, or_10_out, Q_Output[6]);
  and and_11 (and_11_out, and_10_out, Q_Output[6]);
  not not_13 (not_13_out, or_7_out);
  or or_12 (or_12_out, or_7_out, Q_Output[10]);
  and and_12 (and_12_out, and_7_out, Q_Output[10]);
  not not_14 (not_14_out, or_9_out);
  or or_13 (or_13_out, or_9_out, Q_Output[14]);
  and and_13 (and_13_out, and_9_out, Q_Output[14]);
  not not_15 (not_15_out, or_11_out);
  xor xor_1 (xor_1_out, not_8_out, Q_Output[9]);
  xor xor_2 (xor_2_out, and_6_out, Q_Output[9]);
  xor xor_3 (xor_3_out, not_13_out, Q_Output[10]);
  xor xor_4 (xor_4_out, and_7_out, Q_Output[10]);
  not not_16 (not_16_out, or_12_out);
  xor xor_5 (xor_5_out, not_16_out, Q_Output[11]);
  xor xor_6 (xor_6_out, and_12_out, Q_Output[11]);
  not not_17 (not_17_out, or_14_out);
  or or_14 (or_14_out, or_12_out, Q_Output[11]);
  and and_14 (and_14_out, and_12_out, Q_Output[11]);
  not not_18 (not_18_out, or_13_out);
  xor xor_7 (xor_7_out, not_3_out, Q_Output[1]);
  xor xor_8 (xor_8_out, Q_Output[0], Q_Output[1]);
  xor xor_9 (xor_9_out, not_4_out, Q_Output[2]);
  xor xor_10 (xor_10_out, and_1_out, Q_Output[2]);
  xor xor_11 (xor_11_out, not_5_out, Q_Output[3]);
  xor xor_12 (xor_12_out, and_2_out, Q_Output[3]);
  xor xor_13 (xor_13_out, not_6_out, Q_Output[4]);
  xor xor_14 (xor_14_out, and_3_out, Q_Output[4]);
  xor xor_15 (xor_15_out, not_11_out, Q_Output[5]);
  xor xor_16 (xor_16_out, and_5_out, Q_Output[5]);
  xor xor_17 (xor_17_out, not_12_out, Q_Output[6]);
  xor xor_18 (xor_18_out, and_10_out, Q_Output[6]);
  xor xor_19 (xor_19_out, not_15_out, Q_Output[7]);
  xor xor_20 (xor_20_out, and_11_out, Q_Output[7]);
  xor xor_21 (xor_21_out, not_7_out, Q_Output[8]);
  xor xor_22 (xor_22_out, and_4_out, Q_Output[8]);
  buf xor_23 (xor_23_out, not_17_out);  // XOR_Gate
  xor xor_24 (xor_24_out, and_14_out, Q_Output[12]);
  xor xor_25 (xor_25_out, not_9_out, Q_Output[13]);
  xor xor_26 (xor_26_out, and_8_out, Q_Output[13]);
  xor xor_27 (xor_27_out, not_14_out, Q_Output[14]);
  xor xor_28 (xor_28_out, and_9_out, Q_Output[14]);
  xor xor_29 (xor_29_out, not_18_out, Q_Output[15]);
  xor xor_30 (xor_30_out, and_13_out, Q_Output[15]);
  Multiplexer #(.select(2), .enable("false")) multiplexer_17 (
    .in0(multiplexer_1_out), .in1(not_10_out), .in2(not_10_out), .in3(1'b0), .out(multiplexer_17_out),
    .sel(FunSel));
  Multiplexer #(.select(2), .enable("false")) multiplexer_18 (
    .in0(multiplexer_2_out), .in1(xor_7_out), .in2(xor_8_out), .in3(1'b0), .out(multiplexer_18_out),
    .sel(FunSel));
  Multiplexer #(.select(2), .enable("false")) multiplexer_19 (
    .in0(multiplexer_3_out), .in1(xor_9_out), .in2(xor_10_out), .in3(1'b0), .out(multiplexer_19_out),
    .sel(FunSel));
  Multiplexer #(.select(2), .enable("false")) multiplexer_20 (
    .in0(multiplexer_4_out), .in1(xor_11_out), .in2(xor_12_out), .in3(1'b0), .out(multiplexer_20_out),
    .sel(FunSel));
  Multiplexer #(.select(2), .enable("false")) multiplexer_21 (
    .in0(multiplexer_5_out), .in1(xor_13_out), .in2(xor_14_out), .in3(1'b0), .out(multiplexer_21_out),
    .sel(FunSel));
  Multiplexer #(.select(2), .enable("false")) multiplexer_22 (
    .in0(multiplexer_6_out), .in1(xor_15_out), .in2(xor_16_out), .in3(1'b0), .out(multiplexer_22_out),
    .sel(FunSel));
  Multiplexer #(.select(2), .enable("false")) multiplexer_23 (
    .in0(multiplexer_7_out), .in1(xor_17_out), .in2(xor_18_out), .in3(1'b0), .out(multiplexer_23_out),
    .sel(FunSel));
  Multiplexer #(.select(2), .enable("false")) multiplexer_24 (
    .in0(multiplexer_8_out), .in1(xor_19_out), .in2(xor_20_out), .in3(1'b0), .out(multiplexer_24_out),
    .sel(FunSel));
  Multiplexer #(.select(2), .enable("false")) multiplexer_25 (
    .in0(multiplexer_9_out), .in1(xor_21_out), .in2(xor_22_out), .in3(1'b0), .out(multiplexer_25_out),
    .sel(FunSel));
  Multiplexer #(.select(2), .enable("false")) multiplexer_26 (
    .in0(multiplexer_10_out), .in1(xor_1_out), .in2(xor_2_out), .in3(1'b0), .out(multiplexer_26_out),
    .sel(FunSel));
  Multiplexer #(.select(2), .enable("false")) multiplexer_27 (
    .in0(multiplexer_11_out), .in1(xor_3_out), .in2(xor_4_out), .in3(1'b0), .out(multiplexer_27_out),
    .sel(FunSel));
  Multiplexer #(.select(2), .enable("false")) multiplexer_28 (
    .in0(multiplexer_12_out), .in1(xor_5_out), .in2(xor_6_out), .in3(1'b0), .out(multiplexer_28_out),
    .sel(FunSel));
  Multiplexer #(.select(2), .enable("false")) multiplexer_29 (
    .in0(multiplexer_13_out), .in1(xor_23_out), .in2(xor_24_out), .in3(1'b0), .out(multiplexer_29_out),
    .sel(FunSel));
  Multiplexer #(.select(2), .enable("false")) multiplexer_30 (
    .in0(multiplexer_14_out), .in1(xor_25_out), .in2(xor_26_out), .in3(1'b0), .out(multiplexer_30_out),
    .sel(FunSel));
  Multiplexer #(.select(2), .enable("false")) multiplexer_31 (
    .in0(multiplexer_15_out), .in1(xor_27_out), .in2(xor_28_out), .in3(1'b0), .out(multiplexer_31_out),
    .sel(FunSel));
  Multiplexer #(.select(2), .enable("false")) multiplexer_32 (
    .in0(multiplexer_16_out), .in1(xor_29_out), .in2(xor_30_out), .in3(1'b0), .out(multiplexer_32_out),
    .sel(FunSel));
  Clock clock_1 (.out(clock_1_out));
  D_Flip_Flop #(.enable("true")) d_ff_1 (
    .clk(clock_1_out), .D(multiplexer_17_out), .Q(Q_Output[0]), .en(E));  // open: Qn, preset, reset
  D_Flip_Flop #(.enable("true")) d_ff_2 (
    .clk(clock_1_out), .D(multiplexer_18_out), .Q(Q_Output[1]), .en(E));  // open: Qn, preset, reset
  D_Flip_Flop #(.enable("true")) d_ff_3 (
    .clk(clock_1_out), .D(multiplexer_19_out), .Q(Q_Output[2]), .en(E));  // open: Qn, preset, reset
  D_Flip_Flop #(.enable("true")) d_ff_4 (
    .clk(clock_1_out), .D(multiplexer_20_out), .Q(Q_Output[3]), .en(E));  // open: Qn, preset, reset
  D_Flip_Flop #(.enable("true")) d_ff_5 (
    .clk(clock_1_out), .D(multiplexer_21_out), .Q(Q_Output[4]), .en(E));  // open: Qn, preset, reset
  D_Flip_Flop #(.enable("true")) d_ff_6 (
    .clk(clock_1_out), .D(multiplexer_22_out), .Q(Q_Output[5]), .en(E));  // open: Qn, preset, reset
  D_Flip_Flop #(.enable("true")) d_ff_7 (
    .clk(clock_1_out), .D(multiplexer_23_out), .Q(Q_Output[6]), .en(E));  // open: Qn, preset, reset
  D_Flip_Flop #(.enable("true")) d_ff_8 (
    .clk(clock_1_out), .D(multiplexer_24_out), .Q(Q_Output[7]), .en(E));  // open: Qn, preset, reset
  D_Flip_Flop #(.enable("true")) d_ff_9 (
    .clk(clock_1_out), .D(multiplexer_25_out), .Q(Q_Output[8]), .en(E));  // open: Qn, preset, reset
  D_Flip_Flop #(.enable("true")) d_ff_10 (
    .clk(clock_1_out), .D(multiplexer_26_out), .Q(Q_Output[9]), .en(E));  // open: Qn, preset, reset
  D_Flip_Flop #(.enable("true")) d_ff_11 (
    .clk(clock_1_out), .D(multiplexer_27_out), .Q(Q_Output[10]), .en(E));  // open: Qn, preset, reset
  D_Flip_Flop #(.enable("true")) d_ff_12 (
    .clk(clock_1_out), .D(multiplexer_28_out), .Q(Q_Output[11]), .en(E));  // open: Qn, preset, reset
  D_Flip_Flop #(.enable("true")) d_ff_13 (
    .clk(clock_1_out), .D(multiplexer_29_out), .Q(Q_Output[12]), .en(E));  // open: Qn, preset, reset
  D_Flip_Flop #(.enable("true")) d_ff_14 (
    .clk(clock_1_out), .D(multiplexer_30_out), .Q(Q_Output[13]), .en(E));  // open: Qn, preset, reset
  D_Flip_Flop #(.enable("true")) d_ff_15 (
    .clk(clock_1_out), .D(multiplexer_31_out), .Q(Q_Output[14]), .en(E));  // open: Qn, preset, reset
  D_Flip_Flop #(.enable("true")) d_ff_16 (
    .clk(clock_1_out), .D(multiplexer_32_out), .Q(Q_Output[15]), .en(E));  // open: Qn, preset, reset
endmodule
