// Logisim project au.circ as structural Verilog: 1 circuit, main circuit Arithmetic Unit
module Arithmetic_Unit (
  input  Carry_In,
  input  [1:0] FunSel,
  input  [7:0] A,
  input  [7:0] B,
  output [7:0] Output,
  output Carry_Out,
  output Overflow
);

  wire and_1_out, and_2_out, and_3_out, and_4_out, nor_1_out, not_1_out, or_1_out, xor_2_out, xor_3_out;
  wire [7:0] adder_1_out, bit_extender_1_out, xor_1_out;

  and and_1 (and_1_out, FunSel[1], FunSel[0]);
  assign bit_extender_1_out = {{7{1'b0}}, and_1_out};  // Bit_Extender bit_extender_1
  assign xor_1_out = bit_extender_1_out ^ B;  // XOR_Gate xor_1, 8 bits wide
  and and_2 (and_2_out, Carry_In, FunSel[1]);
  or or_1 (or_1_out, and_1_out, and_2_out);
  xor xor_2 (xor_2_out, A[7], B[7]);
  Adder adder_1 (.a(A), .b(xor_1_out), .out(adder_1_out), .cin(or_1_out), .cout(Carry_Out));
  nor nor_1 (nor_1_out, xor_2_out, and_1_out);
  not not_1 (not_1_out, xor_3_out);
  xor xor_3 (xor_3_out, B[7], Output[7]);
  and and_3 (and_3_out, nor_1_out, xor_3_out);
  and and_4 (and_4_out, and_1_out, xor_2_out, not_1_out);
  Multiplexer #(.select(2), .width(8), .enable("false")) multiplexer_1 (
    .in0(A), .in1(adder_1_out), .in2(adder_1_out), .in3(adder_1_out), .out(Output), .sel(FunSel));
  or or_2 (Overflow, and_3_out, and_4_out);

  // Notes on the sheet:
  //   MSB B
  //   Substraction / Addition
  //   MSB A
  //   _________
  //   MSB Output
endmodule
