// Logisim project project2.circ as structural Verilog: 6 circuits, main circuit ALU
module ALU (
  input  [3:0] FunSel,
  input  Cin,
  input  [7:0] A,
  input  [7:0] B,
  output [7:0] OutALU,
  output [3:0] OutFlag_ZCNO_Register
);

  wire and_2_out, arithmetic_unit_1_carry_out, arithmetic_unit_1_overflow, not_3_out, shift_unit_1_carry,
       shift_unit_1_overflow;
  wire [7:0] and_1_out, arithmetic_unit_1_output, not_1_out, not_2_out, or_1_out, shift_unit_1_outsu,
       xor_1_out;

  Hex_Digit_Display hex_digit_display_1 (.value(A[7:4]));  // open: dp
  Hex_Digit_Display hex_digit_display_2 (.value(B[7:4]));  // open: dp
  Hex_Digit_Display hex_digit_display_3 (.value(OutALU[7:4]));  // open: dp
  Hex_Digit_Display hex_digit_display_4 (.value(A[3:0]));  // open: dp
  Hex_Digit_Display hex_digit_display_5 (.value(B[3:0]));  // open: dp
  Hex_Digit_Display hex_digit_display_6 (.value(OutALU[3:0]));  // open: dp
  assign and_1_out = A & B;  // AND_Gate and_1, 8 bits wide
  assign or_1_out = A | B;  // OR_Gate or_1, 8 bits wide
  assign not_1_out = ~A;  // NOT_Gate not_1, 8 bits wide
  assign xor_1_out = A ^ B;  // XOR_Gate xor_1, 8 bits wide
  assign not_2_out = ~B;  // NOT_Gate not_2, 8 bits wide
  Arithmetic_Unit arithmetic_unit_1 (
    .Carry_In(Cin), .FunSel(FunSel[1:0]), .A(A), .Output(arithmetic_unit_1_output),
    .Carry_Out(arithmetic_unit_1_carry_out), .B(B), .Overflow(arithmetic_unit_1_overflow));
  not not_3 (not_3_out, FunSel[3]);
  and and_2 (and_2_out, not_3_out, FunSel[2]);
  Shift_Unit shift_unit_1 (
    .A(A), .FunSel(FunSel), .OutSU(shift_unit_1_outsu), .Overflow(shift_unit_1_overflow),
    .Carry(shift_unit_1_carry));
  Multiplexer #(.enable("false")) multiplexer_1 (
    .in0(shift_unit_1_carry), .in1(arithmetic_unit_1_carry_out), .out(OutFlag_ZCNO_Register[2]),
    .sel(and_2_out));
  Multiplexer #(.enable("false")) multiplexer_2 (
    .in0(shift_unit_1_overflow), .in1(arithmetic_unit_1_overflow), .out(OutFlag_ZCNO_Register[0]),
    .sel(and_2_out));
  Multiplexer #(.select(4), .width(8), .enable("false")) multiplexer_3 (
    .in0(and_1_out), .in1(or_1_out), .in2(not_1_out), .in3(xor_1_out), .in4(arithmetic_unit_1_output),
    .in5(arithmetic_unit_1_output), .in6(arithmetic_unit_1_output), .in7(arithmetic_unit_1_output), .in8(B),
    .in9(not_2_out), .in10(shift_unit_1_outsu), .in11(shift_unit_1_outsu), .in12(shift_unit_1_outsu),
    .in13(shift_unit_1_outsu), .in14(shift_unit_1_outsu), .in15(shift_unit_1_outsu), .out(OutALU),
    .sel(FunSel));
  ZeroChecker zerochecker_1 (.Input(OutALU), .ZeroFlag(OutFlag_ZCNO_Register[3]));

  assign OutFlag_ZCNO_Register[1] = OutALU[7];

  // Notes on the sheet:
  //   A
  //   B
  //   OutALU
  //   Arithmethic Operations
  //   A AND B
  //   A OR B
  //   NOT A
  //   A XOR B
  //   B
  //   NOT B
  //   FunSel
  //   Carry From Arithmetic Unit
  //   Overflow From Arithmetic Unit
  //   Shift Operations
  //   Carry From Shifting Unit
  //   Overflow From Shifting Unit
  //   Carry Selector
  //   Overflow Selector
  //   Negative Checker
endmodule

module ZeroChecker (
  input  [7:0] Input,
  output ZeroFlag
);

  wire or_1_out;

  or or_1 (or_1_out, Input[7], Input[6], Input[5], Input[4], Input[3], Input[2], Input[1], Input[0]);
  not not_1 (ZeroFlag, or_1_out);
endmodule

module Arithmetic_Unit (
  input  Carry_In,
  input  [1:0] FunSel,
  input  [7:0] A,
  input  [7:0] B,
  output [7:0] Output,
  output Carry_Out,
  output Overflow
);

  wire and_1_out, and_2_out, and_3_out, and_4_out, nor_1_out, not_1_out, or_1_out, xor_2_out, xor_3_out;
  wire [7:0] adder_1_out, bit_extender_1_out, xor_1_out;

  and and_1 (and_1_out, FunSel[1], FunSel[0]);
  assign bit_extender_1_out = {{7{1'b0}}, and_1_out};  // Bit_Extender bit_extender_1
  assign xor_1_out = bit_extender_1_out ^ B;  // XOR_Gate xor_1, 8 bits wide
  xor xor_2 (xor_2_out, A[7], B[7]);
  and and_2 (and_2_out, Carry_In, FunSel[1]);
  or or_1 (or_1_out, and_1_out, and_2_out);
  Adder adder_1 (.a(A), .b(xor_1_out), .out(adder_1_out), .cin(or_1_out), .cout(Carry_Out));
  nor nor_1 (nor_1_out, xor_2_out, and_1_out);
  xor xor_3 (xor_3_out, B[7], Output[7]);
  and and_3 (and_3_out, nor_1_out, xor_3_out);
  and and_4 (and_4_out, and_1_out, xor_2_out, not_1_out);
  not not_1 (not_1_out, xor_3_out);
  Multiplexer #(.select(2), .width(8), .enable("false")) multiplexer_1 (
    .in0(A), .in1(adder_1_out), .in2(adder_1_out), .in3(adder_1_out), .out(Output), .sel(FunSel));
  or or_2 (Overflow, and_3_out, and_4_out);

  // Notes on the sheet:
  //   MSB B
  //   Substraction / Addition
  //   MSB A
  //   _________
  //   MSB Output
endmodule

module Shift_Unit (
  input  [7:0] A,
  input  [3:0] FunSel,
  output [7:0] OutSU,
  output Overflow,
  output Carry
);

  wire xor_1_out, xor_2_out, xor_3_out;

  xor xor_1 (xor_1_out, A[7], A[6]);
  xor xor_2 (xor_2_out, A[7], A[6]);
  xor xor_3 (xor_3_out, A[7], A[0]);
  Multiplexer #(.select(3), .width(8), .enable("false")) multiplexer_1 (
    .in0({8{1'b0}}), .in1({8{1'b0}}), .in2({A[6:0], 1'b0}), .in3({1'b0, A[7:1]}), .in4({A[6:0], 1'b0}),
    .in5({{2{A[7]}}, A[6:1]}), .in6({A[6:0], A[7]}), .in7({A[0], A[7:1]}), .out(OutSU), .sel(FunSel[2:0]));
  Multiplexer #(.select(3), .enable("false")) multiplexer_2 (
    .in0(1'b0), .in1(1'b0), .in2(1'b0), .in3(1'b0), .in4(xor_1_out), .in5(1'b0), .in6(xor_2_out),
    .in7(xor_3_out), .out(Overflow), .sel(FunSel[2:0]));
  Multiplexer #(.select(3), .enable("false")) multiplexer_3 (
    .in0(1'b0), .in1(1'b0), .in2(A[7]), .in3(A[0]), .in4(1'b0), .in5(1'b0), .in6(A[7]), .in7(A[0]),
    .out(Carry), .sel(FunSel[2:0]));

  // Notes on the sheet:
  //   Arithmetic Shift Left
  //   Arithmetic Shift Right
  //   Circular Shift Left
  //   Circular Shift Right
  //   Logical Shift Left
  //   Logical Shift Right
  //   OutSU
  //   Overflow Selector
  //   Carry Selector
endmodule

module ALU_System (
  input  [1:0] OutASel,
  input  [3:0] FunSel,
  input  [1:0] OutBSel,
  input  [1:0] FunSel_2,
  input  [3:0] RegSel,
  input  [1:0] MuxASel,
  input  in_7,
  input  in_8,
  input  in_9,
  input  in_10,
  input  [1:0] MuxBSel,
  input  [1:0] OutCSel,
  input  [1:0] FunSel_3,
  input  [2:0] RegSel_2,
  input  L_H,
  input  Enable,
  input  [1:0] FunSel_4,
  output [7:0] IR_8_15
);

  wire clock_1_out, flag_register_1_c, flag_register_1_n, flag_register_1_o, flag_register_1_z;
  wire [3:0] alu_1_outflag_zcno_register;
  wire [7:0] address_registers_1_output_c, alu_1_outalu, ir_register_1_ir_0_7, multiplexer_1_out,
       multiplexer_2_out, ram_1_data, register_file_1_output_a, register_file_1_output_b;

  Multiplexer #(.select(2), .width(8), .enable("false")) multiplexer_1 (
    .in0(ir_register_1_ir_0_7), .in1(ram_1_data), .in2(address_registers_1_output_c), .in3(alu_1_outalu),
    .out(multiplexer_1_out), .sel(MuxASel));
  Register_file register_file_1 (
    .Input(multiplexer_1_out), .FunSel(FunSel_2), .RegSel(RegSel), .OutASel(OutASel), .OutBSel(OutBSel),
    .Output_A(register_file_1_output_a), .Output_B(register_file_1_output_b));
  IR_Register ir_register_1 (
    .E(Enable), .FunSel(FunSel_4), .in_3(ram_1_data), .IR_0_7(ir_register_1_ir_0_7), .IR_8_15(IR_8_15),
    .L_H(L_H));
  LED led_1 (.in(flag_register_1_z));
  Multiplexer #(.select(2), .width(8), .enable("false")) multiplexer_2 (
    .in1(ir_register_1_ir_0_7), .in2(ram_1_data), .in3(alu_1_outalu), .out(multiplexer_2_out), .sel(MuxBSel));  // open: in0
  ALU alu_1 (
    .FunSel(FunSel), .OutALU(alu_1_outalu), .OutFlag_ZCNO_Register(alu_1_outflag_zcno_register),
    .Cin(flag_register_1_c), .A(register_file_1_output_a), .B(register_file_1_output_b));
  Flag_Register flag_register_1 (
    .InFlag(alu_1_outflag_zcno_register), .Z(flag_register_1_z), .C(flag_register_1_c),
    .N(flag_register_1_n), .O(flag_register_1_o));
  LED led_2 (.in(flag_register_1_o));
  LED led_3 (.in(flag_register_1_c));
  LED led_4 (.in(flag_register_1_n));
  Address_Registers address_registers_1 (
    .Input(multiplexer_2_out), .FunSel(FunSel_3), .RegSel(RegSel_2), .OutCSel(OutCSel),
    .Output_C(address_registers_1_output_c));
  Clock clock_1 (.out(clock_1_out));
  RAM #(.bus("separate")) ram_1 (
    .addr(address_registers_1_output_c), .din(alu_1_outalu), .data(ram_1_data), .str(in_7), .sel(in_8),
    .clk(clock_1_out), .ld(in_9), .clr(in_10));

  // Notes on the sheet:
  //   IR(0-7)
  //   OutA
  //   OutB
  //   Address
endmodule

module Flag_Register (
  input  [3:0] InFlag,
  output O,
  output N,
  output C,
  output Z
);

  wire clock_1_out;

  Clock clock_1 (.out(clock_1_out));
  D_Flip_Flop d_ff_1 (.clk(clock_1_out), .D(InFlag[0]), .Q(O));  // open: Qn, preset, reset
  D_Flip_Flop d_ff_2 (.clk(clock_1_out), .D(InFlag[1]), .Q(N));  // open: Qn, preset, reset
  D_Flip_Flop d_ff_3 (.clk(clock_1_out), .D(InFlag[2]), .Q(C));  // open: Qn, preset, reset
  D_Flip_Flop d_ff_4 (.clk(clock_1_out), .D(InFlag[3]), .Q(Z));  // open: Qn, preset, reset

  // Notes on the sheet:
  //   LSB
  //   MSB
endmodule
