// Logisim project project3.circ as structural Verilog: 4 circuits, main circuit Control Unit
module Control_Unit (
);

  wire ADDRMODE, and_1_out, and_2_out, and_3_out, and_4_out, and_5_out, and_6_out, and_7_out, and_8_out,
       and_9_out, and_10_out, and_11_out, and_12_out, and_13_out, and_14_out, and_15_out, and_16_out,
       and_17_out, and_18_out, and_19_out, and_20_out, and_21_out, and_22_out, and_23_out, and_24_out,
       and_25_out, and_26_out, and_27_out, and_28_out, and_29_out, and_30_out, and_31_out, and_32_out,
       and_33_out, and_34_out, and_35_out, and_36_out, and_37_out, and_38_out, and_39_out, and_40_out,
       and_41_out, and_42_out, and_43_out, and_44_out, and_45_out, and_46_out, and_47_out, and_48_out,
       and_49_out, and_50_out, and_51_out, and_52_out, and_53_out, and_54_out, and_55_out, and_56_out,
       and_57_out, and_58_out, and_59_out, and_60_out, and_61_out, and_62_out, and_63_out, and_64_out,
       and_65_out, and_66_out, and_67_out, and_68_out, and_70_out, and_72_out, and_73_out, and_74_out,
       and_75_out, and_76_out, and_77_out, and_78_out, and_79_out, and_80_out, and_81_out, and_82_out,
       and_83_out, and_84_out, and_85_out, and_86_out, and_87_out, and_88_out, and_89_out, and_90_out,
       and_91_out, and_92_out, and_93_out, and_94_out, and_95_out, and_96_out, and_97_out, and_98_out,
       and_99_out, and_100_out, and_101_out, and_102_out, and_103_out, and_104_out, and_105_out, and_106_out,
       and_107_out, and_108_out, and_109_out, and_110_out, and_111_out, and_112_out, and_113_out,
       and_114_out, and_115_out, and_116_out, and_117_out, and_118_out, and_119_out, and_120_out,
       and_121_out, and_122_out, and_123_out, and_124_out, and_125_out, and_126_out, and_127_out,
       and_128_out, and_129_out, and_130_out, and_131_out, and_132_out, and_133_out, and_134_out,
       and_135_out, and_136_out, and_137_out, and_138_out, and_139_out, and_140_out, and_141_out,
       and_142_out, and_143_out, and_144_out, and_145_out, and_146_out, and_147_out, and_148_out,
       and_149_out, and_150_out, and_151_out, and_152_out, and_153_out, and_154_out, and_155_out,
       and_156_out, and_157_out, and_158_out, and_159_out, and_160_out, and_161_out, and_162_out,
       and_163_out, and_164_out, and_165_out, and_166_out, and_167_out, and_168_out, and_169_out,
       and_170_out, and_171_out, and_172_out, and_173_out, and_174_out, and_175_out, and_176_out,
       and_178_out, and_180_out, and_181_out, and_182_out, and_183_out, and_184_out, and_185_out,
       and_186_out, and_187_out, and_188_out, and_189_out, and_190_out, and_191_out, and_192_out,
       and_193_out, and_194_out, and_195_out, and_196_out, and_197_out, and_198_out, and_199_out,
       and_200_out, and_201_out, and_202_out, and_203_out, and_204_out, and_205_out, and_206_out,
       and_207_out, and_208_out, and_209_out, and_210_out, and_211_out, and_212_out, and_213_out,
       and_214_out, and_215_out, and_216_out, and_217_out, and_218_out, and_219_out, and_220_out,
       and_221_out, and_222_out, and_223_out, and_224_out, and_225_out, and_226_out, and_227_out,
       and_228_out, and_229_out, and_230_out, and_231_out, and_232_out, and_233_out, and_234_out,
       and_235_out, and_236_out, and_237_out, and_238_out, and_239_out, and_240_out, and_241_out,
       and_242_out, and_243_out, and_244_out, and_245_out, and_246_out, and_247_out, and_248_out,
       and_249_out, and_250_out, and_251_out, and_252_out, and_253_out, and_254_out, and_255_out,
       and_256_out, and_257_out, and_258_out, and_259_out, and_260_out, and_261_out, and_262_out,
       and_263_out, and_264_out, and_265_out, and_266_out, and_267_out, and_268_out, and_269_out,
       and_270_out, and_271_out, and_272_out, and_273_out, and_274_out, and_275_out, and_276_out,
       and_277_out, and_278_out, and_279_out, and_280_out, and_281_out, and_282_out, and_283_out,
       and_284_out, and_285_out, and_286_out, and_287_out, and_288_out, and_289_out, and_290_out,
       and_291_out, and_292_out, and_293_out, and_294_out, and_295_out, and_296_out, and_297_out,
       and_298_out, and_299_out, ARFARF, D00, D0A, D0B, D0C, D0D, D0E, D01, D02, D03, D04, D05, D06, D07,
       D08, D09, decoder_1_out6, decoder_1_out7, decoder_2_out6, decoder_2_out7, decoder_3_out6,
       decoder_3_out7, decoder_4_out6, decoder_4_out7, decoder_6_out6, decoder_6_out7, decoder_7_out6,
       decoder_7_out7, decoder_8_out6, decoder_8_out7, decoder_9_out6, decoder_9_out7, decoder_10_out6,
       decoder_10_out7, decoder_11_out6, decoder_11_out7, decoder_12_out6, decoder_12_out7, decoder_13_out6,
       decoder_13_out7, decoder_14_out6, decoder_14_out7, decoder_15_out6, decoder_15_out7, decoder_16_out6,
       decoder_16_out7, decoder_17_out6, decoder_17_out7, decoder_18_out6, decoder_18_out7, decoder_20_out6,
       decoder_20_out7, decoder_21_out6, decoder_21_out7, decoder_22_out6, decoder_22_out7, decoder_24_out6,
       decoder_24_out7, decoder_25_out6, decoder_25_out7, decoder_26_out6, decoder_26_out7, decoder_27_out6,
       decoder_27_out7, decoder_28_out6, decoder_28_out7, decoder_29_out6, decoder_29_out7, decoder_30_out6,
       decoder_30_out7, decoder_31_out6, decoder_31_out7, decoder_32_out6, decoder_32_out7, decoder_33_out6,
       decoder_33_out7, decoder_34_out6, decoder_34_out7, decoder_35_out6, decoder_35_out7, decoder_36_out6,
       decoder_36_out7, decoder_37_out6, decoder_37_out7, decoder_38_out6, decoder_38_out7, decoder_39_out6,
       decoder_39_out7, IR_Enable, IR_LH, isequal_1_out_3, isequal_2_out_3, isequal_3_out_3, isequal_4_out_3,
       isequal_5_out_3, isequal_6_out_3, isequal_7_out_3, isequal_8_out_3, isequal_9_out_3, isequal_10_out_3,
       isequal_11_out_3, isequal_12_out_3, isequal_13_out_3, isequal_14_out_3, isequal_15_out_3,
       isequal_16_out_3, isequal_17_out_3, isequal_18_out_3, isequal_19_out_3, isequal_20_out_3,
       isequal_21_out_3, isequal_22_out_3, isequal_23_out_3, isequal_24_out_3, isequal_25_out_3,
       isequal_26_out_3, Mem_clr, Mem_load, Mem_sel, Mem_str, nand_1_out, nand_2_out, nand_3_out, nand_4_out,
       nand_5_out, nand_6_out, nand_7_out, nand_8_out, nor_1_out, nor_2_out, nor_3_out, nor_4_out, nor_5_out,
       nor_6_out, nor_7_out, nor_8_out, nor_9_out, nor_10_out, nor_11_out, nor_12_out, not_1_out, not_2_out,
       not_3_out, not_4_out, not_5_out, not_6_out, not_7_out, not_8_out, not_9_out, not_10_out, not_11_out,
       not_12_out, not_13_out, not_14_out, not_15_out, not_16_out, not_17_out, not_18_out, not_19_out,
       not_20_out, not_21_out, not_22_out, not_23_out, not_24_out, not_25_out, not_26_out, not_27_out,
       not_28_out, not_29_out, not_30_out, not_31_out, not_32_out, not_33_out, not_34_out, not_35_out,
       not_36_out, not_37_out, not_38_out, not_39_out, not_40_out, not_41_out, not_42_out, not_43_out,
       not_44_out, not_45_out, not_46_out, not_47_out, not_48_out, not_49_out, not_50_out, not_51_out,
       not_52_out, not_53_out, not_54_out, not_55_out, not_56_out, not_57_out, not_58_out, not_59_out,
       not_60_out, not_61_out, not_62_out, not_63_out, not_64_out, not_65_out, not_66_out, not_67_out,
       not_68_out, not_69_out, not_70_out, not_71_out, not_72_out, not_73_out, not_74_out, not_75_out,
       not_76_out, not_77_out, not_78_out, not_79_out, not_80_out, not_81_out, or_1_out, or_2_out, or_6_out,
       or_7_out, or_9_out, or_10_out, or_13_out, or_14_out, or_16_out, or_17_out, or_19_out, or_20_out,
       or_26_out, or_27_out, or_31_out, or_32_out, or_33_out, or_34_out, or_36_out, or_37_out, or_38_out,
       or_40_out, or_43_out, or_44_out, SC_Reset, T0, T1, T2, T3, T4, T5, T6, T7, xor_1_out, xor_2_out,
       xor_3_out, xor_4_out, xor_5_out, xor_6_out, xor_7_out, xor_8_out, Z;
  wire [1:0] AR_FunSel, AR_OutCSel, IR_FunSel, MuxASel, MuxBSel, RF_FunSel, RF_OutASel, RF_OutBSel;
  wire [2:0] AR_RegSel, controlled_buffer_118_out, controlled_buffer_125_out, controlled_buffer_276_out,
       controlled_buffer_284_out, or_3_out, or_4_out, or_5_out, or_8_out, or_11_out, or_12_out, or_15_out,
       or_18_out, or_21_out, or_22_out, or_23_out, or_24_out, or_25_out, or_28_out, or_29_out, or_30_out,
       or_35_out, or_39_out, or_41_out, or_42_out, or_45_out, or_46_out, or_47_out, or_48_out, or_49_out,
       or_50_out, or_51_out, or_52_out, or_53_out, or_54_out, or_55_out, or_56_out, or_57_out, or_58_out,
       or_59_out, or_60_out;
  wire [2:1] DESTREG;
  wire [3:0] ALU_FunSel, decoder_1_out3, decoder_2_out3, decoder_3_out3, decoder_4_out3, decoder_7_out3,
       decoder_8_out3, decoder_9_out3, decoder_10_out3, decoder_11_out3, decoder_12_out3, decoder_13_out3,
       decoder_14_out3, decoder_16_out3, decoder_17_out3, decoder_18_out3, decoder_19_out3, decoder_20_out3,
       decoder_21_out3, decoder_22_out3, decoder_23_out3, decoder_25_out3, decoder_26_out3, decoder_27_out3,
       decoder_28_out3, decoder_29_out3, decoder_30_out3, decoder_31_out3, decoder_32_out3, decoder_35_out3,
       decoder_36_out3, decoder_37_out3, decoder_38_out3, RF_RegSel;
  wire [7:0] ADDRESS;
  wire [15:11] Instruction;

  Sequence_Counter sequence_counter_1 (
    .Reset(SC_Reset), .T0(T0), .T1(T1), .T2(T2), .T3(T3), .T4(T4), .T5(T5), .T6(T6), .T7(T7));
  and and_1 (and_1_out, D02, T2);
  and and_2 (and_2_out, D02, T3);
  and and_3 (and_3_out, D02, T4);
  nand nand_1 (nand_1_out, ADDRESS[2], ADDRESS[3]);
  and and_4 (and_4_out, ADDRESS[7], and_5_out);
  and and_5 (and_5_out, ADDRESS[2], ADDRESS[3]);
  and and_6 (and_6_out, and_4_out, and_13_out);
  nand nand_2 (nand_2_out, ADDRESS[2], ADDRESS[3]);
  and and_7 (and_7_out, ADDRESS[7], and_8_out);
  and and_8 (and_8_out, ADDRESS[2], ADDRESS[3]);
  and and_9 (and_9_out, and_7_out, and_16_out);
  isEqual isequal_1 (.in_1(ADDRESS[7:5]), .in_2({DESTREG, ADDRMODE}), .out_3(isequal_1_out_3));
  not not_1 (not_1_out, isequal_1_out_3);
  and and_10 (and_10_out, and_1_out, not_1_out, and_19_out);
  assign RF_OutASel = and_10_out ? ADDRESS[6:5] : 2'bz;  // Controlled_Buffer controlled_buffer_1
  assign ALU_FunSel = and_10_out ? 4'b0100 : 4'bz;  // Controlled_Buffer controlled_buffer_2
  assign MuxASel = and_10_out ? 2'b11 : 2'bz;  // Controlled_Buffer controlled_buffer_3
  assign RF_FunSel = and_10_out ? 2'b00 : 2'bz;  // Controlled_Buffer controlled_buffer_4
  Decoder #(.select(3), .disabled(0)) decoder_1 (
    .out0(decoder_1_out3[3]), .out1(decoder_1_out3[2]), .out2(decoder_1_out3[1]), .out3(decoder_1_out3[0]),
    .out4(or_3_out[2]), .out5(or_3_out[1]), .out6(decoder_1_out6), .out7(decoder_1_out7),
    .sel({DESTREG, ADDRMODE}), .en(and_10_out));
  assign RF_RegSel = and_10_out ? decoder_1_out3 : 4'bz;  // Controlled_Buffer controlled_buffer_5
  assign AR_RegSel = and_10_out ? or_3_out : 3'bz;  // Controlled_Buffer controlled_buffer_6
  isEqual isequal_2 (.in_1(ADDRESS[7:5]), .in_2({DESTREG, ADDRMODE}), .out_3(isequal_2_out_3));
  not not_2 (not_2_out, isequal_2_out_3);
  and and_11 (and_11_out, and_2_out, not_2_out, and_20_out);
  Decoder #(.select(3), .disabled(0)) decoder_2 (
    .out0(decoder_2_out3[3]), .out1(decoder_2_out3[2]), .out2(decoder_2_out3[1]), .out3(decoder_2_out3[0]),
    .out4(or_4_out[2]), .out5(or_4_out[1]), .out6(decoder_2_out6), .out7(decoder_2_out7),
    .sel({DESTREG, ADDRMODE}), .en(and_11_out));
  assign RF_RegSel = and_11_out ? decoder_2_out3 : 4'bz;  // Controlled_Buffer controlled_buffer_7
  assign AR_RegSel = and_11_out ? or_4_out : 3'bz;  // Controlled_Buffer controlled_buffer_8
  assign RF_FunSel = and_11_out ? 2'b01 : 2'bz;  // Controlled_Buffer controlled_buffer_9
  assign AR_FunSel = and_11_out ? 2'b01 : 2'bz;  // Controlled_Buffer controlled_buffer_10
  not not_3 (not_3_out, DESTREG[2]);
  isEqual isequal_3 (.in_1(ADDRESS[7:5]), .in_2({DESTREG, ADDRMODE}), .out_3(isequal_3_out_3));
  not not_4 (not_4_out, isequal_3_out_3);
  and and_12 (and_12_out, and_3_out, not_4_out, and_21_out);
  assign SC_Reset = and_12_out ? 1'b1 : 1'bz;  // Controlled_Buffer controlled_buffer_11
  Organization organization_1 (
    .OutASel(RF_OutASel), .FunSel(ALU_FunSel), .OutBSel(RF_OutBSel), .FunSel_2(RF_FunSel),
    .RegSel(RF_RegSel), .MuxASel(MuxASel), .MuxBSel(MuxBSel), .OutCSel(AR_OutCSel), .FunSel_3(AR_FunSel),
    .RegSel_2(AR_RegSel), .L_H(IR_LH), .Enable(IR_Enable), .FunSel_4(IR_FunSel), .in_7(Mem_str),
    .in_8(Mem_sel), .in_9(Mem_load), .in_10(Mem_clr),
    .Instruction({Instruction, DESTREG, ADDRMODE, ADDRESS}), .Z(Z));
  and and_13 (and_13_out, D00, T2);
  and and_14 (and_14_out, ADDRESS[7], nand_1_out);
  and and_15 (and_15_out, and_14_out, and_13_out);
  assign RF_RegSel = and_6_out ? 4'b0010 : 4'bz;  // Controlled_Buffer controlled_buffer_12
  or or_1 (or_1_out, and_6_out, and_15_out);
  and and_16 (and_16_out, D01, T2);
  and and_17 (and_17_out, ADDRESS[7], nand_2_out);
  and and_18 (and_18_out, and_17_out, and_16_out);
  assign RF_RegSel = and_9_out ? 4'b0010 : 4'bz;  // Controlled_Buffer controlled_buffer_13
  or or_2 (or_2_out, and_9_out, and_18_out);
  assign Mem_str = D01 ? 1'b0 : 1'bz;  // Controlled_Buffer controlled_buffer_14
  assign Mem_load = D01 ? 1'b1 : 1'bz;  // Controlled_Buffer controlled_buffer_15
  assign Mem_clr = D01 ? 1'b0 : 1'bz;  // Controlled_Buffer controlled_buffer_16
  assign Mem_sel = D01 ? 1'b0 : 1'bz;  // Controlled_Buffer controlled_buffer_17
  not not_5 (not_5_out, DESTREG[2]);
  not not_6 (not_6_out, ADDRESS[7]);
  and and_19 (and_19_out, not_5_out, not_6_out);
  or or_3 (or_3_out[0], decoder_1_out6, decoder_1_out7);
  not not_7 (not_7_out, DESTREG[2]);
  not not_8 (not_8_out, ADDRESS[7]);
  and and_20 (and_20_out, not_7_out, not_8_out);
  or or_4 (or_4_out[0], decoder_2_out6, decoder_2_out7);
  not not_9 (not_9_out, ADDRESS[7]);
  and and_21 (and_21_out, not_3_out, not_9_out);
  assign RF_FunSel = or_1_out ? 2'b00 : 2'bz;  // Controlled_Buffer controlled_buffer_18
  assign AR_OutCSel = or_1_out ? ADDRESS[6:5] : 2'bz;  // Controlled_Buffer controlled_buffer_19
  assign MuxASel = or_1_out ? 2'b10 : 2'bz;  // Controlled_Buffer controlled_buffer_20
  assign Mem_str = D00 ? 1'b0 : 1'bz;  // Controlled_Buffer controlled_buffer_21
  assign Mem_load = D00 ? 1'b1 : 1'bz;  // Controlled_Buffer controlled_buffer_22
  assign Mem_clr = D00 ? 1'b0 : 1'bz;  // Controlled_Buffer controlled_buffer_23
  assign Mem_sel = D00 ? 1'b0 : 1'bz;  // Controlled_Buffer controlled_buffer_24
  assign RF_FunSel = or_2_out ? 2'b00 : 2'bz;  // Controlled_Buffer controlled_buffer_25
  assign AR_OutCSel = or_2_out ? ADDRESS[6:5] : 2'bz;  // Controlled_Buffer controlled_buffer_26
  assign MuxASel = or_2_out ? 2'b10 : 2'bz;  // Controlled_Buffer controlled_buffer_27
  assign RF_RegSel = and_15_out ? 4'b0001 : 4'bz;  // Controlled_Buffer controlled_buffer_28
  assign RF_RegSel = and_18_out ? 4'b0001 : 4'bz;  // Controlled_Buffer controlled_buffer_29
  isEqual isequal_4 (.in_1(ADDRESS[7:5]), .in_2({DESTREG, ADDRMODE}), .out_3(isequal_4_out_3));
  and and_22 (and_22_out, D02, T2);
  not not_10 (not_10_out, isequal_4_out_3);
  and and_23 (and_23_out, and_22_out, not_10_out, xor_1_out);
  assign RF_RegSel = and_23_out ? decoder_4_out3 : 4'bz;  // Controlled_Buffer controlled_buffer_30
  assign AR_RegSel = and_23_out ? or_8_out : 3'bz;  // Controlled_Buffer controlled_buffer_31
  isEqual isequal_5 (.in_1(ADDRESS[7:5]), .in_2({DESTREG, ADDRMODE}), .out_3(isequal_5_out_3));
  and and_24 (and_24_out, D02, T3);
  not not_11 (not_11_out, isequal_5_out_3);
  and and_25 (and_25_out, and_24_out, not_11_out, xor_2_out);
  Decoder #(.select(3), .disabled(0)) decoder_3 (
    .out0(decoder_3_out3[3]), .out1(decoder_3_out3[2]), .out2(decoder_3_out3[1]), .out3(decoder_3_out3[0]),
    .out4(or_5_out[2]), .out5(or_5_out[1]), .out6(decoder_3_out6), .out7(decoder_3_out7),
    .sel({DESTREG, ADDRMODE}), .en(and_25_out));
  assign RF_RegSel = and_25_out ? decoder_3_out3 : 4'bz;  // Controlled_Buffer controlled_buffer_32
  assign AR_RegSel = and_25_out ? or_5_out : 3'bz;  // Controlled_Buffer controlled_buffer_33
  assign RF_FunSel = and_25_out ? 2'b01 : 2'bz;  // Controlled_Buffer controlled_buffer_34
  assign AR_FunSel = and_25_out ? 2'b01 : 2'bz;  // Controlled_Buffer controlled_buffer_35
  isEqual isequal_6 (.in_1(ADDRESS[7:5]), .in_2({DESTREG, ADDRMODE}), .out_3(isequal_6_out_3));
  and and_26 (and_26_out, D02, T4);
  not not_12 (not_12_out, isequal_6_out_3);
  and and_27 (and_27_out, and_26_out, not_12_out, xor_3_out);
  assign SC_Reset = and_27_out ? 1'b1 : 1'bz;  // Controlled_Buffer controlled_buffer_36
  nor nor_1 (nor_1_out, ADDRESS[5], ADDRESS[6]);
  nor nor_2 (nor_2_out, ADDRESS[5], ADDRESS[6]);
  xor xor_1 (xor_1_out, DESTREG[2], ADDRESS[7]);
  assign RF_OutASel = and_23_out ? ADDRESS[6:5] : 2'bz;  // Controlled_Buffer controlled_buffer_37
  assign ALU_FunSel = and_23_out ? 4'b0100 : 4'bz;  // Controlled_Buffer controlled_buffer_38
  assign MuxBSel = and_23_out ? 2'b11 : 2'bz;  // Controlled_Buffer controlled_buffer_39
  assign RF_FunSel = and_23_out ? 2'b00 : 2'bz;  // Controlled_Buffer controlled_buffer_40
  assign AR_FunSel = and_23_out ? 2'b00 : 2'bz;  // Controlled_Buffer controlled_buffer_41
  Decoder #(.select(3), .disabled(0)) decoder_4 (
    .out0(decoder_4_out3[3]), .out1(decoder_4_out3[2]), .out2(decoder_4_out3[1]), .out3(decoder_4_out3[0]),
    .out4(or_8_out[2]), .out5(or_8_out[1]), .out6(decoder_4_out6), .out7(decoder_4_out7),
    .sel({DESTREG, ADDRMODE}), .en(and_23_out));
  assign AR_OutCSel = and_23_out ? ADDRESS[6:5] : 2'bz;  // Controlled_Buffer controlled_buffer_42
  assign MuxASel = and_23_out ? 2'b10 : 2'bz;  // Controlled_Buffer controlled_buffer_43
  xor xor_2 (xor_2_out, DESTREG[2], ADDRESS[7]);
  or or_5 (or_5_out[0], decoder_3_out6, decoder_3_out7);
  xor xor_3 (xor_3_out, DESTREG[2], ADDRESS[7]);
  or or_6 (or_6_out, ADDRESS[5], ADDRESS[6]);
  and and_28 (and_28_out, ADDRESS[4], nor_1_out);
  and and_29 (and_29_out, and_28_out, and_32_out);
  assign RF_RegSel = and_29_out ? 4'b0100 : 4'bz;  // Controlled_Buffer controlled_buffer_44
  or or_7 (or_7_out, ADDRESS[5], ADDRESS[6]);
  and and_30 (and_30_out, ADDRESS[4], nor_2_out);
  and and_31 (and_31_out, and_30_out, and_35_out);
  assign RF_RegSel = and_31_out ? 4'b0100 : 4'bz;  // Controlled_Buffer controlled_buffer_45
  or or_8 (or_8_out[0], decoder_4_out6, decoder_4_out7);
  and and_32 (and_32_out, D00, T3);
  and and_33 (and_33_out, ADDRESS[4], or_6_out);
  and and_34 (and_34_out, and_33_out, and_32_out);
  or or_9 (or_9_out, and_29_out, and_34_out);
  and and_35 (and_35_out, D01, T3);
  and and_36 (and_36_out, ADDRESS[4], or_7_out);
  and and_37 (and_37_out, and_36_out, and_35_out);
  or or_10 (or_10_out, and_31_out, and_37_out);
  and and_38 (and_38_out, D02, T5);
  assign IR_LH = T0 ? 1'b0 : 1'bz;  // Controlled_Buffer controlled_buffer_46
  assign IR_Enable = T0 ? 1'b1 : 1'bz;  // Controlled_Buffer controlled_buffer_47
  assign IR_FunSel = T0 ? 2'b00 : 2'bz;  // Controlled_Buffer controlled_buffer_48
  assign Mem_load = T0 ? 1'b1 : 1'bz;  // Controlled_Buffer controlled_buffer_49
  assign Mem_str = T0 ? 1'b0 : 1'bz;  // Controlled_Buffer controlled_buffer_50
  assign Mem_sel = T0 ? 1'b0 : 1'bz;  // Controlled_Buffer controlled_buffer_51
  assign Mem_clr = T0 ? 1'b0 : 1'bz;  // Controlled_Buffer controlled_buffer_52
  assign AR_FunSel = T0 ? 2'b10 : 2'bz;  // Controlled_Buffer controlled_buffer_53
  assign AR_RegSel = T0 ? 3'b001 : 3'bz;  // Controlled_Buffer controlled_buffer_54
  assign AR_OutCSel = T0 ? 2'b10 : 2'bz;  // Controlled_Buffer controlled_buffer_55
  assign RF_RegSel = and_34_out ? 4'b1000 : 4'bz;  // Controlled_Buffer controlled_buffer_56
  assign RF_FunSel = or_9_out ? 2'b00 : 2'bz;  // Controlled_Buffer controlled_buffer_57
  assign AR_OutCSel = or_9_out ? ADDRESS[3:2] : 2'bz;  // Controlled_Buffer controlled_buffer_58
  assign MuxASel = or_9_out ? 2'b10 : 2'bz;  // Controlled_Buffer controlled_buffer_59
  assign RF_RegSel = and_37_out ? 4'b1000 : 4'bz;  // Controlled_Buffer controlled_buffer_60
  assign RF_FunSel = or_10_out ? 2'b00 : 2'bz;  // Controlled_Buffer controlled_buffer_61
  assign AR_OutCSel = or_10_out ? ADDRESS[3:2] : 2'bz;  // Controlled_Buffer controlled_buffer_62
  assign MuxASel = or_10_out ? 2'b10 : 2'bz;  // Controlled_Buffer controlled_buffer_63
  isEqual isequal_7 (.in_1(ADDRESS[7:5]), .in_2({DESTREG, ADDRMODE}), .out_3(isequal_7_out_3));
  and and_39 (and_39_out, D02, T2);
  not not_13 (not_13_out, isequal_7_out_3);
  and and_40 (and_40_out, and_39_out, not_13_out, and_46_out);
  isEqual isequal_8 (.in_1(ADDRESS[7:5]), .in_2({DESTREG, ADDRMODE}), .out_3(isequal_8_out_3));
  and and_41 (and_41_out, D02, T3);
  not not_14 (not_14_out, isequal_8_out_3);
  and and_42 (and_42_out, and_41_out, not_14_out, and_47_out);
  assign RF_OutASel = and_42_out ? 2'b11 : 2'bz;  // Controlled_Buffer controlled_buffer_64
  assign ALU_FunSel = and_42_out ? 4'b0100 : 4'bz;  // Controlled_Buffer controlled_buffer_65
  assign MuxBSel = and_42_out ? 2'b11 : 2'bz;  // Controlled_Buffer controlled_buffer_66
  assign AR_RegSel = and_42_out ? or_11_out : 3'bz;  // Controlled_Buffer controlled_buffer_67
  assign AR_FunSel = and_42_out ? 2'b00 : 2'bz;  // Controlled_Buffer controlled_buffer_68
  isEqual isequal_9 (.in_1(ADDRESS[7:5]), .in_2({DESTREG, ADDRMODE}), .out_3(isequal_9_out_3));
  and and_43 (and_43_out, D02, T4);
  not not_15 (not_15_out, isequal_9_out_3);
  and and_44 (and_44_out, and_43_out, not_15_out, and_48_out);
  assign RF_RegSel = and_44_out ? decoder_7_out3 : 4'bz;  // Controlled_Buffer controlled_buffer_69
  assign AR_RegSel = and_44_out ? or_12_out : 3'bz;  // Controlled_Buffer controlled_buffer_70
  assign RF_FunSel = and_44_out ? 2'b01 : 2'bz;  // Controlled_Buffer controlled_buffer_71
  assign AR_FunSel = and_44_out ? 2'b01 : 2'bz;  // Controlled_Buffer controlled_buffer_72
  isEqual isequal_10 (.in_1(ADDRESS[7:5]), .in_2({DESTREG, ADDRMODE}), .out_3(isequal_10_out_3));
  not not_16 (not_16_out, isequal_10_out_3);
  and and_45 (and_45_out, and_38_out, not_16_out, and_49_out);
  assign SC_Reset = and_45_out ? 1'b1 : 1'bz;  // Controlled_Buffer controlled_buffer_73
  Decoder #(.select(5), .enable("false")) decoder_5 (
    .out0(D00), .out1(D01), .out2(D02), .out3(D03), .out4(D04), .out5(D05), .out6(D06), .out7(D07),
    .out8(D08), .out9(D09), .out10(D0A), .out11(D0B), .out12(D0C), .out13(D0D), .out14(D0E), .sel(Instruction));  // open: out15, out16, out17, out18, out19, out20, out21, out22, out23, out24, out25, out26, out27, out28, out29, out30, out31
  and and_46 (and_46_out, DESTREG[2], ADDRESS[7]);
  assign AR_OutCSel = and_40_out ? ADDRESS[6:5] : 2'bz;  // Controlled_Buffer controlled_buffer_74
  assign MuxASel = and_40_out ? 2'b10 : 2'bz;  // Controlled_Buffer controlled_buffer_75
  assign RF_RegSel = and_40_out ? 4'b0001 : 4'bz;  // Controlled_Buffer controlled_buffer_76
  assign RF_FunSel = and_40_out ? 2'b00 : 2'bz;  // Controlled_Buffer controlled_buffer_77
  and and_47 (and_47_out, DESTREG[2], ADDRESS[7]);
  Decoder #(.select(3), .disabled(0)) decoder_6 (
    .out4(or_11_out[2]), .out5(or_11_out[1]), .out6(decoder_6_out6), .out7(decoder_6_out7),
    .sel({DESTREG, ADDRMODE}), .en(and_42_out));  // open: out0, out1, out2, out3
  or or_11 (or_11_out[0], decoder_6_out6, decoder_6_out7);
  and and_48 (and_48_out, DESTREG[2], ADDRESS[7]);
  Decoder #(.select(3), .disabled(0)) decoder_7 (
    .out0(decoder_7_out3[3]), .out1(decoder_7_out3[2]), .out2(decoder_7_out3[1]), .out3(decoder_7_out3[0]),
    .out4(or_12_out[2]), .out5(or_12_out[1]), .out6(decoder_7_out6), .out7(decoder_7_out7),
    .sel({DESTREG, ADDRMODE}), .en(and_44_out));
  or or_12 (or_12_out[0], decoder_7_out6, decoder_7_out7);
  and and_49 (and_49_out, DESTREG[2], ADDRESS[7]);
  assign IR_LH = T1 ? 1'b1 : 1'bz;  // Controlled_Buffer controlled_buffer_78
  assign IR_Enable = T1 ? 1'b1 : 1'bz;  // Controlled_Buffer controlled_buffer_79
  assign IR_FunSel = T1 ? 2'b00 : 2'bz;  // Controlled_Buffer controlled_buffer_80
  assign Mem_load = T1 ? 1'b1 : 1'bz;  // Controlled_Buffer controlled_buffer_81
  assign Mem_str = T1 ? 1'b0 : 1'bz;  // Controlled_Buffer controlled_buffer_82
  assign Mem_sel = T1 ? 1'b0 : 1'bz;  // Controlled_Buffer controlled_buffer_83
  assign Mem_clr = T1 ? 1'b0 : 1'bz;  // Controlled_Buffer controlled_buffer_84
  assign AR_FunSel = T1 ? 2'b10 : 2'bz;  // Controlled_Buffer controlled_buffer_85
  assign AR_RegSel = T1 ? 3'b001 : 3'bz;  // Controlled_Buffer controlled_buffer_86
  assign AR_OutCSel = T1 ? 2'b10 : 2'bz;  // Controlled_Buffer controlled_buffer_87
  and and_50 (and_50_out, ADDRESS[7], and_51_out);
  and and_51 (and_51_out, ADDRESS[2], ADDRESS[3]);
  and and_52 (and_52_out, ADDRESS[7], and_53_out);
  and and_53 (and_53_out, ADDRESS[2], ADDRESS[3]);
  and and_54 (and_54_out, and_50_out, and_68_out);
  assign RF_OutASel = and_54_out ? 2'b10 : 2'bz;  // Controlled_Buffer controlled_buffer_88
  not not_17 (not_17_out, ARFARF);
  and and_55 (and_55_out, and_52_out, and_70_out);
  assign RF_OutBSel = and_55_out ? 2'b10 : 2'bz;  // Controlled_Buffer controlled_buffer_89
  not not_18 (not_18_out, ARFARF);
  and and_56 (and_56_out, D02, T2);
  and and_57 (and_57_out, D02, T3);
  and and_58 (and_58_out, D02, T4);
  assign Mem_str = D02 ? 1'b0 : 1'bz;  // Controlled_Buffer controlled_buffer_90
  assign Mem_load = D02 ? 1'b1 : 1'bz;  // Controlled_Buffer controlled_buffer_91
  assign Mem_clr = D02 ? 1'b0 : 1'bz;  // Controlled_Buffer controlled_buffer_92
  assign Mem_sel = D02 ? 1'b0 : 1'bz;  // Controlled_Buffer controlled_buffer_93
  and and_59 (and_59_out, ADDRESS[7], nand_3_out);
  nand nand_3 (nand_3_out, ADDRESS[2], ADDRESS[3]);
  and and_60 (and_60_out, and_59_out, and_68_out);
  or or_13 (or_13_out, and_54_out, and_60_out);
  and and_61 (and_61_out, not_17_out, or_13_out);
  assign RF_OutBSel = and_61_out ? ADDRESS[3:2] : 2'bz;  // Controlled_Buffer controlled_buffer_94
  and and_62 (and_62_out, ADDRESS[7], nand_4_out);
  nand nand_4 (nand_4_out, ADDRESS[2], ADDRESS[3]);
  and and_63 (and_63_out, and_62_out, and_70_out);
  or or_14 (or_14_out, and_55_out, and_63_out);
  and and_64 (and_64_out, not_18_out, or_14_out);
  assign RF_OutASel = and_64_out ? ADDRESS[3:2] : 2'bz;  // Controlled_Buffer controlled_buffer_95
  and and_65 (and_65_out, and_56_out, isequal_12_out_3);
  Decoder #(.select(3), .disabled(0)) decoder_8 (
    .out0(decoder_8_out3[3]), .out1(decoder_8_out3[2]), .out2(decoder_8_out3[1]), .out3(decoder_8_out3[0]),
    .out4(or_15_out[2]), .out5(or_15_out[1]), .out6(decoder_8_out6), .out7(decoder_8_out7),
    .sel({DESTREG, ADDRMODE}), .en(and_65_out));
  assign RF_RegSel = and_65_out ? decoder_8_out3 : 4'bz;  // Controlled_Buffer controlled_buffer_96
  assign AR_RegSel = and_65_out ? or_15_out : 3'bz;  // Controlled_Buffer controlled_buffer_97
  assign RF_FunSel = and_65_out ? 2'b01 : 2'bz;  // Controlled_Buffer controlled_buffer_98
  assign AR_FunSel = and_65_out ? 2'b01 : 2'bz;  // Controlled_Buffer controlled_buffer_99
  and and_66 (and_66_out, and_57_out, isequal_13_out_3);
  assign ALU_FunSel = and_66_out ? 4'b0100 : 4'bz;  // Controlled_Buffer controlled_buffer_100
  assign RF_OutASel = and_66_out ? ADDRESS[6:5] : 2'bz;  // Controlled_Buffer controlled_buffer_101
  assign RF_RegSel = and_66_out ? 4'b0000 : 4'bz;  // Controlled_Buffer controlled_buffer_102
  assign AR_RegSel = and_66_out ? 3'b000 : 3'bz;  // Controlled_Buffer controlled_buffer_103
  isEqual isequal_11 (.in_1(ADDRESS[7:5]), .in_2({DESTREG, ADDRMODE}), .out_3(isequal_11_out_3));
  and and_67 (and_67_out, and_58_out, isequal_11_out_3);
  assign SC_Reset = and_67_out ? 1'b1 : 1'bz;  // Controlled_Buffer controlled_buffer_104
  assign IR_Enable = T2 ? 1'b0 : 1'bz;  // Controlled_Buffer controlled_buffer_105
  and and_68 (and_68_out, D00, T4);
  and and_69 (ARFARF, and_59_out, and_72_out);
  assign RF_OutASel = and_60_out ? 2'b11 : 2'bz;  // Controlled_Buffer controlled_buffer_106
  assign RF_RegSel = and_68_out ? decoder_9_out3 : 4'bz;  // Controlled_Buffer controlled_buffer_107
  assign AR_RegSel = and_68_out ? or_18_out : 3'bz;  // Controlled_Buffer controlled_buffer_108
  and and_70 (and_70_out, D01, T4);
  and and_71 (ARFARF, and_62_out, and_74_out);
  assign RF_OutBSel = and_63_out ? 2'b11 : 2'bz;  // Controlled_Buffer controlled_buffer_109
  assign RF_RegSel = and_70_out ? decoder_10_out3 : 4'bz;  // Controlled_Buffer controlled_buffer_110
  assign AR_RegSel = and_70_out ? or_21_out : 3'bz;  // Controlled_Buffer controlled_buffer_111
  isEqual isequal_12 (.in_1(ADDRESS[7:5]), .in_2({DESTREG, ADDRMODE}), .out_3(isequal_12_out_3));
  or or_15 (or_15_out[0], decoder_8_out6, decoder_8_out7);
  isEqual isequal_13 (.in_1(ADDRESS[7:5]), .in_2({DESTREG, ADDRMODE}), .out_3(isequal_13_out_3));
  and and_72 (and_72_out, ADDRESS[4], or_16_out);
  and and_73 (and_73_out, and_68_out, and_72_out);
  assign RF_OutBSel = and_73_out ? 2'b00 : 2'bz;  // Controlled_Buffer controlled_buffer_112
  assign MuxASel = and_68_out ? 2'b11 : 2'bz;  // Controlled_Buffer controlled_buffer_113
  assign MuxBSel = and_68_out ? 2'b11 : 2'bz;  // Controlled_Buffer controlled_buffer_114
  assign ALU_FunSel = and_68_out ? 4'b0101 : 4'bz;  // Controlled_Buffer controlled_buffer_115
  assign RF_FunSel = and_68_out ? 2'b00 : 2'bz;  // Controlled_Buffer controlled_buffer_116
  assign AR_FunSel = and_68_out ? 2'b00 : 2'bz;  // Controlled_Buffer controlled_buffer_117
  Decoder #(.select(3), .disabled(0)) decoder_9 (
    .out0(decoder_9_out3[3]), .out1(decoder_9_out3[2]), .out2(decoder_9_out3[1]), .out3(decoder_9_out3[0]),
    .out4(or_18_out[2]), .out5(or_18_out[1]), .out6(decoder_9_out6), .out7(decoder_9_out7),
    .sel(controlled_buffer_118_out), .en(and_68_out));
  assign controlled_buffer_118_out = and_68_out ? {DESTREG, ADDRMODE} : 3'bz;  // Controlled_Buffer controlled_buffer_118
  and and_74 (and_74_out, ADDRESS[4], or_19_out);
  and and_75 (and_75_out, and_70_out, and_74_out);
  assign RF_OutASel = and_75_out ? 2'b00 : 2'bz;  // Controlled_Buffer controlled_buffer_119
  assign MuxASel = and_70_out ? 2'b11 : 2'bz;  // Controlled_Buffer controlled_buffer_120
  assign MuxBSel = and_70_out ? 2'b11 : 2'bz;  // Controlled_Buffer controlled_buffer_121
  assign ALU_FunSel = and_70_out ? 4'b0110 : 4'bz;  // Controlled_Buffer controlled_buffer_122
  assign RF_FunSel = and_70_out ? 2'b00 : 2'bz;  // Controlled_Buffer controlled_buffer_123
  assign AR_FunSel = and_70_out ? 2'b00 : 2'bz;  // Controlled_Buffer controlled_buffer_124
  assign controlled_buffer_125_out = and_70_out ? {DESTREG, ADDRMODE} : 3'bz;  // Controlled_Buffer controlled_buffer_125
  Decoder #(.select(3), .disabled(0)) decoder_10 (
    .out0(decoder_10_out3[3]), .out1(decoder_10_out3[2]), .out2(decoder_10_out3[1]),
    .out3(decoder_10_out3[0]), .out4(or_21_out[2]), .out5(or_21_out[1]), .out6(decoder_10_out6),
    .out7(decoder_10_out7), .sel(controlled_buffer_125_out), .en(and_70_out));
  or or_16 (or_16_out, ADDRESS[5], ADDRESS[6]);
  and and_76 (and_76_out, and_68_out, and_81_out);
  or or_17 (or_17_out, and_73_out, and_76_out);
  or or_18 (or_18_out[0], decoder_9_out6, decoder_9_out7);
  or or_19 (or_19_out, ADDRESS[5], ADDRESS[6]);
  and and_77 (and_77_out, and_70_out, and_83_out);
  or or_20 (or_20_out, and_75_out, and_77_out);
  or or_21 (or_21_out[0], decoder_10_out6, decoder_10_out7);
  and and_78 (and_78_out, D03, T2);
  and and_79 (and_79_out, D03, T3);
  and and_80 (and_80_out, D03, T4);
  and and_81 (and_81_out, ADDRESS[4], nor_3_out);
  nor nor_3 (nor_3_out, ADDRESS[5], ADDRESS[6]);
  assign RF_OutBSel = and_76_out ? 2'b01 : 2'bz;  // Controlled_Buffer controlled_buffer_126
  not not_19 (not_19_out, ARFARF);
  and and_82 (and_82_out, or_17_out, not_19_out);
  assign RF_OutASel = and_82_out ? ADDRESS[6:5] : 2'bz;  // Controlled_Buffer controlled_buffer_127
  assign RF_OutASel = ARFARF ? 2'b11 : 2'bz;  // Controlled_Buffer controlled_buffer_128
  assign RF_OutBSel = ARFARF ? 2'b00 : 2'bz;  // Controlled_Buffer controlled_buffer_129
  and and_83 (and_83_out, ADDRESS[4], nor_4_out);
  nor nor_4 (nor_4_out, ADDRESS[5], ADDRESS[6]);
  assign RF_OutASel = and_77_out ? 2'b01 : 2'bz;  // Controlled_Buffer controlled_buffer_130
  not not_20 (not_20_out, ARFARF);
  and and_84 (and_84_out, or_20_out, not_20_out);
  assign RF_OutBSel = and_84_out ? ADDRESS[6:5] : 2'bz;  // Controlled_Buffer controlled_buffer_131
  assign RF_OutBSel = ARFARF ? 2'b11 : 2'bz;  // Controlled_Buffer controlled_buffer_132
  assign RF_OutASel = ARFARF ? 2'b00 : 2'bz;  // Controlled_Buffer controlled_buffer_133
  isEqual isequal_14 (.in_1(ADDRESS[7:5]), .in_2({DESTREG, ADDRMODE}), .out_3(isequal_14_out_3));
  not not_21 (not_21_out, isequal_14_out_3);
  and and_85 (and_85_out, and_78_out, not_21_out, and_88_out);
  assign RF_OutASel = and_85_out ? ADDRESS[6:5] : 2'bz;  // Controlled_Buffer controlled_buffer_134
  assign ALU_FunSel = and_85_out ? 4'b0100 : 4'bz;  // Controlled_Buffer controlled_buffer_135
  assign MuxASel = and_85_out ? 2'b11 : 2'bz;  // Controlled_Buffer controlled_buffer_136
  assign RF_FunSel = and_85_out ? 2'b00 : 2'bz;  // Controlled_Buffer controlled_buffer_137
  Decoder #(.select(3), .disabled(0)) decoder_11 (
    .out0(decoder_11_out3[3]), .out1(decoder_11_out3[2]), .out2(decoder_11_out3[1]),
    .out3(decoder_11_out3[0]), .out4(or_22_out[2]), .out5(or_22_out[1]), .out6(decoder_11_out6),
    .out7(decoder_11_out7), .sel({DESTREG, ADDRMODE}), .en(and_85_out));
  assign RF_RegSel = and_85_out ? decoder_11_out3 : 4'bz;  // Controlled_Buffer controlled_buffer_138
  assign AR_RegSel = and_85_out ? or_22_out : 3'bz;  // Controlled_Buffer controlled_buffer_139
  isEqual isequal_15 (.in_1(ADDRESS[7:5]), .in_2({DESTREG, ADDRMODE}), .out_3(isequal_15_out_3));
  not not_22 (not_22_out, isequal_15_out_3);
  and and_86 (and_86_out, and_79_out, not_22_out, and_89_out);
  Decoder #(.select(3), .disabled(0)) decoder_12 (
    .out0(decoder_12_out3[3]), .out1(decoder_12_out3[2]), .out2(decoder_12_out3[1]),
    .out3(decoder_12_out3[0]), .out4(or_23_out[2]), .out5(or_23_out[1]), .out6(decoder_12_out6),
    .out7(decoder_12_out7), .sel({DESTREG, ADDRMODE}), .en(and_86_out));
  assign RF_RegSel = and_86_out ? decoder_12_out3 : 4'bz;  // Controlled_Buffer controlled_buffer_140
  assign AR_RegSel = and_86_out ? or_23_out : 3'bz;  // Controlled_Buffer controlled_buffer_141
  assign RF_FunSel = and_86_out ? 2'b10 : 2'bz;  // Controlled_Buffer controlled_buffer_142
  assign AR_FunSel = and_86_out ? 2'b10 : 2'bz;  // Controlled_Buffer controlled_buffer_143
  isEqual isequal_16 (.in_1(ADDRESS[7:5]), .in_2({DESTREG, ADDRMODE}), .out_3(isequal_16_out_3));
  not not_23 (not_23_out, isequal_16_out_3);
  and and_87 (and_87_out, and_80_out, not_23_out, and_90_out);
  assign SC_Reset = and_87_out ? 1'b1 : 1'bz;  // Controlled_Buffer controlled_buffer_144
  not not_24 (not_24_out, DESTREG[2]);
  not not_25 (not_25_out, ADDRESS[7]);
  and and_88 (and_88_out, not_24_out, not_25_out);
  or or_22 (or_22_out[0], decoder_11_out6, decoder_11_out7);
  not not_26 (not_26_out, ADDRESS[7]);
  not not_27 (not_27_out, DESTREG[2]);
  and and_89 (and_89_out, not_27_out, not_26_out);
  or or_23 (or_23_out[0], decoder_12_out6, decoder_12_out7);
  not not_28 (not_28_out, ADDRESS[7]);
  not not_29 (not_29_out, DESTREG[2]);
  and and_90 (and_90_out, not_29_out, not_28_out);
  and and_91 (and_91_out, D00, T5);
  not not_30 (not_30_out, and_68_out);
  nor nor_5 (nor_5_out, and_82_out, and_61_out, not_30_out, ARFARF);
  assign RF_OutASel = nor_5_out ? ADDRESS[6:5] : 2'bz;  // Controlled_Buffer controlled_buffer_145
  assign RF_OutBSel = nor_5_out ? ADDRESS[3:2] : 2'bz;  // Controlled_Buffer controlled_buffer_146
  and and_92 (and_92_out, D01, T5);
  not not_31 (not_31_out, and_70_out);
  nor nor_6 (nor_6_out, and_84_out, and_64_out, not_31_out, ARFARF);
  assign RF_OutBSel = nor_6_out ? ADDRESS[6:5] : 2'bz;  // Controlled_Buffer controlled_buffer_147
  assign RF_OutASel = nor_6_out ? ADDRESS[3:2] : 2'bz;  // Controlled_Buffer controlled_buffer_148
  assign SC_Reset = and_91_out ? 1'b1 : 1'bz;  // Controlled_Buffer controlled_buffer_149
  assign SC_Reset = and_92_out ? 1'b1 : 1'bz;  // Controlled_Buffer controlled_buffer_150
  and and_93 (and_93_out, D03, T2);
  assign RF_RegSel = and_98_out ? decoder_13_out3 : 4'bz;  // Controlled_Buffer controlled_buffer_151
  assign AR_RegSel = and_98_out ? or_25_out : 3'bz;  // Controlled_Buffer controlled_buffer_152
  isEqual isequal_17 (.in_1(ADDRESS[7:5]), .in_2({DESTREG, ADDRMODE}), .out_3(isequal_17_out_3));
  and and_94 (and_94_out, D03, T3);
  not not_32 (not_32_out, isequal_17_out_3);
  and and_95 (and_95_out, and_94_out, not_32_out, xor_5_out);
  assign RF_RegSel = and_95_out ? decoder_14_out3 : 4'bz;  // Controlled_Buffer controlled_buffer_153
  assign AR_RegSel = and_95_out ? or_24_out : 3'bz;  // Controlled_Buffer controlled_buffer_154
  assign RF_FunSel = and_95_out ? 2'b10 : 2'bz;  // Controlled_Buffer controlled_buffer_155
  assign AR_FunSel = and_95_out ? 2'b10 : 2'bz;  // Controlled_Buffer controlled_buffer_156
  isEqual isequal_18 (.in_1(ADDRESS[7:5]), .in_2({DESTREG, ADDRMODE}), .out_3(isequal_18_out_3));
  and and_96 (and_96_out, D03, T4);
  not not_33 (not_33_out, isequal_18_out_3);
  and and_97 (and_97_out, and_96_out, not_33_out, xor_6_out);
  assign SC_Reset = and_97_out ? 1'b1 : 1'bz;  // Controlled_Buffer controlled_buffer_157
  isEqual isequal_19 (.in_1(ADDRESS[7:5]), .in_2({DESTREG, ADDRMODE}), .out_3(isequal_19_out_3));
  xor xor_4 (xor_4_out, DESTREG[2], ADDRESS[7]);
  not not_34 (not_34_out, isequal_19_out_3);
  and and_98 (and_98_out, and_93_out, not_34_out, xor_4_out);
  assign RF_OutASel = and_98_out ? ADDRESS[6:5] : 2'bz;  // Controlled_Buffer controlled_buffer_158
  assign ALU_FunSel = and_98_out ? 4'b0100 : 4'bz;  // Controlled_Buffer controlled_buffer_159
  assign MuxBSel = and_98_out ? 2'b11 : 2'bz;  // Controlled_Buffer controlled_buffer_160
  assign RF_FunSel = and_98_out ? 2'b00 : 2'bz;  // Controlled_Buffer controlled_buffer_161
  assign AR_FunSel = and_98_out ? 2'b00 : 2'bz;  // Controlled_Buffer controlled_buffer_162
  Decoder #(.select(3), .disabled(0)) decoder_13 (
    .out0(decoder_13_out3[3]), .out1(decoder_13_out3[2]), .out2(decoder_13_out3[1]),
    .out3(decoder_13_out3[0]), .out4(or_25_out[2]), .out5(or_25_out[1]), .out6(decoder_13_out6),
    .out7(decoder_13_out7), .sel({DESTREG, ADDRMODE}), .en(and_98_out));
  assign AR_OutCSel = and_98_out ? ADDRESS[6:5] : 2'bz;  // Controlled_Buffer controlled_buffer_163
  assign MuxASel = and_98_out ? 2'b10 : 2'bz;  // Controlled_Buffer controlled_buffer_164
  xor xor_5 (xor_5_out, DESTREG[2], ADDRESS[7]);
  Decoder #(.select(3), .disabled(0)) decoder_14 (
    .out0(decoder_14_out3[3]), .out1(decoder_14_out3[2]), .out2(decoder_14_out3[1]),
    .out3(decoder_14_out3[0]), .out4(or_24_out[2]), .out5(or_24_out[1]), .out6(decoder_14_out6),
    .out7(decoder_14_out7), .sel({DESTREG, ADDRMODE}), .en(and_95_out));
  or or_24 (or_24_out[0], decoder_14_out6, decoder_14_out7);
  xor xor_6 (xor_6_out, DESTREG[2], ADDRESS[7]);
  or or_25 (or_25_out[0], decoder_13_out6, decoder_13_out7);
  and and_99 (and_99_out, D04, T2);
  and and_100 (and_100_out, ADDRESS[2], ADDRESS[3]);
  and and_101 (and_101_out, ADDRESS[2], ADDRESS[3]);
  and and_102 (and_102_out, D03, T5);
  and and_103 (and_103_out, and_99_out, ADDRMODE);
  assign MuxBSel = and_103_out ? 2'b01 : 2'bz;  // Controlled_Buffer controlled_buffer_165
  assign AR_RegSel = and_103_out ? 3'b001 : 3'bz;  // Controlled_Buffer controlled_buffer_166
  assign AR_FunSel = and_103_out ? 2'b00 : 2'bz;  // Controlled_Buffer controlled_buffer_167
  and and_104 (and_104_out, D04, T3);
  and and_105 (and_105_out, and_104_out, ADDRMODE);
  assign SC_Reset = and_105_out ? 1'b1 : 1'bz;  // Controlled_Buffer controlled_buffer_168
  assign Mem_str = D04 ? 1'b0 : 1'bz;  // Controlled_Buffer controlled_buffer_169
  assign Mem_load = D04 ? 1'b1 : 1'bz;  // Controlled_Buffer controlled_buffer_170
  assign Mem_clr = D04 ? 1'b0 : 1'bz;  // Controlled_Buffer controlled_buffer_171
  assign Mem_sel = D04 ? 1'b0 : 1'bz;  // Controlled_Buffer controlled_buffer_172
  assign RF_RegSel = D04 ? 4'b0000 : 4'bz;  // Controlled_Buffer controlled_buffer_173
  nand nand_5 (nand_5_out, ADDRESS[2], ADDRESS[3]);
  and and_106 (and_106_out, ADDRESS[7], and_100_out);
  and and_107 (and_107_out, and_106_out, and_116_out);
  assign RF_RegSel = and_107_out ? 4'b0010 : 4'bz;  // Controlled_Buffer controlled_buffer_174
  nand nand_6 (nand_6_out, ADDRESS[2], ADDRESS[3]);
  and and_108 (and_108_out, ADDRESS[7], and_101_out);
  and and_109 (and_109_out, and_108_out, and_119_out);
  assign RF_RegSel = and_109_out ? 4'b0010 : 4'bz;  // Controlled_Buffer controlled_buffer_175
  and and_110 (and_110_out, D03, T2);
  isEqual isequal_20 (.in_1(ADDRESS[7:5]), .in_2({DESTREG, ADDRMODE}), .out_3(isequal_20_out_3));
  and and_111 (and_111_out, D03, T3);
  not not_35 (not_35_out, isequal_20_out_3);
  and and_112 (and_112_out, and_111_out, not_35_out, and_124_out);
  assign AR_RegSel = and_112_out ? or_28_out : 3'bz;  // Controlled_Buffer controlled_buffer_176
  isEqual isequal_21 (.in_1(ADDRESS[7:5]), .in_2({DESTREG, ADDRMODE}), .out_3(isequal_21_out_3));
  and and_113 (and_113_out, D03, T4);
  not not_36 (not_36_out, isequal_21_out_3);
  and and_114 (and_114_out, and_113_out, not_36_out, and_125_out);
  assign RF_RegSel = and_114_out ? decoder_16_out3 : 4'bz;  // Controlled_Buffer controlled_buffer_177
  assign AR_RegSel = and_114_out ? or_29_out : 3'bz;  // Controlled_Buffer controlled_buffer_178
  isEqual isequal_22 (.in_1(ADDRESS[7:5]), .in_2({DESTREG, ADDRMODE}), .out_3(isequal_22_out_3));
  not not_37 (not_37_out, isequal_22_out_3);
  and and_115 (and_115_out, and_102_out, not_37_out, and_126_out);
  assign SC_Reset = and_115_out ? 1'b1 : 1'bz;  // Controlled_Buffer controlled_buffer_179
  and and_116 (and_116_out, D0D, T2);
  and and_117 (and_117_out, ADDRESS[7], nand_5_out);
  and and_118 (and_118_out, and_117_out, and_116_out);
  or or_26 (or_26_out, and_107_out, and_118_out);
  assign RF_FunSel = or_26_out ? 2'b00 : 2'bz;  // Controlled_Buffer controlled_buffer_180
  assign AR_OutCSel = or_26_out ? ADDRESS[6:5] : 2'bz;  // Controlled_Buffer controlled_buffer_181
  assign MuxASel = or_26_out ? 2'b10 : 2'bz;  // Controlled_Buffer controlled_buffer_182
  assign Mem_str = D0D ? 1'b0 : 1'bz;  // Controlled_Buffer controlled_buffer_183
  assign Mem_load = D0D ? 1'b1 : 1'bz;  // Controlled_Buffer controlled_buffer_184
  assign Mem_clr = D0D ? 1'b0 : 1'bz;  // Controlled_Buffer controlled_buffer_185
  assign Mem_sel = D0D ? 1'b0 : 1'bz;  // Controlled_Buffer controlled_buffer_186
  and and_119 (and_119_out, D0E, T2);
  and and_120 (and_120_out, ADDRESS[7], nand_6_out);
  and and_121 (and_121_out, and_120_out, and_119_out);
  or or_27 (or_27_out, and_109_out, and_121_out);
  assign RF_FunSel = or_27_out ? 2'b00 : 2'bz;  // Controlled_Buffer controlled_buffer_187
  assign AR_OutCSel = or_27_out ? ADDRESS[6:5] : 2'bz;  // Controlled_Buffer controlled_buffer_188
  assign MuxASel = or_27_out ? 2'b10 : 2'bz;  // Controlled_Buffer controlled_buffer_189
  assign Mem_str = D0D ? 1'b0 : 1'bz;  // Controlled_Buffer controlled_buffer_190
  assign Mem_load = D0D ? 1'b1 : 1'bz;  // Controlled_Buffer controlled_buffer_191
  assign Mem_clr = D0D ? 1'b0 : 1'bz;  // Controlled_Buffer controlled_buffer_192
  assign Mem_sel = D0D ? 1'b0 : 1'bz;  // Controlled_Buffer controlled_buffer_193
  isEqual isequal_23 (.in_1(ADDRESS[7:5]), .in_2({DESTREG, ADDRMODE}), .out_3(isequal_23_out_3));
  and and_122 (and_122_out, DESTREG[2], ADDRESS[7]);
  not not_38 (not_38_out, isequal_23_out_3);
  and and_123 (and_123_out, and_110_out, not_38_out, and_122_out);
  assign AR_OutCSel = and_123_out ? ADDRESS[6:5] : 2'bz;  // Controlled_Buffer controlled_buffer_194
  assign MuxASel = and_123_out ? 2'b10 : 2'bz;  // Controlled_Buffer controlled_buffer_195
  assign RF_RegSel = and_123_out ? 4'b0001 : 4'bz;  // Controlled_Buffer controlled_buffer_196
  assign RF_FunSel = and_123_out ? 2'b00 : 2'bz;  // Controlled_Buffer controlled_buffer_197
  and and_124 (and_124_out, DESTREG[2], ADDRESS[7]);
  assign RF_OutASel = and_112_out ? 2'b11 : 2'bz;  // Controlled_Buffer controlled_buffer_198
  assign ALU_FunSel = and_112_out ? 4'b0100 : 4'bz;  // Controlled_Buffer controlled_buffer_199
  assign MuxBSel = and_112_out ? 2'b11 : 2'bz;  // Controlled_Buffer controlled_buffer_200
  Decoder #(.select(3), .disabled(0)) decoder_15 (
    .out4(or_28_out[2]), .out5(or_28_out[1]), .out6(decoder_15_out6), .out7(decoder_15_out7),
    .sel({DESTREG, ADDRMODE}), .en(and_112_out));  // open: out0, out1, out2, out3
  assign AR_FunSel = and_112_out ? 2'b00 : 2'bz;  // Controlled_Buffer controlled_buffer_201
  and and_125 (and_125_out, DESTREG[2], ADDRESS[7]);
  Decoder #(.select(3), .disabled(0)) decoder_16 (
    .out0(decoder_16_out3[3]), .out1(decoder_16_out3[2]), .out2(decoder_16_out3[1]),
    .out3(decoder_16_out3[0]), .out4(or_29_out[2]), .out5(or_29_out[1]), .out6(decoder_16_out6),
    .out7(decoder_16_out7), .sel({DESTREG, ADDRMODE}), .en(and_114_out));
  assign RF_FunSel = and_114_out ? 2'b10 : 2'bz;  // Controlled_Buffer controlled_buffer_202
  assign AR_FunSel = and_114_out ? 2'b10 : 2'bz;  // Controlled_Buffer controlled_buffer_203
  and and_126 (and_126_out, DESTREG[2], ADDRESS[7]);
  assign RF_RegSel = and_118_out ? 4'b0001 : 4'bz;  // Controlled_Buffer controlled_buffer_204
  assign RF_RegSel = and_121_out ? 4'b0001 : 4'bz;  // Controlled_Buffer controlled_buffer_205
  or or_28 (or_28_out[0], decoder_15_out6, decoder_15_out7);
  or or_29 (or_29_out[0], decoder_16_out6, decoder_16_out7);
  and and_127 (and_127_out, D03, T3);
  and and_128 (and_128_out, D03, T4);
  and and_129 (and_129_out, Z, D05, T2);
  and and_130 (and_130_out, Z, D05, T3);
  and and_131 (and_131_out, D03, T2);
  and and_132 (and_132_out, and_131_out, isequal_24_out_3);
  Decoder #(.select(3), .disabled(0)) decoder_17 (
    .out0(decoder_17_out3[3]), .out1(decoder_17_out3[2]), .out2(decoder_17_out3[1]),
    .out3(decoder_17_out3[0]), .out4(or_30_out[2]), .out5(or_30_out[1]), .out6(decoder_17_out6),
    .out7(decoder_17_out7), .sel({DESTREG, ADDRMODE}), .en(and_132_out));
  assign RF_RegSel = and_132_out ? decoder_17_out3 : 4'bz;  // Controlled_Buffer controlled_buffer_206
  assign AR_RegSel = and_132_out ? or_30_out : 3'bz;  // Controlled_Buffer controlled_buffer_207
  assign RF_FunSel = and_132_out ? 2'b10 : 2'bz;  // Controlled_Buffer controlled_buffer_208
  assign AR_FunSel = and_132_out ? 2'b10 : 2'bz;  // Controlled_Buffer controlled_buffer_209
  assign ALU_FunSel = and_132_out ? 4'b0100 : 4'bz;  // Controlled_Buffer controlled_buffer_210
  assign RF_OutASel = and_132_out ? ADDRESS[6:5] : 2'bz;  // Controlled_Buffer controlled_buffer_211
  and and_133 (and_133_out, and_127_out, isequal_25_out_3);
  assign ALU_FunSel = and_133_out ? 4'b0100 : 4'bz;  // Controlled_Buffer controlled_buffer_212
  assign RF_OutASel = and_133_out ? ADDRESS[6:5] : 2'bz;  // Controlled_Buffer controlled_buffer_213
  assign RF_RegSel = and_133_out ? 4'b0000 : 4'bz;  // Controlled_Buffer controlled_buffer_214
  assign AR_RegSel = and_133_out ? 3'b000 : 3'bz;  // Controlled_Buffer controlled_buffer_215
  and and_134 (and_134_out, and_128_out, isequal_26_out_3);
  assign SC_Reset = and_134_out ? 1'b1 : 1'bz;  // Controlled_Buffer controlled_buffer_216
  assign Mem_str = D03 ? 1'b0 : 1'bz;  // Controlled_Buffer controlled_buffer_217
  assign Mem_load = D03 ? 1'b1 : 1'bz;  // Controlled_Buffer controlled_buffer_218
  assign Mem_clr = D03 ? 1'b0 : 1'bz;  // Controlled_Buffer controlled_buffer_219
  assign Mem_sel = D03 ? 1'b0 : 1'bz;  // Controlled_Buffer controlled_buffer_220
  and and_135 (and_135_out, and_129_out, ADDRMODE);
  assign MuxBSel = and_135_out ? 2'b01 : 2'bz;  // Controlled_Buffer controlled_buffer_221
  assign AR_RegSel = and_135_out ? 3'b001 : 3'bz;  // Controlled_Buffer controlled_buffer_222
  assign AR_FunSel = and_135_out ? 2'b00 : 2'bz;  // Controlled_Buffer controlled_buffer_223
  and and_136 (and_136_out, and_130_out, ADDRMODE);
  assign SC_Reset = and_136_out ? 1'b1 : 1'bz;  // Controlled_Buffer controlled_buffer_224
  assign Mem_str = D05 ? 1'b0 : 1'bz;  // Controlled_Buffer controlled_buffer_225
  assign Mem_load = D05 ? 1'b1 : 1'bz;  // Controlled_Buffer controlled_buffer_226
  assign Mem_clr = D05 ? 1'b0 : 1'bz;  // Controlled_Buffer controlled_buffer_227
  assign Mem_sel = D05 ? 1'b0 : 1'bz;  // Controlled_Buffer controlled_buffer_228
  assign RF_RegSel = D05 ? 4'b0000 : 4'bz;  // Controlled_Buffer controlled_buffer_229
  and and_137 (and_137_out, ADDRESS[4], nor_7_out);
  nor nor_7 (nor_7_out, ADDRESS[5], ADDRESS[6]);
  and and_138 (and_138_out, ADDRESS[4], nor_8_out);
  nor nor_8 (nor_8_out, ADDRESS[5], ADDRESS[6]);
  isEqual isequal_24 (.in_1(ADDRESS[7:5]), .in_2({DESTREG, ADDRMODE}), .out_3(isequal_24_out_3));
  or or_30 (or_30_out[0], decoder_17_out6, decoder_17_out7);
  isEqual isequal_25 (.in_1(ADDRESS[7:5]), .in_2({DESTREG, ADDRMODE}), .out_3(isequal_25_out_3));
  isEqual isequal_26 (.in_1(ADDRESS[7:5]), .in_2({DESTREG, ADDRMODE}), .out_3(isequal_26_out_3));
  or or_31 (or_31_out, ADDRESS[5], ADDRESS[6]);
  and and_139 (and_139_out, and_137_out, and_141_out);
  assign RF_RegSel = and_139_out ? 4'b0100 : 4'bz;  // Controlled_Buffer controlled_buffer_230
  or or_32 (or_32_out, ADDRESS[5], ADDRESS[6]);
  and and_140 (and_140_out, and_138_out, and_144_out);
  assign RF_RegSel = and_140_out ? 4'b0100 : 4'bz;  // Controlled_Buffer controlled_buffer_231
  and and_141 (and_141_out, D0D, T3);
  and and_142 (and_142_out, ADDRESS[4], or_31_out);
  and and_143 (and_143_out, and_142_out, and_141_out);
  or or_33 (or_33_out, and_139_out, and_143_out);
  assign RF_FunSel = or_33_out ? 2'b00 : 2'bz;  // Controlled_Buffer controlled_buffer_232
  assign AR_OutCSel = or_33_out ? ADDRESS[3:2] : 2'bz;  // Controlled_Buffer controlled_buffer_233
  assign MuxASel = or_33_out ? 2'b10 : 2'bz;  // Controlled_Buffer controlled_buffer_234
  and and_144 (and_144_out, D0E, T3);
  and and_145 (and_145_out, ADDRESS[4], or_32_out);
  and and_146 (and_146_out, and_145_out, and_144_out);
  or or_34 (or_34_out, and_140_out, and_146_out);
  assign RF_FunSel = or_34_out ? 2'b00 : 2'bz;  // Controlled_Buffer controlled_buffer_235
  assign AR_OutCSel = or_34_out ? ADDRESS[3:2] : 2'bz;  // Controlled_Buffer controlled_buffer_236
  assign MuxASel = or_34_out ? 2'b10 : 2'bz;  // Controlled_Buffer controlled_buffer_237
  not not_39 (not_39_out, Z);
  not not_40 (not_40_out, Z);
  assign RF_RegSel = and_143_out ? 4'b1000 : 4'bz;  // Controlled_Buffer controlled_buffer_238
  assign RF_RegSel = and_146_out ? 4'b1000 : 4'bz;  // Controlled_Buffer controlled_buffer_239
  and and_147 (and_147_out, D0B, T2);
  assign RF_RegSel = and_157_out ? decoder_18_out3 : 4'bz;  // Controlled_Buffer controlled_buffer_240
  assign AR_RegSel = and_157_out ? or_35_out : 3'bz;  // Controlled_Buffer controlled_buffer_241
  and and_148 (and_148_out, D0B, T3);
  and and_149 (and_149_out, and_148_out, and_158_out);
  assign SC_Reset = and_149_out ? 1'b1 : 1'bz;  // Controlled_Buffer controlled_buffer_242
  and and_150 (and_150_out, not_39_out, D06, T2);
  and and_151 (and_151_out, and_150_out, ADDRMODE);
  assign MuxBSel = and_151_out ? 2'b01 : 2'bz;  // Controlled_Buffer controlled_buffer_243
  assign AR_RegSel = and_151_out ? 3'b001 : 3'bz;  // Controlled_Buffer controlled_buffer_244
  assign AR_FunSel = and_151_out ? 2'b00 : 2'bz;  // Controlled_Buffer controlled_buffer_245
  and and_152 (and_152_out, not_40_out, D06, T3);
  and and_153 (and_153_out, and_152_out, ADDRMODE);
  assign SC_Reset = and_153_out ? 1'b1 : 1'bz;  // Controlled_Buffer controlled_buffer_246
  assign Mem_str = D06 ? 1'b0 : 1'bz;  // Controlled_Buffer controlled_buffer_247
  assign Mem_load = D06 ? 1'b1 : 1'bz;  // Controlled_Buffer controlled_buffer_248
  assign Mem_clr = D06 ? 1'b0 : 1'bz;  // Controlled_Buffer controlled_buffer_249
  assign Mem_sel = D06 ? 1'b0 : 1'bz;  // Controlled_Buffer controlled_buffer_250
  assign RF_RegSel = D06 ? 4'b0000 : 4'bz;  // Controlled_Buffer controlled_buffer_251
  and and_154 (and_154_out, ADDRESS[2], ADDRESS[3]);
  and and_155 (and_155_out, ADDRESS[2], ADDRESS[3]);
  not not_41 (not_41_out, ADDRESS[7]);
  not not_42 (not_42_out, DESTREG[2]);
  and and_156 (and_156_out, not_42_out, not_41_out);
  and and_157 (and_157_out, and_147_out, and_156_out);
  assign RF_OutASel = and_157_out ? ADDRESS[6:5] : 2'bz;  // Controlled_Buffer controlled_buffer_252
  assign ALU_FunSel = and_157_out ? 4'b0100 : 4'bz;  // Controlled_Buffer controlled_buffer_253
  assign MuxASel = and_157_out ? 2'b11 : 2'bz;  // Controlled_Buffer controlled_buffer_254
  assign RF_FunSel = and_157_out ? 2'b00 : 2'bz;  // Controlled_Buffer controlled_buffer_255
  Decoder #(.select(3), .disabled(0)) decoder_18 (
    .out0(decoder_18_out3[3]), .out1(decoder_18_out3[2]), .out2(decoder_18_out3[1]),
    .out3(decoder_18_out3[0]), .out4(or_35_out[2]), .out5(or_35_out[1]), .out6(decoder_18_out6),
    .out7(decoder_18_out7), .sel({DESTREG, ADDRMODE}), .en(and_157_out));
  not not_43 (not_43_out, ADDRESS[7]);
  not not_44 (not_44_out, DESTREG[2]);
  and and_158 (and_158_out, not_44_out, not_43_out);
  and and_159 (and_159_out, ADDRESS[7], and_154_out);
  and and_160 (and_160_out, and_159_out, and_176_out);
  assign RF_OutASel = and_160_out ? 2'b10 : 2'bz;  // Controlled_Buffer controlled_buffer_256
  and and_161 (and_161_out, ADDRESS[7], and_155_out);
  and and_162 (and_162_out, and_161_out, and_178_out);
  assign RF_OutASel = and_162_out ? 2'b10 : 2'bz;  // Controlled_Buffer controlled_buffer_257
  or or_35 (or_35_out[0], decoder_18_out6, decoder_18_out7);
  nand nand_7 (nand_7_out, ADDRESS[2], ADDRESS[3]);
  not not_45 (not_45_out, ARFARF);
  and and_163 (and_163_out, not_45_out, or_36_out);
  assign RF_OutBSel = and_163_out ? ADDRESS[3:2] : 2'bz;  // Controlled_Buffer controlled_buffer_258
  nand nand_8 (nand_8_out, ADDRESS[2], ADDRESS[3]);
  not not_46 (not_46_out, ARFARF);
  and and_164 (and_164_out, not_46_out, or_37_out);
  assign RF_OutBSel = and_164_out ? ADDRESS[3:2] : 2'bz;  // Controlled_Buffer controlled_buffer_259
  and and_165 (and_165_out, ADDRESS[7], nand_7_out);
  and and_166 (and_166_out, and_165_out, and_176_out);
  assign RF_OutASel = and_166_out ? 2'b11 : 2'bz;  // Controlled_Buffer controlled_buffer_260
  or or_36 (or_36_out, and_160_out, and_166_out);
  and and_167 (and_167_out, ADDRESS[7], nand_8_out);
  and and_168 (and_168_out, and_167_out, and_178_out);
  assign RF_OutASel = and_168_out ? 2'b11 : 2'bz;  // Controlled_Buffer controlled_buffer_261
  or or_37 (or_37_out, and_162_out, and_168_out);
  and and_169 (and_169_out, D0B, T2);
  and and_170 (and_170_out, D0B, T4);
  and and_171 (and_171_out, and_170_out, xor_7_out);
  assign Mem_str = D0B ? 1'b0 : 1'bz;  // Controlled_Buffer controlled_buffer_262
  assign Mem_load = D0B ? 1'b1 : 1'bz;  // Controlled_Buffer controlled_buffer_263
  assign Mem_clr = D0B ? 1'b0 : 1'bz;  // Controlled_Buffer controlled_buffer_264
  assign Mem_sel = D0B ? 1'b0 : 1'bz;  // Controlled_Buffer controlled_buffer_265
  and and_172 (and_172_out, D09, T2);
  not not_47 (not_47_out, ADDRMODE);
  and and_173 (and_173_out, and_172_out, not_47_out);
  assign AR_OutCSel = and_173_out ? 2'b00 : 2'bz;  // Controlled_Buffer controlled_buffer_266
  assign MuxASel = and_173_out ? 2'b01 : 2'bz;  // Controlled_Buffer controlled_buffer_267
  assign RF_FunSel = and_173_out ? 2'b00 : 2'bz;  // Controlled_Buffer controlled_buffer_268
  Decoder #(.select(2), .disabled(0)) decoder_19 (
    .out0(decoder_19_out3[3]), .out1(decoder_19_out3[2]), .out2(decoder_19_out3[1]),
    .out3(decoder_19_out3[0]), .sel(DESTREG), .en(and_173_out));
  assign RF_RegSel = and_173_out ? decoder_19_out3 : 4'bz;  // Controlled_Buffer controlled_buffer_269
  and and_174 (and_174_out, D09, T3);
  not not_48 (not_48_out, ADDRMODE);
  and and_175 (and_175_out, and_174_out, not_48_out);
  assign SC_Reset = and_175_out ? 1'b1 : 1'bz;  // Controlled_Buffer controlled_buffer_270
  and and_176 (and_176_out, D0D, T4);
  and and_177 (ARFARF, and_165_out, and_181_out);
  assign MuxASel = and_176_out ? 2'b11 : 2'bz;  // Controlled_Buffer controlled_buffer_271
  assign MuxBSel = and_176_out ? 2'b11 : 2'bz;  // Controlled_Buffer controlled_buffer_272
  assign ALU_FunSel = and_176_out ? 4'b0001 : 4'bz;  // Controlled_Buffer controlled_buffer_273
  assign RF_FunSel = and_176_out ? 2'b00 : 2'bz;  // Controlled_Buffer controlled_buffer_274
  assign AR_FunSel = and_176_out ? 2'b00 : 2'bz;  // Controlled_Buffer controlled_buffer_275
  assign controlled_buffer_276_out = and_176_out ? {DESTREG, ADDRMODE} : 3'bz;  // Controlled_Buffer controlled_buffer_276
  assign RF_RegSel = and_176_out ? decoder_21_out3 : 4'bz;  // Controlled_Buffer controlled_buffer_277
  assign AR_RegSel = and_176_out ? or_39_out : 3'bz;  // Controlled_Buffer controlled_buffer_278
  and and_178 (and_178_out, D0E, T4);
  and and_179 (ARFARF, and_167_out, and_183_out);
  assign MuxASel = and_178_out ? 2'b11 : 2'bz;  // Controlled_Buffer controlled_buffer_279
  assign MuxBSel = and_178_out ? 2'b11 : 2'bz;  // Controlled_Buffer controlled_buffer_280
  assign ALU_FunSel = and_178_out ? 4'b0000 : 4'bz;  // Controlled_Buffer controlled_buffer_281
  assign RF_FunSel = and_178_out ? 2'b00 : 2'bz;  // Controlled_Buffer controlled_buffer_282
  assign AR_FunSel = and_178_out ? 2'b00 : 2'bz;  // Controlled_Buffer controlled_buffer_283
  assign controlled_buffer_284_out = and_178_out ? {DESTREG, ADDRMODE} : 3'bz;  // Controlled_Buffer controlled_buffer_284
  assign RF_RegSel = and_178_out ? decoder_22_out3 : 4'bz;  // Controlled_Buffer controlled_buffer_285
  assign AR_RegSel = and_178_out ? or_41_out : 3'bz;  // Controlled_Buffer controlled_buffer_286
  and and_180 (and_180_out, and_169_out, xor_8_out);
  assign RF_OutASel = and_180_out ? ADDRESS[6:5] : 2'bz;  // Controlled_Buffer controlled_buffer_287
  assign ALU_FunSel = and_180_out ? 4'b0100 : 4'bz;  // Controlled_Buffer controlled_buffer_288
  assign MuxBSel = and_180_out ? 2'b11 : 2'bz;  // Controlled_Buffer controlled_buffer_289
  assign RF_FunSel = and_180_out ? 2'b00 : 2'bz;  // Controlled_Buffer controlled_buffer_290
  assign AR_FunSel = and_180_out ? 2'b00 : 2'bz;  // Controlled_Buffer controlled_buffer_291
  Decoder #(.select(3), .disabled(0)) decoder_20 (
    .out0(decoder_20_out3[3]), .out1(decoder_20_out3[2]), .out2(decoder_20_out3[1]),
    .out3(decoder_20_out3[0]), .out4(or_42_out[2]), .out5(or_42_out[1]), .out6(decoder_20_out6),
    .out7(decoder_20_out7), .sel({DESTREG, ADDRMODE}), .en(and_180_out));
  assign RF_RegSel = and_180_out ? decoder_20_out3 : 4'bz;  // Controlled_Buffer controlled_buffer_292
  assign AR_RegSel = and_180_out ? or_42_out : 3'bz;  // Controlled_Buffer controlled_buffer_293
  assign AR_OutCSel = and_180_out ? ADDRESS[6:5] : 2'bz;  // Controlled_Buffer controlled_buffer_294
  assign MuxASel = and_180_out ? 2'b10 : 2'bz;  // Controlled_Buffer controlled_buffer_295
  xor xor_7 (xor_7_out, DESTREG[2], ADDRESS[7]);
  assign SC_Reset = and_171_out ? 1'b1 : 1'bz;  // Controlled_Buffer controlled_buffer_296
  and and_181 (and_181_out, ADDRESS[4], or_38_out);
  or or_38 (or_38_out, ADDRESS[5], ADDRESS[6]);
  and and_182 (and_182_out, and_176_out, and_181_out);
  assign RF_OutBSel = and_182_out ? 2'b00 : 2'bz;  // Controlled_Buffer controlled_buffer_297
  Decoder #(.select(3), .disabled(0)) decoder_21 (
    .out0(decoder_21_out3[3]), .out1(decoder_21_out3[2]), .out2(decoder_21_out3[1]),
    .out3(decoder_21_out3[0]), .out4(or_39_out[2]), .out5(or_39_out[1]), .out6(decoder_21_out6),
    .out7(decoder_21_out7), .sel(controlled_buffer_276_out), .en(and_176_out));
  or or_39 (or_39_out[0], decoder_21_out6, decoder_21_out7);
  and and_183 (and_183_out, ADDRESS[4], or_40_out);
  or or_40 (or_40_out, ADDRESS[5], ADDRESS[6]);
  and and_184 (and_184_out, and_178_out, and_183_out);
  assign RF_OutBSel = and_184_out ? 2'b00 : 2'bz;  // Controlled_Buffer controlled_buffer_298
  Decoder #(.select(3), .disabled(0)) decoder_22 (
    .out0(decoder_22_out3[3]), .out1(decoder_22_out3[2]), .out2(decoder_22_out3[1]),
    .out3(decoder_22_out3[0]), .out4(or_41_out[2]), .out5(or_41_out[1]), .out6(decoder_22_out6),
    .out7(decoder_22_out7), .sel(controlled_buffer_284_out), .en(and_178_out));
  or or_41 (or_41_out[0], decoder_22_out6, decoder_22_out7);
  xor xor_8 (xor_8_out, DESTREG[2], ADDRESS[7]);
  or or_42 (or_42_out[0], decoder_20_out6, decoder_20_out7);
  assign Mem_str = D09 ? 1'b0 : 1'bz;  // Controlled_Buffer controlled_buffer_299
  assign Mem_load = D09 ? 1'b1 : 1'bz;  // Controlled_Buffer controlled_buffer_300
  assign Mem_clr = D09 ? 1'b0 : 1'bz;  // Controlled_Buffer controlled_buffer_301
  assign Mem_sel = D09 ? 1'b0 : 1'bz;  // Controlled_Buffer controlled_buffer_302
  assign AR_RegSel = D09 ? 3'b000 : 3'bz;  // Controlled_Buffer controlled_buffer_303
  and and_185 (and_185_out, ADDRESS[4], nor_9_out);
  and and_186 (and_186_out, and_176_out, and_185_out);
  assign RF_OutBSel = and_186_out ? 2'b01 : 2'bz;  // Controlled_Buffer controlled_buffer_304
  or or_43 (or_43_out, and_182_out, and_186_out);
  and and_187 (and_187_out, ADDRESS[4], nor_10_out);
  and and_188 (and_188_out, and_178_out, and_187_out);
  assign RF_OutBSel = and_188_out ? 2'b01 : 2'bz;  // Controlled_Buffer controlled_buffer_305
  or or_44 (or_44_out, and_184_out, and_188_out);
  and and_189 (and_189_out, D09, T2);
  assign RF_RegSel = and_192_out ? decoder_23_out3 : 4'bz;  // Controlled_Buffer controlled_buffer_306
  nor nor_9 (nor_9_out, ADDRESS[5], ADDRESS[6]);
  not not_49 (not_49_out, ARFARF);
  and and_190 (and_190_out, or_43_out, not_49_out);
  assign RF_OutASel = and_190_out ? ADDRESS[6:5] : 2'bz;  // Controlled_Buffer controlled_buffer_307
  assign RF_OutASel = ARFARF ? 2'b11 : 2'bz;  // Controlled_Buffer controlled_buffer_308
  assign RF_OutBSel = ARFARF ? 2'b00 : 2'bz;  // Controlled_Buffer controlled_buffer_309
  nor nor_10 (nor_10_out, ADDRESS[5], ADDRESS[6]);
  not not_50 (not_50_out, ARFARF);
  and and_191 (and_191_out, or_44_out, not_50_out);
  assign RF_OutASel = and_191_out ? ADDRESS[6:5] : 2'bz;  // Controlled_Buffer controlled_buffer_310
  assign RF_OutASel = ARFARF ? 2'b11 : 2'bz;  // Controlled_Buffer controlled_buffer_311
  assign RF_OutBSel = ARFARF ? 2'b00 : 2'bz;  // Controlled_Buffer controlled_buffer_312
  and and_192 (and_192_out, and_189_out, ADDRMODE);
  assign MuxASel = and_192_out ? 2'b00 : 2'bz;  // Controlled_Buffer controlled_buffer_313
  assign RF_FunSel = and_192_out ? 2'b00 : 2'bz;  // Controlled_Buffer controlled_buffer_314
  Decoder #(.select(2), .disabled(0)) decoder_23 (
    .out0(decoder_23_out3[3]), .out1(decoder_23_out3[2]), .out2(decoder_23_out3[1]),
    .out3(decoder_23_out3[0]), .sel(DESTREG), .en(and_192_out));
  and and_193 (and_193_out, D09, T3);
  and and_194 (and_194_out, and_193_out, ADDRMODE);
  assign SC_Reset = and_194_out ? 1'b1 : 1'bz;  // Controlled_Buffer controlled_buffer_315
  and and_195 (and_195_out, D0B, T2);
  and and_196 (and_196_out, D0B, T3);
  and and_197 (and_197_out, D0B, T5);
  and and_198 (and_198_out, and_197_out, and_205_out);
  assign SC_Reset = and_198_out ? 1'b1 : 1'bz;  // Controlled_Buffer controlled_buffer_316
  and and_199 (and_199_out, D0D, T5);
  assign SC_Reset = and_199_out ? 1'b1 : 1'bz;  // Controlled_Buffer controlled_buffer_317
  not not_51 (not_51_out, and_176_out);
  nor nor_11 (nor_11_out, and_190_out, and_163_out, not_51_out, ARFARF);
  assign RF_OutASel = nor_11_out ? ADDRESS[6:5] : 2'bz;  // Controlled_Buffer controlled_buffer_318
  assign RF_OutBSel = nor_11_out ? ADDRESS[3:2] : 2'bz;  // Controlled_Buffer controlled_buffer_319
  and and_200 (and_200_out, D0E, T5);
  assign SC_Reset = and_200_out ? 1'b1 : 1'bz;  // Controlled_Buffer controlled_buffer_320
  not not_52 (not_52_out, and_178_out);
  nor nor_12 (nor_12_out, and_191_out, and_164_out, not_52_out, ARFARF);
  assign RF_OutASel = nor_12_out ? ADDRESS[6:5] : 2'bz;  // Controlled_Buffer controlled_buffer_321
  assign RF_OutBSel = nor_12_out ? ADDRESS[3:2] : 2'bz;  // Controlled_Buffer controlled_buffer_322
  and and_201 (and_201_out, DESTREG[2], ADDRESS[7]);
  and and_202 (and_202_out, and_195_out, and_201_out);
  assign AR_OutCSel = and_202_out ? ADDRESS[6:5] : 2'bz;  // Controlled_Buffer controlled_buffer_323
  assign MuxASel = and_202_out ? 2'b10 : 2'bz;  // Controlled_Buffer controlled_buffer_324
  assign RF_RegSel = and_202_out ? 4'b0001 : 4'bz;  // Controlled_Buffer controlled_buffer_325
  assign RF_FunSel = and_202_out ? 2'b00 : 2'bz;  // Controlled_Buffer controlled_buffer_326
  and and_203 (and_203_out, DESTREG[2], ADDRESS[7]);
  and and_204 (and_204_out, and_196_out, and_203_out);
  assign RF_OutASel = and_204_out ? 2'b11 : 2'bz;  // Controlled_Buffer controlled_buffer_327
  assign ALU_FunSel = and_204_out ? 4'b0100 : 4'bz;  // Controlled_Buffer controlled_buffer_328
  assign MuxBSel = and_204_out ? 2'b11 : 2'bz;  // Controlled_Buffer controlled_buffer_329
  Decoder #(.select(3), .disabled(0)) decoder_24 (
    .out4(or_45_out[2]), .out5(or_45_out[1]), .out6(decoder_24_out6), .out7(decoder_24_out7),
    .sel({DESTREG, ADDRMODE}), .en(and_204_out));  // open: out0, out1, out2, out3
  assign AR_RegSel = and_204_out ? or_45_out : 3'bz;  // Controlled_Buffer controlled_buffer_330
  assign AR_FunSel = and_204_out ? 2'b00 : 2'bz;  // Controlled_Buffer controlled_buffer_331
  and and_205 (and_205_out, DESTREG[2], ADDRESS[7]);
  or or_45 (or_45_out[0], decoder_24_out6, decoder_24_out7);
  and and_206 (and_206_out, D0A, T2);
  not not_53 (not_53_out, ADDRMODE);
  and and_207 (and_207_out, and_206_out, not_53_out);
  assign RF_OutASel = and_207_out ? DESTREG : 2'bz;  // Controlled_Buffer controlled_buffer_332
  assign ALU_FunSel = and_207_out ? 4'b0100 : 4'bz;  // Controlled_Buffer controlled_buffer_333
  assign AR_OutCSel = and_207_out ? 2'b00 : 2'bz;  // Controlled_Buffer controlled_buffer_334
  assign Mem_sel = and_207_out ? 1'b0 : 1'bz;  // Controlled_Buffer controlled_buffer_335
  assign Mem_str = and_207_out ? 1'b1 : 1'bz;  // Controlled_Buffer controlled_buffer_336
  assign Mem_load = and_207_out ? 1'b0 : 1'bz;  // Controlled_Buffer controlled_buffer_337
  not not_54 (not_54_out, ADDRMODE);
  and and_208 (and_208_out, D0A, T3);
  and and_209 (and_209_out, and_208_out, not_54_out);
  assign SC_Reset = and_209_out ? 1'b1 : 1'bz;  // Controlled_Buffer controlled_buffer_338
  assign Mem_str = and_209_out ? 1'b0 : 1'bz;  // Controlled_Buffer controlled_buffer_339
  assign Mem_clr = D0A ? 1'b0 : 1'bz;  // Controlled_Buffer controlled_buffer_340
  assign AR_RegSel = D0A ? 3'b000 : 3'bz;  // Controlled_Buffer controlled_buffer_341
  assign RF_RegSel = D0A ? 4'b0000 : 4'bz;  // Controlled_Buffer controlled_buffer_342
  and and_210 (and_210_out, D0C, T2);
  and and_211 (and_211_out, D0C, T3);
  and and_212 (and_212_out, D07, T2);
  and and_213 (and_213_out, D07, T3);
  and and_214 (and_214_out, and_213_out, and_220_out);
  not not_55 (not_55_out, DESTREG[2]);
  and and_215 (and_215_out, and_210_out, and_221_out);
  assign RF_OutASel = and_215_out ? ADDRESS[6:5] : 2'bz;  // Controlled_Buffer controlled_buffer_343
  assign ALU_FunSel = and_215_out ? 4'b0010 : 4'bz;  // Controlled_Buffer controlled_buffer_344
  assign MuxASel = and_215_out ? 2'b11 : 2'bz;  // Controlled_Buffer controlled_buffer_345
  assign RF_FunSel = and_215_out ? 2'b00 : 2'bz;  // Controlled_Buffer controlled_buffer_346
  Decoder #(.select(3), .disabled(0)) decoder_25 (
    .out0(decoder_25_out3[3]), .out1(decoder_25_out3[2]), .out2(decoder_25_out3[1]),
    .out3(decoder_25_out3[0]), .out4(or_46_out[2]), .out5(or_46_out[1]), .out6(decoder_25_out6),
    .out7(decoder_25_out7), .sel({DESTREG, ADDRMODE}), .en(and_215_out));
  assign RF_RegSel = and_215_out ? decoder_25_out3 : 4'bz;  // Controlled_Buffer controlled_buffer_347
  assign AR_RegSel = and_215_out ? or_46_out : 3'bz;  // Controlled_Buffer controlled_buffer_348
  not not_56 (not_56_out, DESTREG[2]);
  not not_57 (not_57_out, ADDRESS[7]);
  and and_216 (and_216_out, not_56_out, not_57_out);
  and and_217 (and_217_out, and_211_out, and_216_out);
  assign SC_Reset = and_217_out ? 1'b1 : 1'bz;  // Controlled_Buffer controlled_buffer_349
  not not_58 (not_58_out, DESTREG[2]);
  and and_218 (and_218_out, not_58_out, not_62_out);
  and and_219 (and_219_out, and_212_out, and_218_out);
  assign RF_OutASel = and_219_out ? ADDRESS[6:5] : 2'bz;  // Controlled_Buffer controlled_buffer_350
  assign ALU_FunSel = and_219_out ? 4'b1010 : 4'bz;  // Controlled_Buffer controlled_buffer_351
  assign MuxASel = and_219_out ? 2'b11 : 2'bz;  // Controlled_Buffer controlled_buffer_352
  assign RF_FunSel = and_219_out ? 2'b00 : 2'bz;  // Controlled_Buffer controlled_buffer_353
  Decoder #(.select(3), .disabled(0)) decoder_26 (
    .out0(decoder_26_out3[3]), .out1(decoder_26_out3[2]), .out2(decoder_26_out3[1]),
    .out3(decoder_26_out3[0]), .out4(or_47_out[2]), .out5(or_47_out[1]), .out6(decoder_26_out6),
    .out7(decoder_26_out7), .sel({DESTREG, ADDRMODE}), .en(and_219_out));
  assign RF_RegSel = and_219_out ? decoder_26_out3 : 4'bz;  // Controlled_Buffer controlled_buffer_354
  assign AR_RegSel = and_219_out ? or_47_out : 3'bz;  // Controlled_Buffer controlled_buffer_355
  not not_59 (not_59_out, DESTREG[2]);
  not not_60 (not_60_out, ADDRESS[7]);
  and and_220 (and_220_out, not_59_out, not_60_out);
  assign SC_Reset = and_214_out ? 1'b1 : 1'bz;  // Controlled_Buffer controlled_buffer_356
  not not_61 (not_61_out, ADDRESS[7]);
  and and_221 (and_221_out, not_55_out, not_61_out);
  or or_46 (or_46_out[0], decoder_25_out6, decoder_25_out7);
  not not_62 (not_62_out, ADDRESS[7]);
  or or_47 (or_47_out[0], decoder_26_out6, decoder_26_out7);
  and and_222 (and_222_out, D0C, T3);
  and and_223 (and_223_out, D07, T3);
  and and_224 (and_224_out, D0C, T2);
  and and_225 (and_225_out, and_224_out, and_232_out);
  assign RF_OutASel = and_225_out ? ADDRESS[6:5] : 2'bz;  // Controlled_Buffer controlled_buffer_357
  assign ALU_FunSel = and_225_out ? 4'b0010 : 4'bz;  // Controlled_Buffer controlled_buffer_358
  assign MuxBSel = and_225_out ? 2'b11 : 2'bz;  // Controlled_Buffer controlled_buffer_359
  assign RF_FunSel = and_225_out ? 2'b00 : 2'bz;  // Controlled_Buffer controlled_buffer_360
  assign AR_FunSel = and_225_out ? 2'b00 : 2'bz;  // Controlled_Buffer controlled_buffer_361
  assign RF_RegSel = and_225_out ? decoder_28_out3 : 4'bz;  // Controlled_Buffer controlled_buffer_362
  assign AR_RegSel = and_225_out ? or_48_out : 3'bz;  // Controlled_Buffer controlled_buffer_363
  assign AR_OutCSel = and_225_out ? ADDRESS[6:5] : 2'bz;  // Controlled_Buffer controlled_buffer_364
  assign MuxASel = and_225_out ? 2'b10 : 2'bz;  // Controlled_Buffer controlled_buffer_365
  and and_226 (and_226_out, DESTREG[2], not_65_out);
  and and_227 (and_227_out, and_222_out, and_226_out);
  assign SC_Reset = and_227_out ? 1'b1 : 1'bz;  // Controlled_Buffer controlled_buffer_366
  assign Mem_str = D0C ? 1'b0 : 1'bz;  // Controlled_Buffer controlled_buffer_367
  assign Mem_load = D0C ? 1'b1 : 1'bz;  // Controlled_Buffer controlled_buffer_368
  assign Mem_clr = D0C ? 1'b0 : 1'bz;  // Controlled_Buffer controlled_buffer_369
  assign Mem_sel = D0C ? 1'b0 : 1'bz;  // Controlled_Buffer controlled_buffer_370
  and and_228 (and_228_out, D07, T2);
  and and_229 (and_229_out, and_228_out, and_233_out);
  assign RF_OutASel = and_229_out ? ADDRESS[6:5] : 2'bz;  // Controlled_Buffer controlled_buffer_371
  assign ALU_FunSel = and_229_out ? 4'b1010 : 4'bz;  // Controlled_Buffer controlled_buffer_372
  assign MuxBSel = and_229_out ? 2'b11 : 2'bz;  // Controlled_Buffer controlled_buffer_373
  assign RF_FunSel = and_229_out ? 2'b00 : 2'bz;  // Controlled_Buffer controlled_buffer_374
  assign AR_FunSel = and_229_out ? 2'b00 : 2'bz;  // Controlled_Buffer controlled_buffer_375
  Decoder #(.select(3), .disabled(0)) decoder_27 (
    .out0(decoder_27_out3[3]), .out1(decoder_27_out3[2]), .out2(decoder_27_out3[1]),
    .out3(decoder_27_out3[0]), .out4(or_49_out[2]), .out5(or_49_out[1]), .out6(decoder_27_out6),
    .out7(decoder_27_out7), .sel({DESTREG, ADDRMODE}), .en(and_229_out));
  assign RF_RegSel = and_229_out ? decoder_27_out3 : 4'bz;  // Controlled_Buffer controlled_buffer_376
  assign AR_RegSel = and_229_out ? or_49_out : 3'bz;  // Controlled_Buffer controlled_buffer_377
  assign AR_OutCSel = and_229_out ? ADDRESS[6:5] : 2'bz;  // Controlled_Buffer controlled_buffer_378
  assign MuxASel = and_229_out ? 2'b10 : 2'bz;  // Controlled_Buffer controlled_buffer_379
  not not_63 (not_63_out, ADDRESS[7]);
  and and_230 (and_230_out, DESTREG[2], not_63_out);
  and and_231 (and_231_out, and_223_out, and_230_out);
  assign SC_Reset = and_231_out ? 1'b1 : 1'bz;  // Controlled_Buffer controlled_buffer_380
  assign Mem_str = D07 ? 1'b0 : 1'bz;  // Controlled_Buffer controlled_buffer_381
  assign Mem_load = D07 ? 1'b1 : 1'bz;  // Controlled_Buffer controlled_buffer_382
  assign Mem_clr = D07 ? 1'b0 : 1'bz;  // Controlled_Buffer controlled_buffer_383
  assign Mem_sel = D07 ? 1'b0 : 1'bz;  // Controlled_Buffer controlled_buffer_384
  not not_64 (not_64_out, ADDRESS[7]);
  and and_232 (and_232_out, DESTREG[2], not_64_out);
  Decoder #(.select(3), .disabled(0)) decoder_28 (
    .out0(decoder_28_out3[3]), .out1(decoder_28_out3[2]), .out2(decoder_28_out3[1]),
    .out3(decoder_28_out3[0]), .out4(or_48_out[2]), .out5(or_48_out[1]), .out6(decoder_28_out6),
    .out7(decoder_28_out7), .sel({DESTREG, ADDRMODE}), .en(and_225_out));
  or or_48 (or_48_out[0], decoder_28_out6, decoder_28_out7);
  not not_65 (not_65_out, ADDRESS[7]);
  not not_66 (not_66_out, ADDRESS[7]);
  and and_233 (and_233_out, DESTREG[2], not_66_out);
  or or_49 (or_49_out[0], decoder_27_out6, decoder_27_out7);
  and and_234 (and_234_out, D0C, T2);
  assign RF_RegSel = and_244_out ? decoder_29_out3 : 4'bz;  // Controlled_Buffer controlled_buffer_385
  assign AR_RegSel = and_244_out ? or_50_out : 3'bz;  // Controlled_Buffer controlled_buffer_386
  and and_235 (and_235_out, D0C, T3);
  assign RF_RegSel = and_246_out ? decoder_30_out3 : 4'bz;  // Controlled_Buffer controlled_buffer_387
  assign AR_RegSel = and_246_out ? or_51_out : 3'bz;  // Controlled_Buffer controlled_buffer_388
  and and_236 (and_236_out, D0C, T4);
  and and_237 (and_237_out, D07, T2);
  and and_238 (and_238_out, and_237_out, and_249_out);
  assign RF_RegSel = and_238_out ? decoder_31_out3 : 4'bz;  // Controlled_Buffer controlled_buffer_389
  assign AR_RegSel = and_238_out ? or_52_out : 3'bz;  // Controlled_Buffer controlled_buffer_390
  and and_239 (and_239_out, D07, T3);
  and and_240 (and_240_out, and_239_out, and_250_out);
  assign RF_RegSel = and_240_out ? decoder_32_out3 : 4'bz;  // Controlled_Buffer controlled_buffer_391
  assign AR_RegSel = and_240_out ? or_53_out : 3'bz;  // Controlled_Buffer controlled_buffer_392
  and and_241 (and_241_out, D07, T4);
  and and_242 (and_242_out, and_241_out, and_251_out);
  not not_67 (not_67_out, DESTREG[2]);
  and and_243 (and_243_out, not_67_out, ADDRESS[7]);
  and and_244 (and_244_out, and_234_out, and_243_out);
  assign RF_OutASel = and_244_out ? ADDRESS[6:5] : 2'bz;  // Controlled_Buffer controlled_buffer_393
  assign MuxBSel = and_244_out ? 2'b11 : 2'bz;  // Controlled_Buffer controlled_buffer_394
  assign RF_FunSel = and_244_out ? 2'b00 : 2'bz;  // Controlled_Buffer controlled_buffer_395
  assign AR_FunSel = and_244_out ? 2'b00 : 2'bz;  // Controlled_Buffer controlled_buffer_396
  Decoder #(.select(3), .disabled(0)) decoder_29 (
    .out0(decoder_29_out3[3]), .out1(decoder_29_out3[2]), .out2(decoder_29_out3[1]),
    .out3(decoder_29_out3[0]), .out4(or_50_out[2]), .out5(or_50_out[1]), .out6(decoder_29_out6),
    .out7(decoder_29_out7), .sel({DESTREG, ADDRMODE}), .en(and_244_out));
  assign AR_OutCSel = and_244_out ? ADDRESS[6:5] : 2'bz;  // Controlled_Buffer controlled_buffer_397
  assign MuxASel = and_244_out ? 2'b10 : 2'bz;  // Controlled_Buffer controlled_buffer_398
  not not_68 (not_68_out, DESTREG[2]);
  and and_245 (and_245_out, not_68_out, ADDRESS[7]);
  and and_246 (and_246_out, and_235_out, and_245_out);
  assign RF_OutASel = and_246_out ? {DESTREG[1], ADDRMODE} : 2'bz;  // Controlled_Buffer controlled_buffer_399
  assign ALU_FunSel = and_246_out ? 4'b0010 : 4'bz;  // Controlled_Buffer controlled_buffer_400
  assign MuxASel = and_246_out ? 2'b11 : 2'bz;  // Controlled_Buffer controlled_buffer_401
  assign RF_FunSel = and_246_out ? 2'b00 : 2'bz;  // Controlled_Buffer controlled_buffer_402
  Decoder #(.select(3), .disabled(0)) decoder_30 (
    .out0(decoder_30_out3[3]), .out1(decoder_30_out3[2]), .out2(decoder_30_out3[1]),
    .out3(decoder_30_out3[0]), .out4(or_51_out[2]), .out5(or_51_out[1]), .out6(decoder_30_out6),
    .out7(decoder_30_out7), .sel({DESTREG, ADDRMODE}), .en(and_246_out));
  not not_69 (not_69_out, DESTREG[2]);
  and and_247 (and_247_out, not_69_out, ADDRESS[7]);
  and and_248 (and_248_out, and_236_out, and_247_out);
  assign SC_Reset = and_248_out ? 1'b1 : 1'bz;  // Controlled_Buffer controlled_buffer_403
  not not_70 (not_70_out, DESTREG[2]);
  and and_249 (and_249_out, not_70_out, ADDRESS[7]);
  assign RF_OutASel = and_238_out ? ADDRESS[6:5] : 2'bz;  // Controlled_Buffer controlled_buffer_404
  assign MuxBSel = and_238_out ? 2'b11 : 2'bz;  // Controlled_Buffer controlled_buffer_405
  assign RF_FunSel = and_238_out ? 2'b00 : 2'bz;  // Controlled_Buffer controlled_buffer_406
  assign AR_FunSel = and_238_out ? 2'b00 : 2'bz;  // Controlled_Buffer controlled_buffer_407
  Decoder #(.select(3), .disabled(0)) decoder_31 (
    .out0(decoder_31_out3[3]), .out1(decoder_31_out3[2]), .out2(decoder_31_out3[1]),
    .out3(decoder_31_out3[0]), .out4(or_52_out[2]), .out5(or_52_out[1]), .out6(decoder_31_out6),
    .out7(decoder_31_out7), .sel({DESTREG, ADDRMODE}), .en(and_238_out));
  assign AR_OutCSel = and_238_out ? ADDRESS[6:5] : 2'bz;  // Controlled_Buffer controlled_buffer_408
  assign MuxASel = and_238_out ? 2'b10 : 2'bz;  // Controlled_Buffer controlled_buffer_409
  not not_71 (not_71_out, DESTREG[2]);
  and and_250 (and_250_out, not_71_out, ADDRESS[7]);
  assign RF_OutASel = and_240_out ? {DESTREG[1], ADDRMODE} : 2'bz;  // Controlled_Buffer controlled_buffer_410
  assign ALU_FunSel = and_240_out ? 4'b1010 : 4'bz;  // Controlled_Buffer controlled_buffer_411
  assign MuxASel = and_240_out ? 2'b11 : 2'bz;  // Controlled_Buffer controlled_buffer_412
  assign RF_FunSel = and_240_out ? 2'b00 : 2'bz;  // Controlled_Buffer controlled_buffer_413
  Decoder #(.select(3), .disabled(0)) decoder_32 (
    .out0(decoder_32_out3[3]), .out1(decoder_32_out3[2]), .out2(decoder_32_out3[1]),
    .out3(decoder_32_out3[0]), .out4(or_53_out[2]), .out5(or_53_out[1]), .out6(decoder_32_out6),
    .out7(decoder_32_out7), .sel({DESTREG, ADDRMODE}), .en(and_240_out));
  not not_72 (not_72_out, DESTREG[2]);
  and and_251 (and_251_out, not_72_out, ADDRESS[7]);
  assign SC_Reset = and_242_out ? 1'b1 : 1'bz;  // Controlled_Buffer controlled_buffer_414
  or or_50 (or_50_out[0], decoder_29_out6, decoder_29_out7);
  or or_51 (or_51_out[0], decoder_30_out6, decoder_30_out7);
  or or_52 (or_52_out[0], decoder_31_out6, decoder_31_out7);
  or or_53 (or_53_out[0], decoder_32_out6, decoder_32_out7);
  and and_252 (and_252_out, D08, T4);
  and and_253 (and_253_out, D0C, T2);
  and and_254 (and_254_out, D0C, T3);
  assign AR_RegSel = and_264_out ? or_54_out : 3'bz;  // Controlled_Buffer controlled_buffer_415
  and and_255 (and_255_out, D0C, T4);
  and and_256 (and_256_out, and_255_out, and_265_out);
  assign SC_Reset = and_256_out ? 1'b1 : 1'bz;  // Controlled_Buffer controlled_buffer_416
  and and_257 (and_257_out, D08, T2);
  and and_258 (and_258_out, D08, T3);
  and and_259 (and_259_out, and_258_out, and_268_out);
  assign AR_RegSel = and_259_out ? or_55_out : 3'bz;  // Controlled_Buffer controlled_buffer_417
  and and_260 (and_260_out, and_252_out, and_269_out);
  assign SC_Reset = and_260_out ? 1'b1 : 1'bz;  // Controlled_Buffer controlled_buffer_418
  and and_261 (and_261_out, DESTREG[2], ADDRESS[7]);
  and and_262 (and_262_out, and_253_out, and_261_out);
  assign AR_OutCSel = and_262_out ? ADDRESS[6:5] : 2'bz;  // Controlled_Buffer controlled_buffer_419
  assign MuxASel = and_262_out ? 2'b10 : 2'bz;  // Controlled_Buffer controlled_buffer_420
  assign RF_RegSel = and_262_out ? 4'b0001 : 4'bz;  // Controlled_Buffer controlled_buffer_421
  assign RF_FunSel = and_262_out ? 2'b00 : 2'bz;  // Controlled_Buffer controlled_buffer_422
  and and_263 (and_263_out, DESTREG[2], ADDRESS[7]);
  and and_264 (and_264_out, and_254_out, and_263_out);
  assign RF_OutASel = and_264_out ? 2'b11 : 2'bz;  // Controlled_Buffer controlled_buffer_423
  assign ALU_FunSel = and_264_out ? 4'b0010 : 4'bz;  // Controlled_Buffer controlled_buffer_424
  assign MuxBSel = and_264_out ? 2'b11 : 2'bz;  // Controlled_Buffer controlled_buffer_425
  Decoder #(.select(3), .disabled(0)) decoder_33 (
    .out4(or_54_out[2]), .out5(or_54_out[1]), .out6(decoder_33_out6), .out7(decoder_33_out7),
    .sel({DESTREG, ADDRMODE}), .en(and_264_out));  // open: out0, out1, out2, out3
  assign AR_FunSel = and_264_out ? 2'b00 : 2'bz;  // Controlled_Buffer controlled_buffer_426
  and and_265 (and_265_out, DESTREG[2], ADDRESS[7]);
  and and_266 (and_266_out, DESTREG[2], ADDRESS[7]);
  and and_267 (and_267_out, and_257_out, and_266_out);
  assign AR_OutCSel = and_267_out ? ADDRESS[6:5] : 2'bz;  // Controlled_Buffer controlled_buffer_427
  assign MuxASel = and_267_out ? 2'b10 : 2'bz;  // Controlled_Buffer controlled_buffer_428
  assign RF_RegSel = and_267_out ? 4'b0001 : 4'bz;  // Controlled_Buffer controlled_buffer_429
  assign RF_FunSel = and_267_out ? 2'b00 : 2'bz;  // Controlled_Buffer controlled_buffer_430
  and and_268 (and_268_out, DESTREG[2], ADDRESS[7]);
  assign RF_OutASel = and_259_out ? 2'b11 : 2'bz;  // Controlled_Buffer controlled_buffer_431
  assign ALU_FunSel = and_259_out ? 4'b1010 : 4'bz;  // Controlled_Buffer controlled_buffer_432
  assign MuxBSel = and_259_out ? 2'b11 : 2'bz;  // Controlled_Buffer controlled_buffer_433
  Decoder #(.select(3), .disabled(0)) decoder_34 (
    .out4(or_55_out[2]), .out5(or_55_out[1]), .out6(decoder_34_out6), .out7(decoder_34_out7),
    .sel({DESTREG, ADDRMODE}), .en(and_259_out));  // open: out0, out1, out2, out3
  assign AR_FunSel = and_259_out ? 2'b00 : 2'bz;  // Controlled_Buffer controlled_buffer_434
  and and_269 (and_269_out, DESTREG[2], ADDRESS[7]);
  or or_54 (or_54_out[0], decoder_33_out6, decoder_33_out7);
  or or_55 (or_55_out[0], decoder_34_out6, decoder_34_out7);
  and and_270 (and_270_out, D08, T2);
  assign RF_RegSel = and_274_out ? decoder_35_out3 : 4'bz;  // Controlled_Buffer controlled_buffer_435
  assign AR_RegSel = and_274_out ? or_56_out : 3'bz;  // Controlled_Buffer controlled_buffer_436
  and and_271 (and_271_out, D08, T3);
  and and_272 (and_272_out, and_271_out, and_275_out);
  assign SC_Reset = and_272_out ? 1'b1 : 1'bz;  // Controlled_Buffer controlled_buffer_437
  not not_73 (not_73_out, ADDRESS[7]);
  not not_74 (not_74_out, DESTREG[2]);
  and and_273 (and_273_out, not_74_out, not_73_out);
  and and_274 (and_274_out, and_270_out, and_273_out);
  assign RF_OutASel = and_274_out ? ADDRESS[6:5] : 2'bz;  // Controlled_Buffer controlled_buffer_438
  assign ALU_FunSel = and_274_out ? 4'b1011 : 4'bz;  // Controlled_Buffer controlled_buffer_439
  assign MuxASel = and_274_out ? 2'b11 : 2'bz;  // Controlled_Buffer controlled_buffer_440
  assign RF_FunSel = and_274_out ? 2'b00 : 2'bz;  // Controlled_Buffer controlled_buffer_441
  Decoder #(.select(3), .disabled(0)) decoder_35 (
    .out0(decoder_35_out3[3]), .out1(decoder_35_out3[2]), .out2(decoder_35_out3[1]),
    .out3(decoder_35_out3[0]), .out4(or_56_out[2]), .out5(or_56_out[1]), .out6(decoder_35_out6),
    .out7(decoder_35_out7), .sel({DESTREG, ADDRMODE}), .en(and_274_out));
  not not_75 (not_75_out, DESTREG[2]);
  not not_76 (not_76_out, ADDRESS[7]);
  and and_275 (and_275_out, not_75_out, not_76_out);
  or or_56 (or_56_out[0], decoder_35_out6, decoder_35_out7);
  and and_276 (and_276_out, D08, T2);
  and and_277 (and_277_out, D08, T3);
  and and_278 (and_278_out, and_277_out, and_280_out);
  assign Mem_str = D08 ? 1'b0 : 1'bz;  // Controlled_Buffer controlled_buffer_442
  assign Mem_load = D08 ? 1'b1 : 1'bz;  // Controlled_Buffer controlled_buffer_443
  assign Mem_clr = D08 ? 1'b0 : 1'bz;  // Controlled_Buffer controlled_buffer_444
  assign Mem_sel = D08 ? 1'b0 : 1'bz;  // Controlled_Buffer controlled_buffer_445
  and and_279 (and_279_out, and_276_out, and_281_out);
  assign RF_OutASel = and_279_out ? ADDRESS[6:5] : 2'bz;  // Controlled_Buffer controlled_buffer_446
  assign ALU_FunSel = and_279_out ? 4'b1011 : 4'bz;  // Controlled_Buffer controlled_buffer_447
  assign MuxBSel = and_279_out ? 2'b11 : 2'bz;  // Controlled_Buffer controlled_buffer_448
  assign RF_FunSel = and_279_out ? 2'b00 : 2'bz;  // Controlled_Buffer controlled_buffer_449
  assign AR_FunSel = and_279_out ? 2'b00 : 2'bz;  // Controlled_Buffer controlled_buffer_450
  Decoder #(.select(3), .disabled(0)) decoder_36 (
    .out0(decoder_36_out3[3]), .out1(decoder_36_out3[2]), .out2(decoder_36_out3[1]),
    .out3(decoder_36_out3[0]), .out4(or_57_out[2]), .out5(or_57_out[1]), .out6(decoder_36_out6),
    .out7(decoder_36_out7), .sel({DESTREG, ADDRMODE}), .en(and_279_out));
  assign RF_RegSel = and_279_out ? decoder_36_out3 : 4'bz;  // Controlled_Buffer controlled_buffer_451
  assign AR_RegSel = and_279_out ? or_57_out : 3'bz;  // Controlled_Buffer controlled_buffer_452
  assign AR_OutCSel = and_279_out ? ADDRESS[6:5] : 2'bz;  // Controlled_Buffer controlled_buffer_453
  assign MuxASel = and_279_out ? 2'b10 : 2'bz;  // Controlled_Buffer controlled_buffer_454
  not not_77 (not_77_out, ADDRESS[7]);
  and and_280 (and_280_out, DESTREG[2], not_77_out);
  assign SC_Reset = and_278_out ? 1'b1 : 1'bz;  // Controlled_Buffer controlled_buffer_455
  not not_78 (not_78_out, ADDRESS[7]);
  and and_281 (and_281_out, DESTREG[2], not_78_out);
  or or_57 (or_57_out[0], decoder_36_out6, decoder_36_out7);
  and and_282 (and_282_out, D08, T2);
  and and_283 (and_283_out, and_282_out, and_288_out);
  assign RF_OutASel = and_283_out ? ADDRESS[6:5] : 2'bz;  // Controlled_Buffer controlled_buffer_456
  assign MuxBSel = and_283_out ? 2'b11 : 2'bz;  // Controlled_Buffer controlled_buffer_457
  assign RF_FunSel = and_283_out ? 2'b00 : 2'bz;  // Controlled_Buffer controlled_buffer_458
  assign AR_FunSel = and_283_out ? 2'b00 : 2'bz;  // Controlled_Buffer controlled_buffer_459
  Decoder #(.select(3), .disabled(0)) decoder_37 (
    .out0(decoder_37_out3[3]), .out1(decoder_37_out3[2]), .out2(decoder_37_out3[1]),
    .out3(decoder_37_out3[0]), .out4(or_58_out[2]), .out5(or_58_out[1]), .out6(decoder_37_out6),
    .out7(decoder_37_out7), .sel({DESTREG, ADDRMODE}), .en(and_283_out));
  assign RF_RegSel = and_283_out ? decoder_37_out3 : 4'bz;  // Controlled_Buffer controlled_buffer_460
  assign AR_RegSel = and_283_out ? or_58_out : 3'bz;  // Controlled_Buffer controlled_buffer_461
  assign AR_OutCSel = and_283_out ? ADDRESS[6:5] : 2'bz;  // Controlled_Buffer controlled_buffer_462
  assign MuxASel = and_283_out ? 2'b10 : 2'bz;  // Controlled_Buffer controlled_buffer_463
  and and_284 (and_284_out, D08, T3);
  and and_285 (and_285_out, and_284_out, and_289_out);
  assign RF_OutASel = and_285_out ? {DESTREG[1], ADDRMODE} : 2'bz;  // Controlled_Buffer controlled_buffer_464
  assign ALU_FunSel = and_285_out ? 4'b1011 : 4'bz;  // Controlled_Buffer controlled_buffer_465
  assign MuxASel = and_285_out ? 2'b11 : 2'bz;  // Controlled_Buffer controlled_buffer_466
  assign RF_FunSel = and_285_out ? 2'b00 : 2'bz;  // Controlled_Buffer controlled_buffer_467
  Decoder #(.select(3), .disabled(0)) decoder_38 (
    .out0(decoder_38_out3[3]), .out1(decoder_38_out3[2]), .out2(decoder_38_out3[1]),
    .out3(decoder_38_out3[0]), .out4(or_59_out[2]), .out5(or_59_out[1]), .out6(decoder_38_out6),
    .out7(decoder_38_out7), .sel({DESTREG, ADDRMODE}), .en(and_285_out));
  assign RF_RegSel = and_285_out ? decoder_38_out3 : 4'bz;  // Controlled_Buffer controlled_buffer_468
  assign AR_RegSel = and_285_out ? or_59_out : 3'bz;  // Controlled_Buffer controlled_buffer_469
  and and_286 (and_286_out, D08, T4);
  and and_287 (and_287_out, and_286_out, and_290_out);
  assign SC_Reset = and_287_out ? 1'b1 : 1'bz;  // Controlled_Buffer controlled_buffer_470
  not not_79 (not_79_out, DESTREG[2]);
  and and_288 (and_288_out, not_79_out, ADDRESS[7]);
  or or_58 (or_58_out[0], decoder_37_out6, decoder_37_out7);
  not not_80 (not_80_out, DESTREG[2]);
  and and_289 (and_289_out, not_80_out, ADDRESS[7]);
  or or_59 (or_59_out[0], decoder_38_out6, decoder_38_out7);
  not not_81 (not_81_out, DESTREG[2]);
  and and_290 (and_290_out, not_81_out, ADDRESS[7]);
  and and_291 (and_291_out, D08, T4);
  and and_292 (and_292_out, D08, T2);
  and and_293 (and_293_out, and_292_out, and_298_out);
  assign AR_OutCSel = and_293_out ? ADDRESS[6:5] : 2'bz;  // Controlled_Buffer controlled_buffer_471
  assign MuxASel = and_293_out ? 2'b10 : 2'bz;  // Controlled_Buffer controlled_buffer_472
  assign RF_RegSel = and_293_out ? 4'b0001 : 4'bz;  // Controlled_Buffer controlled_buffer_473
  assign RF_FunSel = and_293_out ? 2'b00 : 2'bz;  // Controlled_Buffer controlled_buffer_474
  and and_294 (and_294_out, D08, T3);
  and and_295 (and_295_out, and_294_out, and_299_out);
  assign RF_OutASel = and_295_out ? 2'b11 : 2'bz;  // Controlled_Buffer controlled_buffer_475
  assign ALU_FunSel = and_295_out ? 4'b1011 : 4'bz;  // Controlled_Buffer controlled_buffer_476
  assign MuxBSel = and_295_out ? 2'b11 : 2'bz;  // Controlled_Buffer controlled_buffer_477
  Decoder #(.select(3), .disabled(0)) decoder_39 (
    .out4(or_60_out[2]), .out5(or_60_out[1]), .out6(decoder_39_out6), .out7(decoder_39_out7),
    .sel({DESTREG, ADDRMODE}), .en(and_295_out));  // open: out0, out1, out2, out3
  assign AR_RegSel = and_295_out ? or_60_out : 3'bz;  // Controlled_Buffer controlled_buffer_478
  assign AR_FunSel = and_295_out ? 2'b00 : 2'bz;  // Controlled_Buffer controlled_buffer_479
  and and_296 (and_296_out, DESTREG[2], ADDRESS[7]);
  and and_297 (and_297_out, and_291_out, and_296_out);
  assign SC_Reset = and_297_out ? 1'b1 : 1'bz;  // Controlled_Buffer controlled_buffer_480
  and and_298 (and_298_out, DESTREG[2], ADDRESS[7]);
  and and_299 (and_299_out, DESTREG[2], ADDRESS[7]);
  or or_60 (or_60_out[0], decoder_39_out6, decoder_39_out7);

  // Other names for the same wires on the sheet: Instruction[10:0] = {DESTREG, ADDRMODE, ADDRESS};
  //   SRCREG2[2:0] = ADDRESS[4:2]; SRCREG1[2:0] = ADDRESS[7:5]; DESTREG[0] = ADDRMODE; REGSEL[1:0] = DESTREG;
  //   OPCODE[4:0] = Instruction

  // Notes on the sheet:
  //   Sequence Counter
  //   RF TO RF
  //   ORGANIZATION
  //   D02 - DEC
  //   RF TO AR or AR TO RF
  //   D00 - ADD
  //   D01 - SUB
  //   AR TO AR
  //   FETCH & DECODE
  //   DESTREG == SRCREG1
  //   RF TO RF
  //   D03 - INC
  //   RF TO AR or AR TO RF
  //   D04 - BRA
  //   AR TO AR
  //   D05 - BEQ
  //   DESTREG == SRCREG1
  //   D0D - OR
  //   D0E - AND
  //   RF TO RF
  //   D06 - BNE
  //   D0B - MOV
  //   RF TO AR or AR TO RF
  //   D09 - LD
  //   AR TO AR
  //   D0A - ST
  //   RF TO RF
  //   RF TO RF
  //   D0C - NOT
  //   RF TO AR
  //   D07 - LSL
  //   RF TO AR
  //   AR TO RF
  //   AR TO RF
  //   AR TO AR
  //   AR TO AR
  //   RF TO RF
  //   D08 - LSR
  //   RF TO AR
  //   AR TO RF
  //   AR TO AR
endmodule

module Sequence_Counter (
  input  Reset,
  output T0,
  output T1,
  output T2,
  output T3,
  output T4,
  output T5,
  output T6,
  output T7
);

  wire clock_1_out;
  wire [2:0] counter_1_q;

  Clock clock_1 (.out(clock_1_out));
  Counter #(.width(3), .max('h7)) counter_1 (
    .count(1'b1), .Q(counter_1_q), .clk(clock_1_out), .clr(Reset));  // open: load, D, carry, preset, down
  Decoder #(.select(3), .enable("false")) decoder_1 (
    .out0(T0), .out1(T1), .out2(T2), .out3(T3), .out4(T4), .out5(T5), .out6(T6), .out7(T7), .sel(counter_1_q));
endmodule

module isEqual (
  input  [2:0] in_1,
  input  [2:0] in_2,
  output out_3
);

  wire [2:0] xnor_1_out;

  assign xnor_1_out = ~(in_1 ^ in_2);  // XNOR_Gate xnor_1, 3 bits wide
  and and_1 (out_3, xnor_1_out[0], xnor_1_out[1], xnor_1_out[2]);
endmodule
module tmp (
);

  wire and_1_out, and_2_out, and_3_out, and_4_out, and_5_out, and_6_out, and_7_out, and_8_out, and_9_out,
       and_10_out, and_11_out, and_12_out, and_13_out, and_14_out, and_15_out, and_16_out, and_17_out,
       and_18_out, and_19_out, and_20_out, and_21_out, and_22_out, and_23_out, and_24_out, and_25_out,
       and_26_out, and_27_out, and_28_out, and_29_out, and_30_out, and_31_out, and_32_out, and_33_out, D03,
       decoder_1_out6, decoder_1_out7, decoder_2_out6, decoder_2_out7, decoder_3_out6, decoder_3_out7,
       decoder_4_out6, decoder_4_out7, decoder_5_out6, decoder_5_out7, decoder_6_out6, decoder_6_out7,
       decoder_7_out6, decoder_7_out7, isequal_1_out_3, isequal_2_out_3, isequal_3_out_3, isequal_4_out_3,
       isequal_5_out_3, isequal_6_out_3, isequal_7_out_3, isequal_8_out_3, isequal_9_out_3, isequal_10_out_3,
       isequal_11_out_3, isequal_12_out_3, isequal_13_out_3, Mem_clr, Mem_load, Mem_sel, Mem_str, not_1_out,
       not_2_out, not_3_out, not_4_out, not_5_out, not_6_out, not_7_out, not_8_out, not_9_out, not_10_out,
       not_11_out, not_12_out, not_13_out, not_14_out, not_15_out, not_16_out, SC_Reset, T2, T3, T4, T5,
       xor_1_out, xor_2_out, xor_3_out;
  wire [1:0] AR_FunSel, AR_OutCSel, MuxASel, MuxBSel, RF_FunSel, RF_OutASel;
  wire [2:0] AR_RegSel, DESTREG, or_1_out, or_2_out, or_3_out, or_4_out, or_5_out, or_6_out, or_7_out,
       SRCREG1;
  wire [3:0] ALU_FunSel, decoder_1_out3, decoder_2_out3, decoder_3_out3, decoder_4_out3, decoder_6_out3,
       decoder_7_out3, RF_RegSel;

  and and_1 (and_1_out, D03, T2);
  and and_2 (and_2_out, D03, T3);
  and and_3 (and_3_out, D03, T4);
  isEqual isequal_1 (.in_1(SRCREG1), .in_2(DESTREG), .out_3(isequal_1_out_3));
  not not_1 (not_1_out, isequal_1_out_3);
  and and_4 (and_4_out, and_1_out, not_1_out, and_7_out);
  assign RF_OutASel = and_4_out ? SRCREG1[1:0] : 2'bz;  // Controlled_Buffer controlled_buffer_1
  assign ALU_FunSel = and_4_out ? 4'b0100 : 4'bz;  // Controlled_Buffer controlled_buffer_2
  assign MuxASel = and_4_out ? 2'b11 : 2'bz;  // Controlled_Buffer controlled_buffer_3
  assign RF_FunSel = and_4_out ? 2'b00 : 2'bz;  // Controlled_Buffer controlled_buffer_4
  Decoder #(.select(3), .disabled(0)) decoder_1 (
    .out0(decoder_1_out3[3]), .out1(decoder_1_out3[2]), .out2(decoder_1_out3[1]), .out3(decoder_1_out3[0]),
    .out4(or_1_out[2]), .out5(or_1_out[1]), .out6(decoder_1_out6), .out7(decoder_1_out7), .sel(DESTREG),
    .en(and_4_out));
  assign RF_RegSel = and_4_out ? decoder_1_out3 : 4'bz;  // Controlled_Buffer controlled_buffer_5
  assign AR_RegSel = and_4_out ? or_1_out : 3'bz;  // Controlled_Buffer controlled_buffer_6
  isEqual isequal_2 (.in_1(SRCREG1), .in_2(DESTREG), .out_3(isequal_2_out_3));
  not not_2 (not_2_out, isequal_2_out_3);
  and and_5 (and_5_out, and_2_out, not_2_out, and_8_out);
  Decoder #(.select(3), .disabled(0)) decoder_2 (
    .out0(decoder_2_out3[3]), .out1(decoder_2_out3[2]), .out2(decoder_2_out3[1]), .out3(decoder_2_out3[0]),
    .out4(or_2_out[2]), .out5(or_2_out[1]), .out6(decoder_2_out6), .out7(decoder_2_out7), .sel(DESTREG),
    .en(and_5_out));
  assign RF_RegSel = and_5_out ? decoder_2_out3 : 4'bz;  // Controlled_Buffer controlled_buffer_7
  assign AR_RegSel = and_5_out ? or_2_out : 3'bz;  // Controlled_Buffer controlled_buffer_8
  assign RF_FunSel = and_5_out ? 2'b10 : 2'bz;  // Controlled_Buffer controlled_buffer_9
  assign AR_FunSel = and_5_out ? 2'b10 : 2'bz;  // Controlled_Buffer controlled_buffer_10
  isEqual isequal_3 (.in_1(SRCREG1), .in_2(DESTREG), .out_3(isequal_3_out_3));
  not not_3 (not_3_out, isequal_3_out_3);
  and and_6 (and_6_out, and_3_out, not_3_out, and_9_out);
  assign SC_Reset = and_6_out ? 1'b1 : 1'bz;  // Controlled_Buffer controlled_buffer_11
  not not_4 (not_4_out, SRCREG1[2]);
  not not_5 (not_5_out, DESTREG[2]);
  and and_7 (and_7_out, not_5_out, not_4_out);
  or or_1 (or_1_out[0], decoder_1_out6, decoder_1_out7);
  not not_6 (not_6_out, SRCREG1[2]);
  not not_7 (not_7_out, DESTREG[2]);
  and and_8 (and_8_out, not_7_out, not_6_out);
  or or_2 (or_2_out[0], decoder_2_out6, decoder_2_out7);
  not not_8 (not_8_out, DESTREG[2]);
  not not_9 (not_9_out, SRCREG1[2]);
  and and_9 (and_9_out, not_8_out, not_9_out);
  and and_10 (and_10_out, D03, T2);
  assign RF_RegSel = and_15_out ? decoder_3_out3 : 4'bz;  // Controlled_Buffer controlled_buffer_12
  assign AR_RegSel = and_15_out ? or_4_out : 3'bz;  // Controlled_Buffer controlled_buffer_13
  isEqual isequal_4 (.in_1(SRCREG1), .in_2(DESTREG), .out_3(isequal_4_out_3));
  and and_11 (and_11_out, D03, T3);
  not not_10 (not_10_out, isequal_4_out_3);
  and and_12 (and_12_out, and_11_out, not_10_out, xor_2_out);
  assign RF_RegSel = and_12_out ? decoder_4_out3 : 4'bz;  // Controlled_Buffer controlled_buffer_14
  assign AR_RegSel = and_12_out ? or_3_out : 3'bz;  // Controlled_Buffer controlled_buffer_15
  assign RF_FunSel = and_12_out ? 2'b10 : 2'bz;  // Controlled_Buffer controlled_buffer_16
  assign AR_FunSel = and_12_out ? 2'b10 : 2'bz;  // Controlled_Buffer controlled_buffer_17
  isEqual isequal_5 (.in_1(SRCREG1), .in_2(DESTREG), .out_3(isequal_5_out_3));
  and and_13 (and_13_out, D03, T4);
  not not_11 (not_11_out, isequal_5_out_3);
  and and_14 (and_14_out, and_13_out, not_11_out, xor_3_out);
  assign SC_Reset = and_14_out ? 1'b1 : 1'bz;  // Controlled_Buffer controlled_buffer_18
  isEqual isequal_6 (.in_1(SRCREG1), .in_2(DESTREG), .out_3(isequal_6_out_3));
  xor xor_1 (xor_1_out, DESTREG[2], SRCREG1[2]);
  not not_12 (not_12_out, isequal_6_out_3);
  and and_15 (and_15_out, and_10_out, not_12_out, xor_1_out);
  assign RF_OutASel = and_15_out ? SRCREG1[1:0] : 2'bz;  // Controlled_Buffer controlled_buffer_19
  assign ALU_FunSel = and_15_out ? 4'b0100 : 4'bz;  // Controlled_Buffer controlled_buffer_20
  assign MuxBSel = and_15_out ? 2'b11 : 2'bz;  // Controlled_Buffer controlled_buffer_21
  assign RF_FunSel = and_15_out ? 2'b00 : 2'bz;  // Controlled_Buffer controlled_buffer_22
  assign AR_FunSel = and_15_out ? 2'b00 : 2'bz;  // Controlled_Buffer controlled_buffer_23
  Decoder #(.select(3), .disabled(0)) decoder_3 (
    .out0(decoder_3_out3[3]), .out1(decoder_3_out3[2]), .out2(decoder_3_out3[1]), .out3(decoder_3_out3[0]),
    .out4(or_4_out[2]), .out5(or_4_out[1]), .out6(decoder_3_out6), .out7(decoder_3_out7), .sel(DESTREG),
    .en(and_15_out));
  assign AR_OutCSel = and_15_out ? SRCREG1[1:0] : 2'bz;  // Controlled_Buffer controlled_buffer_24
  assign MuxASel = and_15_out ? 2'b10 : 2'bz;  // Controlled_Buffer controlled_buffer_25
  xor xor_2 (xor_2_out, DESTREG[2], SRCREG1[2]);
  Decoder #(.select(3), .disabled(0)) decoder_4 (
    .out0(decoder_4_out3[3]), .out1(decoder_4_out3[2]), .out2(decoder_4_out3[1]), .out3(decoder_4_out3[0]),
    .out4(or_3_out[2]), .out5(or_3_out[1]), .out6(decoder_4_out6), .out7(decoder_4_out7), .sel(DESTREG),
    .en(and_12_out));
  or or_3 (or_3_out[0], decoder_4_out6, decoder_4_out7);
  xor xor_3 (xor_3_out, DESTREG[2], SRCREG1[2]);
  or or_4 (or_4_out[0], decoder_3_out6, decoder_3_out7);
  and and_16 (and_16_out, D03, T5);
  and and_17 (and_17_out, D03, T2);
  isEqual isequal_7 (.in_1(SRCREG1), .in_2(DESTREG), .out_3(isequal_7_out_3));
  and and_18 (and_18_out, D03, T3);
  not not_13 (not_13_out, isequal_7_out_3);
  and and_19 (and_19_out, and_18_out, not_13_out, and_25_out);
  assign AR_RegSel = and_19_out ? or_5_out : 3'bz;  // Controlled_Buffer controlled_buffer_26
  isEqual isequal_8 (.in_1(SRCREG1), .in_2(DESTREG), .out_3(isequal_8_out_3));
  and and_20 (and_20_out, D03, T4);
  not not_14 (not_14_out, isequal_8_out_3);
  and and_21 (and_21_out, and_20_out, not_14_out, and_26_out);
  assign RF_RegSel = and_21_out ? decoder_6_out3 : 4'bz;  // Controlled_Buffer controlled_buffer_27
  assign AR_RegSel = and_21_out ? or_6_out : 3'bz;  // Controlled_Buffer controlled_buffer_28
  isEqual isequal_9 (.in_1(SRCREG1), .in_2(DESTREG), .out_3(isequal_9_out_3));
  not not_15 (not_15_out, isequal_9_out_3);
  and and_22 (and_22_out, and_16_out, not_15_out, and_27_out);
  assign SC_Reset = and_22_out ? 1'b1 : 1'bz;  // Controlled_Buffer controlled_buffer_29
  isEqual isequal_10 (.in_1(SRCREG1), .in_2(DESTREG), .out_3(isequal_10_out_3));
  and and_23 (and_23_out, DESTREG[2], SRCREG1[2]);
  not not_16 (not_16_out, isequal_10_out_3);
  and and_24 (and_24_out, and_17_out, not_16_out, and_23_out);
  assign AR_OutCSel = and_24_out ? SRCREG1[1:0] : 2'bz;  // Controlled_Buffer controlled_buffer_30
  assign MuxASel = and_24_out ? 2'b10 : 2'bz;  // Controlled_Buffer controlled_buffer_31
  assign RF_RegSel = and_24_out ? 4'b0001 : 4'bz;  // Controlled_Buffer controlled_buffer_32
  assign RF_FunSel = and_24_out ? 2'b00 : 2'bz;  // Controlled_Buffer controlled_buffer_33
  and and_25 (and_25_out, DESTREG[2], SRCREG1[2]);
  assign RF_OutASel = and_19_out ? 2'b11 : 2'bz;  // Controlled_Buffer controlled_buffer_34
  assign ALU_FunSel = and_19_out ? 4'b0100 : 4'bz;  // Controlled_Buffer controlled_buffer_35
  assign MuxBSel = and_19_out ? 2'b11 : 2'bz;  // Controlled_Buffer controlled_buffer_36
  Decoder #(.select(3), .disabled(0)) decoder_5 (
    .out4(or_5_out[2]), .out5(or_5_out[1]), .out6(decoder_5_out6), .out7(decoder_5_out7), .sel(DESTREG),
    .en(and_19_out));  // open: out0, out1, out2, out3
  assign AR_FunSel = and_19_out ? 2'b00 : 2'bz;  // Controlled_Buffer controlled_buffer_37
  and and_26 (and_26_out, DESTREG[2], SRCREG1[2]);
  Decoder #(.select(3), .disabled(0)) decoder_6 (
    .out0(decoder_6_out3[3]), .out1(decoder_6_out3[2]), .out2(decoder_6_out3[1]), .out3(decoder_6_out3[0]),
    .out4(or_6_out[2]), .out5(or_6_out[1]), .out6(decoder_6_out6), .out7(decoder_6_out7), .sel(DESTREG),
    .en(and_21_out));
  assign RF_FunSel = and_21_out ? 2'b10 : 2'bz;  // Controlled_Buffer controlled_buffer_38
  assign AR_FunSel = and_21_out ? 2'b10 : 2'bz;  // Controlled_Buffer controlled_buffer_39
  and and_27 (and_27_out, DESTREG[2], SRCREG1[2]);
  or or_5 (or_5_out[0], decoder_5_out6, decoder_5_out7);
  or or_6 (or_6_out[0], decoder_6_out6, decoder_6_out7);
  and and_28 (and_28_out, D03, T3);
  and and_29 (and_29_out, D03, T4);
  and and_30 (and_30_out, D03, T2);
  and and_31 (and_31_out, and_30_out, isequal_11_out_3);
  Decoder #(.select(3), .disabled(0)) decoder_7 (
    .out0(decoder_7_out3[3]), .out1(decoder_7_out3[2]), .out2(decoder_7_out3[1]), .out3(decoder_7_out3[0]),
    .out4(or_7_out[2]), .out5(or_7_out[1]), .out6(decoder_7_out6), .out7(decoder_7_out7), .sel(DESTREG),
    .en(and_31_out));
  assign RF_RegSel = and_31_out ? decoder_7_out3 : 4'bz;  // Controlled_Buffer controlled_buffer_40
  assign AR_RegSel = and_31_out ? or_7_out : 3'bz;  // Controlled_Buffer controlled_buffer_41
  assign RF_FunSel = and_31_out ? 2'b10 : 2'bz;  // Controlled_Buffer controlled_buffer_42
  assign AR_FunSel = and_31_out ? 2'b10 : 2'bz;  // Controlled_Buffer controlled_buffer_43
  assign ALU_FunSel = and_31_out ? 4'b0100 : 4'bz;  // Controlled_Buffer controlled_buffer_44
  assign RF_OutASel = and_31_out ? SRCREG1[1:0] : 2'bz;  // Controlled_Buffer controlled_buffer_45
  and and_32 (and_32_out, and_28_out, isequal_12_out_3);
  assign ALU_FunSel = and_32_out ? 4'b0100 : 4'bz;  // Controlled_Buffer controlled_buffer_46
  assign RF_OutASel = and_32_out ? SRCREG1[1:0] : 2'bz;  // Controlled_Buffer controlled_buffer_47
  assign RF_RegSel = and_32_out ? 4'b0000 : 4'bz;  // Controlled_Buffer controlled_buffer_48
  assign AR_RegSel = and_32_out ? 3'b000 : 3'bz;  // Controlled_Buffer controlled_buffer_49
  and and_33 (and_33_out, and_29_out, isequal_13_out_3);
  assign SC_Reset = and_33_out ? 1'b1 : 1'bz;  // Controlled_Buffer controlled_buffer_50
  assign Mem_str = D03 ? 1'b0 : 1'bz;  // Controlled_Buffer controlled_buffer_51
  assign Mem_load = D03 ? 1'b1 : 1'bz;  // Controlled_Buffer controlled_buffer_52
  assign Mem_clr = D03 ? 1'b0 : 1'bz;  // Controlled_Buffer controlled_buffer_53
  assign Mem_sel = D03 ? 1'b0 : 1'bz;  // Controlled_Buffer controlled_buffer_54
  isEqual isequal_11 (.in_1(SRCREG1), .in_2(DESTREG), .out_3(isequal_11_out_3));
  or or_7 (or_7_out[0], decoder_7_out6, decoder_7_out7);
  isEqual isequal_12 (.in_1(SRCREG1), .in_2(DESTREG), .out_3(isequal_12_out_3));
  isEqual isequal_13 (.in_1(SRCREG1), .in_2(DESTREG), .out_3(isequal_13_out_3));

  // Notes on the sheet:
  //   RF TO RF
  //   D03 - INC
  //   RF TO AR or AR TO RF
  //   AR TO AR
  //   DESTREG == SRCREG1
endmodule
